// Logisim project Buscador_de_Memória.circ as structural Verilog: 1 circuit, main circuit main
module main (
  input  in_1,
  input  in_2,
  input  in_3,
  output out_4,
  output out_5,
  output out_6,
  output out_7,
  output out_8,
  output out_9,
  output out_10,
  output out_11,
  output out_12
);

  wire and_1_out, and_2_out, and_3_out, and_4_out, and_5_out, and_6_out, and_7_out, and_8_out, and_9_out,
       and_10_out, and_11_out, and_12_out, and_13_out, and_14_out, and_15_out, and_16_out, and_17_out,
       and_18_out, and_19_out, and_20_out, and_21_out, and_22_out, and_23_out, and_24_out, and_25_out,
       and_26_out, and_27_out, and_28_out, and_29_out, and_30_out, and_31_out, and_32_out, and_33_out,
       and_34_out, and_35_out, and_36_out, and_37_out, and_38_out, and_39_out, and_40_out, and_41_out,
       and_42_out, and_43_out, and_44_out, and_45_out, and_46_out, and_47_out, and_48_out, and_49_out,
       and_50_out, and_51_out, and_52_out, and_53_out, and_54_out, and_55_out, and_56_out, and_57_out,
       and_58_out, and_59_out, and_60_out, and_61_out, and_62_out, and_63_out, and_64_out, and_65_out,
       and_66_out, and_67_out, and_68_out, and_69_out, and_70_out, and_71_out, and_72_out, and_73_out,
       and_74_out, and_75_out, and_76_out, clock_1_out, d_ff_1_q, d_ff_2_q, d_ff_3_q, d_ff_4_q, d_ff_5_q,
       d_ff_6_q, d_ff_7_q, d_ff_8_q, d_ff_13_q, d_ff_14_q, d_ff_15_q, d_ff_16_q, d_ff_17_q, d_ff_18_q,
       d_ff_19_q, d_ff_20_q, d_ff_21_q, d_ff_22_q, d_ff_23_q, d_ff_24_q, d_ff_25_q, d_ff_26_q, d_ff_39_q,
       d_ff_40_q, d_ff_41_q, d_ff_42_q, d_ff_43_q, d_ff_44_q, d_ff_45_q, d_ff_46_q, d_ff_47_q, d_ff_48_q,
       d_ff_49_q, d_ff_50_q, d_ff_51_q, d_ff_52_q, d_ff_53_q, d_ff_54_q, d_ff_55_q, d_ff_56_q, d_ff_57_q,
       d_ff_58_q, d_ff_59_q, d_ff_60_q, d_ff_61_q, d_ff_62_q, d_ff_63_q, d_ff_64_q, d_ff_65_q, d_ff_66_q,
       d_ff_67_q, d_ff_68_q, d_ff_69_q, d_ff_70_q, nand_1_out, nor_1_out, not_1_out, not_2_out, not_3_out,
       not_4_out, not_5_out, not_6_out, not_7_out, not_8_out, not_9_out, not_10_out, not_11_out, not_12_out,
       not_13_out, not_14_out, not_15_out, not_16_out, not_17_out, not_18_out, not_19_out, not_20_out,
       not_21_out, not_22_out, not_23_out, not_24_out, not_25_out, not_26_out, not_27_out, not_28_out,
       not_29_out, not_30_out, not_31_out, not_32_out, not_33_out, not_34_out, not_35_out, not_36_out,
       not_37_out, not_38_out, or_1_out, or_2_out, or_3_out, t_ff_1_q, t_ff_2_q, t_ff_3_q, t_ff_4_q,
       undriven, undriven_2, undriven_3, undriven_4, undriven_5;

  D_Flip_Flop d_ff_1 (.clk(clock_1_out), .D(out_5), .Q(d_ff_1_q), .en(and_18_out));  // open: Qn, preset, reset
  Clock clock_1 (.out(clock_1_out));
  D_Flip_Flop d_ff_2 (.clk(clock_1_out), .D(out_6), .Q(d_ff_2_q), .en(and_18_out));  // open: Qn, preset, reset
  D_Flip_Flop d_ff_3 (.clk(clock_1_out), .D(out_7), .Q(d_ff_3_q), .en(and_18_out));  // open: Qn, preset, reset
  not not_1 (not_1_out, d_ff_8_q);
  not not_2 (not_2_out, d_ff_7_q);
  not not_3 (not_3_out, d_ff_7_q);
  not not_4 (not_4_out, d_ff_8_q);
  nand nand_1 (nand_1_out, in_3, out_4);
  D_Flip_Flop d_ff_4 (.clk(clock_1_out), .D(out_8), .Q(d_ff_4_q), .en(and_18_out));  // open: Qn, preset, reset
  not not_5 (not_5_out, d_ff_2_q);
  not not_6 (not_6_out, d_ff_3_q);
  not not_7 (not_7_out, d_ff_4_q);
  not not_8 (not_8_out, d_ff_2_q);
  not not_9 (not_9_out, d_ff_3_q);
  not not_10 (not_10_out, d_ff_2_q);
  not not_11 (not_11_out, d_ff_4_q);
  not not_12 (not_12_out, d_ff_2_q);
  not not_13 (not_13_out, d_ff_3_q);
  not not_14 (not_14_out, d_ff_4_q);
  not not_15 (not_15_out, d_ff_3_q);
  not not_16 (not_16_out, d_ff_4_q);
  D_Flip_Flop d_ff_5 (.clk(clock_1_out), .D(out_9), .Q(d_ff_5_q), .en(and_18_out));  // open: Qn, preset, reset
  D_Flip_Flop d_ff_6 (.clk(clock_1_out), .D(out_10), .Q(d_ff_6_q), .en(and_18_out));  // open: Qn, preset, reset
  not not_17 (not_17_out, d_ff_1_q);
  not not_18 (not_18_out, d_ff_1_q);
  not not_19 (not_19_out, d_ff_1_q);
  not not_20 (not_20_out, d_ff_1_q);
  not not_21 (not_21_out, d_ff_1_q);
  not not_22 (not_22_out, d_ff_1_q);
  not not_23 (not_23_out, d_ff_1_q);
  not not_24 (not_24_out, d_ff_1_q);
  LED led_1 (.in(and_1_out));
  and and_1 (and_1_out, not_1_out, not_2_out, and_15_out);
  and and_2 (and_2_out, not_3_out, d_ff_8_q, and_15_out);
  LED led_2 (.in(and_2_out));
  and and_3 (and_3_out, not_4_out, d_ff_7_q, and_15_out);
  LED led_3 (.in(and_3_out));
  LED led_4 (.in(and_4_out));
  and and_4 (and_4_out, d_ff_8_q, d_ff_7_q, and_15_out);
  T_Flip_Flop t_ff_1 (
    .clk(clock_1_out), .T(nand_1_out), .Q(t_ff_1_q), .reset(in_2), .en(nand_1_out));  // open: Qn, preset
  D_Flip_Flop d_ff_7 (.clk(clock_1_out), .D(out_11), .Q(d_ff_7_q), .en(and_18_out));  // open: Qn, preset, reset
  and and_5 (and_5_out, not_17_out, not_5_out, not_6_out, not_7_out, and_16_out);
  and and_6 (and_6_out, not_18_out, not_8_out, not_9_out, d_ff_4_q, and_16_out);
  and and_7 (and_7_out, not_19_out, not_10_out, d_ff_3_q, not_11_out, and_16_out);
  and and_8 (and_8_out, not_20_out, not_12_out, d_ff_3_q, d_ff_4_q, and_16_out);
  and and_9 (and_9_out, not_21_out, d_ff_2_q, not_13_out, not_14_out, and_16_out);
  and and_10 (and_10_out, not_22_out, d_ff_2_q, not_15_out, d_ff_4_q, and_16_out);
  and and_11 (and_11_out, not_23_out, d_ff_2_q, d_ff_3_q, not_16_out, and_16_out);
  and and_12 (and_12_out, not_24_out, d_ff_2_q, d_ff_3_q, d_ff_4_q, and_16_out);
  T_Flip_Flop t_ff_2 (
    .clk(clock_1_out), .T(t_ff_1_q), .Q(t_ff_2_q), .reset(in_2), .en(nand_1_out));  // open: Qn, preset
  D_Flip_Flop d_ff_8 (.clk(clock_1_out), .D(out_12), .Q(d_ff_8_q), .en(and_18_out));  // open: Qn, preset, reset
  LED led_5 (.in(and_5_out));
  LED led_6 (.in(and_6_out));
  LED led_7 (.in(and_7_out));
  LED led_8 (.in(and_8_out));
  LED led_9 (.in(and_9_out));
  LED led_10 (.in(and_10_out));
  LED led_11 (.in(and_11_out));
  LED led_12 (.in(and_12_out));
  and and_13 (and_13_out, t_ff_1_q, t_ff_2_q);
  T_Flip_Flop t_ff_3 (
    .clk(clock_1_out), .T(and_13_out), .Q(t_ff_3_q), .reset(in_2), .en(nand_1_out));  // open: Qn, preset
  D_Flip_Flop #(.trigger("falling")) d_ff_9 (.clk(and_19_out), .D(and_1_out));  // open: Q, Qn, preset, en, reset
  D_Flip_Flop #(.trigger("falling")) d_ff_10 (.clk(and_19_out), .D(and_2_out));  // open: Q, Qn, preset, en, reset
  D_Flip_Flop #(.trigger("falling")) d_ff_11 (.clk(and_19_out), .D(and_3_out));  // open: Q, Qn, preset, en, reset
  D_Flip_Flop #(.trigger("falling")) d_ff_12 (.clk(and_19_out), .D(and_4_out));  // open: Q, Qn, preset, en, reset
  and and_14 (and_14_out, t_ff_1_q, t_ff_2_q, t_ff_3_q);
  D_Flip_Flop #(.trigger("falling")) d_ff_13 (
    .clk(and_19_out), .D(and_5_out), .Q(d_ff_13_q));  // open: Qn, preset, en, reset
  D_Flip_Flop #(.trigger("falling")) d_ff_14 (
    .clk(and_19_out), .D(and_6_out), .Q(d_ff_14_q));  // open: Qn, preset, en, reset
  D_Flip_Flop #(.trigger("falling")) d_ff_15 (
    .clk(and_19_out), .D(and_7_out), .Q(d_ff_15_q));  // open: Qn, preset, en, reset
  D_Flip_Flop #(.trigger("falling")) d_ff_16 (
    .clk(and_19_out), .D(and_8_out), .Q(d_ff_16_q));  // open: Qn, preset, en, reset
  D_Flip_Flop #(.trigger("falling")) d_ff_17 (
    .clk(and_19_out), .D(and_9_out), .Q(d_ff_17_q));  // open: Qn, preset, en, reset
  D_Flip_Flop #(.trigger("falling")) d_ff_18 (
    .clk(and_19_out), .D(and_10_out), .Q(d_ff_18_q));  // open: Qn, preset, en, reset
  D_Flip_Flop #(.trigger("falling")) d_ff_19 (
    .clk(and_19_out), .D(and_11_out), .Q(d_ff_19_q));  // open: Qn, preset, en, reset
  D_Flip_Flop #(.trigger("falling")) d_ff_20 (
    .clk(and_19_out), .D(and_12_out), .Q(d_ff_20_q));  // open: Qn, preset, en, reset
  and and_15 (and_15_out, and_16_out, nor_1_out);
  T_Flip_Flop t_ff_4 (
    .clk(clock_1_out), .T(and_14_out), .Q(t_ff_4_q), .reset(in_2), .en(nand_1_out));  // open: Qn, preset
  not not_25 (not_25_out, t_ff_1_q);
  not not_26 (not_26_out, t_ff_2_q);
  not not_27 (not_27_out, t_ff_2_q);
  not not_28 (not_28_out, t_ff_1_q);
  and and_16 (and_16_out, and_19_out, not_29_out);
  and and_17 (and_17_out, t_ff_1_q, t_ff_2_q, t_ff_3_q, t_ff_4_q);
  T_Flip_Flop t_ff_5 (.clk(clock_1_out), .T(or_1_out), .Q(out_4), .reset(in_2), .en(nand_1_out));  // open: Qn, preset
  and and_18 (and_18_out, not_25_out, not_26_out);
  and and_19 (and_19_out, not_27_out, t_ff_1_q);
  and and_20 (and_20_out, not_28_out, t_ff_2_q);
  and and_21 (and_21_out, t_ff_1_q, t_ff_2_q);
  not not_29 (not_29_out, or_3_out);
  nor nor_1 (nor_1_out, and_22_out, and_23_out, and_24_out);
  or or_1 (or_1_out, in_1, and_17_out);
  LED led_13 (.in(and_18_out));
  LED led_14 (.in(and_19_out));
  LED led_15 (.in(and_20_out));
  LED led_16 (.in(and_21_out));
  not not_30 (not_30_out, d_ff_2_q);
  not not_31 (not_31_out, d_ff_3_q);
  not not_32 (not_32_out, d_ff_2_q);
  not not_33 (not_33_out, d_ff_4_q);
  not not_34 (not_34_out, d_ff_2_q);
  and and_22 (and_22_out, d_ff_1_q, not_30_out, not_31_out, d_ff_4_q, and_19_out);
  and and_23 (and_23_out, d_ff_1_q, not_32_out, d_ff_3_q, not_33_out, and_19_out);
  and and_24 (and_24_out, d_ff_1_q, not_34_out, d_ff_3_q, d_ff_4_q, and_19_out);
  D_Flip_Flop #(.trigger("falling")) d_ff_21 (
    .clk(and_19_out), .D(and_22_out), .Q(d_ff_21_q));  // open: Qn, preset, en, reset
  D_Flip_Flop #(.trigger("falling")) d_ff_22 (
    .clk(and_19_out), .D(and_23_out), .Q(d_ff_22_q));  // open: Qn, preset, en, reset
  D_Flip_Flop #(.trigger("falling")) d_ff_23 (
    .clk(and_19_out), .D(and_24_out), .Q(d_ff_23_q));  // open: Qn, preset, en, reset
  D_Flip_Flop #(.trigger("falling")) d_ff_24 (
    .clk(and_19_out), .D(d_ff_21_q), .Q(d_ff_24_q));  // open: Qn, preset, en, reset
  D_Flip_Flop #(.trigger("falling")) d_ff_25 (
    .clk(and_19_out), .D(d_ff_22_q), .Q(d_ff_25_q));  // open: Qn, preset, en, reset
  D_Flip_Flop #(.trigger("falling")) d_ff_26 (
    .clk(and_19_out), .D(d_ff_23_q), .Q(d_ff_26_q));  // open: Qn, preset, en, reset
  or or_2 (or_2_out, d_ff_24_q, d_ff_25_q, d_ff_26_q);
  or or_3 (or_3_out, d_ff_21_q, d_ff_22_q, d_ff_23_q);
  and and_25 (and_25_out, d_ff_13_q, and_20_out);
  and and_26 (and_26_out, d_ff_14_q, and_20_out);
  and and_27 (and_27_out, d_ff_15_q, and_20_out);
  and and_28 (and_28_out, d_ff_16_q, and_20_out);
  and and_29 (and_29_out, d_ff_17_q, and_20_out);
  and and_30 (and_30_out, d_ff_18_q, and_20_out);
  and and_31 (and_31_out, d_ff_19_q, and_20_out);
  and and_32 (and_32_out, d_ff_20_q, and_20_out);
  and and_33 (and_33_out, undriven_5, and_20_out);
  and and_34 (and_34_out, undriven_4, and_20_out);
  and and_35 (and_35_out, undriven_3, and_20_out);
  and and_36 (and_36_out, undriven, and_20_out);
  and and_37 (and_37_out, undriven_2, and_20_out);
  and and_38 (and_38_out, d_ff_24_q, and_20_out);
  and and_39 (and_39_out, d_ff_25_q, and_20_out);
  and and_40 (and_40_out, d_ff_26_q, and_20_out);
  D_Flip_Flop d_ff_27 (.clk(or_3_out), .D(d_ff_5_q));  // open: Q, Qn, preset, en, reset
  D_Flip_Flop d_ff_28 (.clk(or_3_out), .D(d_ff_6_q));  // open: Q, Qn, preset, en, reset
  D_Flip_Flop d_ff_29 (.clk(or_3_out), .D(d_ff_7_q));  // open: Q, Qn, preset, en, reset
  D_Flip_Flop d_ff_30 (.clk(or_3_out), .D(d_ff_8_q));  // open: Q, Qn, preset, en, reset
  D_Flip_Flop d_ff_31 (.clk(or_2_out), .D(d_ff_1_q));  // open: Q, Qn, preset, en, reset
  D_Flip_Flop d_ff_32 (.clk(or_2_out), .D(d_ff_2_q));  // open: Q, Qn, preset, en, reset
  D_Flip_Flop d_ff_33 (.clk(or_2_out), .D(d_ff_3_q));  // open: Q, Qn, preset, en, reset
  D_Flip_Flop d_ff_34 (.clk(or_2_out), .D(d_ff_4_q));  // open: Q, Qn, preset, en, reset
  D_Flip_Flop d_ff_35 (.clk(or_2_out), .D(d_ff_5_q));  // open: Q, Qn, preset, en, reset
  D_Flip_Flop d_ff_36 (.clk(or_2_out), .D(d_ff_6_q));  // open: Q, Qn, preset, en, reset
  D_Flip_Flop d_ff_37 (.clk(or_2_out), .D(d_ff_7_q));  // open: Q, Qn, preset, en, reset
  D_Flip_Flop d_ff_38 (.clk(or_2_out), .D(d_ff_8_q));  // open: Q, Qn, preset, en, reset
  not not_35 (not_35_out, t_ff_3_q);
  not not_36 (not_36_out, t_ff_4_q);
  not not_37 (not_37_out, t_ff_4_q);
  not not_38 (not_38_out, t_ff_3_q);
  and and_41 (and_41_out, not_35_out, and_18_out, not_36_out);
  and and_42 (and_42_out, not_37_out, t_ff_3_q, and_18_out);
  and and_43 (and_43_out, not_38_out, t_ff_4_q, and_18_out);
  and and_44 (and_44_out, t_ff_3_q, t_ff_4_q, and_18_out);
  LED led_17 (.in(and_41_out));
  LED led_18 (.in(and_42_out));
  LED led_19 (.in(and_43_out));
  LED led_20 (.in(and_44_out));
  D_Flip_Flop d_ff_39 (.Q(d_ff_39_q));  // open: clk, D, Qn, preset, en, reset
  D_Flip_Flop d_ff_40 (.Q(d_ff_40_q));  // open: clk, D, Qn, preset, en, reset
  D_Flip_Flop d_ff_41 (.Q(d_ff_41_q));  // open: clk, D, Qn, preset, en, reset
  D_Flip_Flop d_ff_42 (.Q(d_ff_42_q));  // open: clk, D, Qn, preset, en, reset
  D_Flip_Flop d_ff_43 (.Q(d_ff_43_q));  // open: clk, D, Qn, preset, en, reset
  D_Flip_Flop d_ff_44 (.Q(d_ff_44_q));  // open: clk, D, Qn, preset, en, reset
  D_Flip_Flop d_ff_45 (.Q(d_ff_45_q));  // open: clk, D, Qn, preset, en, reset
  D_Flip_Flop d_ff_46 (.Q(d_ff_46_q));  // open: clk, D, Qn, preset, en, reset
  D_Flip_Flop d_ff_47 (.Q(d_ff_47_q));  // open: clk, D, Qn, preset, en, reset
  D_Flip_Flop d_ff_48 (.Q(d_ff_48_q));  // open: clk, D, Qn, preset, en, reset
  D_Flip_Flop d_ff_49 (.Q(d_ff_49_q));  // open: clk, D, Qn, preset, en, reset
  D_Flip_Flop d_ff_50 (.Q(d_ff_50_q));  // open: clk, D, Qn, preset, en, reset
  D_Flip_Flop d_ff_51 (.Q(d_ff_51_q));  // open: clk, D, Qn, preset, en, reset
  D_Flip_Flop d_ff_52 (.Q(d_ff_52_q));  // open: clk, D, Qn, preset, en, reset
  D_Flip_Flop d_ff_53 (.Q(d_ff_53_q));  // open: clk, D, Qn, preset, en, reset
  D_Flip_Flop d_ff_54 (.Q(d_ff_54_q));  // open: clk, D, Qn, preset, en, reset
  D_Flip_Flop d_ff_55 (.Q(d_ff_55_q));  // open: clk, D, Qn, preset, en, reset
  D_Flip_Flop d_ff_56 (.Q(d_ff_56_q));  // open: clk, D, Qn, preset, en, reset
  D_Flip_Flop d_ff_57 (.Q(d_ff_57_q));  // open: clk, D, Qn, preset, en, reset
  D_Flip_Flop d_ff_58 (.Q(d_ff_58_q));  // open: clk, D, Qn, preset, en, reset
  D_Flip_Flop d_ff_59 (.Q(d_ff_59_q));  // open: clk, D, Qn, preset, en, reset
  D_Flip_Flop d_ff_60 (.Q(d_ff_60_q));  // open: clk, D, Qn, preset, en, reset
  D_Flip_Flop d_ff_61 (.Q(d_ff_61_q));  // open: clk, D, Qn, preset, en, reset
  D_Flip_Flop d_ff_62 (.Q(d_ff_62_q));  // open: clk, D, Qn, preset, en, reset
  D_Flip_Flop d_ff_63 (.Q(d_ff_63_q));  // open: clk, D, Qn, preset, en, reset
  D_Flip_Flop d_ff_64 (.Q(d_ff_64_q));  // open: clk, D, Qn, preset, en, reset
  D_Flip_Flop d_ff_65 (.Q(d_ff_65_q));  // open: clk, D, Qn, preset, en, reset
  D_Flip_Flop d_ff_66 (.Q(d_ff_66_q));  // open: clk, D, Qn, preset, en, reset
  D_Flip_Flop d_ff_67 (.Q(d_ff_67_q));  // open: clk, D, Qn, preset, en, reset
  D_Flip_Flop d_ff_68 (.Q(d_ff_68_q));  // open: clk, D, Qn, preset, en, reset
  D_Flip_Flop d_ff_69 (.Q(d_ff_69_q));  // open: clk, D, Qn, preset, en, reset
  D_Flip_Flop d_ff_70 (.Q(d_ff_70_q));  // open: clk, D, Qn, preset, en, reset
  and and_45 (and_45_out, and_44_out, d_ff_70_q);
  and and_46 (and_46_out, and_41_out, d_ff_67_q);
  and and_47 (and_47_out, and_42_out, d_ff_68_q);
  and and_48 (and_48_out, and_43_out, d_ff_69_q);
  and and_49 (and_49_out, and_44_out, d_ff_66_q);
  and and_50 (and_50_out, and_41_out, d_ff_63_q);
  and and_51 (and_51_out, and_42_out, d_ff_64_q);
  and and_52 (and_52_out, and_43_out, d_ff_65_q);
  and and_53 (and_53_out, and_44_out, d_ff_62_q);
  and and_54 (and_54_out, and_41_out, d_ff_59_q);
  and and_55 (and_55_out, and_42_out, d_ff_60_q);
  and and_56 (and_56_out, and_43_out, d_ff_61_q);
  and and_57 (and_57_out, and_44_out, d_ff_58_q);
  and and_58 (and_58_out, and_41_out, d_ff_55_q);
  and and_59 (and_59_out, and_42_out, d_ff_56_q);
  and and_60 (and_60_out, and_43_out, d_ff_57_q);
  and and_61 (and_61_out, and_44_out, d_ff_54_q);
  and and_62 (and_62_out, and_41_out, d_ff_51_q);
  and and_63 (and_63_out, and_42_out, d_ff_52_q);
  and and_64 (and_64_out, and_43_out, d_ff_53_q);
  and and_65 (and_65_out, and_44_out, d_ff_50_q);
  or or_4 (out_5, and_73_out, and_76_out, and_75_out, and_74_out);
  or or_5 (out_6, and_69_out, and_72_out, and_71_out, and_70_out);
  or or_6 (out_7, and_65_out, and_68_out, and_67_out, and_66_out);
  or or_7 (out_8, and_61_out, and_64_out, and_63_out, and_62_out);
  or or_8 (out_9, and_57_out, and_60_out, and_59_out, and_58_out);
  or or_9 (out_10, and_53_out, and_56_out, and_55_out, and_54_out);
  or or_10 (out_11, and_49_out, and_52_out, and_51_out, and_50_out);
  or or_11 (out_12, and_45_out, and_48_out, and_47_out, and_46_out);
  and and_66 (and_66_out, and_41_out, d_ff_47_q);
  and and_67 (and_67_out, and_42_out, d_ff_48_q);
  and and_68 (and_68_out, and_43_out, d_ff_49_q);
  and and_69 (and_69_out, and_44_out, d_ff_46_q);
  and and_70 (and_70_out, and_41_out, d_ff_43_q);
  and and_71 (and_71_out, and_42_out, d_ff_44_q);
  and and_72 (and_72_out, and_43_out, d_ff_45_q);
  and and_73 (and_73_out, and_44_out, d_ff_42_q);
  and and_74 (and_74_out, and_41_out, d_ff_39_q);
  and and_75 (and_75_out, and_42_out, d_ff_40_q);
  and and_76 (and_76_out, and_43_out, d_ff_41_q);

  // Notes on the sheet:
  //   Decodificador de Opcodes
  //   Registrador de Instrução (IR:AR)
  //   Decodificador de Dados
  //   R0 register
  //   R1 register
  //   R2 register
  //   R3 register
  //   OR circuit
  //   Contador de Programa (PC)
  //   AND circuit
  //   NOT circuit
  //   XOR circuit
  //   ADD circuit
  //   SUB circuit
  //   ST circuit
  //   LD circuit
  //   Seletor de Estágios (Micro-operações)
  //   Estagio 1 - busca
  //   Estagio 2 - decodificação
  //   Estagio 3 - execução
  //   Estagio 4 - escrita
  //   JC circuit
  //   JZ circuit
  //   JP circuit
  //   Barramento de Endereço - 2 bits (entrada)
  //   Barramento de dados - 8 bits (saída)
  //   Memória de Programa - 8x4 bits
endmodule
