// Logisim project contadorv2.0.circ as structural Verilog: 1 circuit, main circuit main
module main (
  input  in_1
);

  wire clock_1_out, t_ff_1_qn, t_ff_2_qn, t_ff_3_qn, t_ff_4_qn, t_ff_5_qn, t_ff_6_qn, t_ff_7_qn, t_ff_8_qn,
       t_ff_9_qn, t_ff_10_qn, t_ff_11_qn;

  Clock clock_1 (.out(clock_1_out));
  T_Flip_Flop t_ff_1 (.clk(clock_1_out), .T(in_1), .Qn(t_ff_1_qn));  // open: Q, preset, reset, en
  T_Flip_Flop t_ff_2 (.clk(t_ff_1_qn), .T(in_1), .Qn(t_ff_2_qn));  // open: Q, preset, reset, en
  T_Flip_Flop t_ff_3 (.clk(t_ff_2_qn), .T(in_1), .Qn(t_ff_3_qn));  // open: Q, preset, reset, en
  T_Flip_Flop t_ff_4 (.clk(t_ff_3_qn), .T(in_1), .Qn(t_ff_4_qn));  // open: Q, preset, reset, en
  T_Flip_Flop t_ff_5 (.clk(t_ff_4_qn), .T(in_1), .Qn(t_ff_5_qn));  // open: Q, preset, reset, en
  T_Flip_Flop t_ff_6 (.clk(t_ff_5_qn), .T(in_1), .Qn(t_ff_6_qn));  // open: Q, preset, reset, en
  T_Flip_Flop t_ff_7 (.clk(t_ff_6_qn), .T(in_1), .Qn(t_ff_7_qn));  // open: Q, preset, reset, en
  T_Flip_Flop t_ff_8 (.clk(t_ff_7_qn), .T(in_1), .Qn(t_ff_8_qn));  // open: Q, preset, reset, en
  T_Flip_Flop t_ff_9 (.clk(t_ff_8_qn), .T(in_1), .Qn(t_ff_9_qn));  // open: Q, preset, reset, en
  T_Flip_Flop t_ff_10 (.clk(t_ff_9_qn), .T(in_1), .Qn(t_ff_10_qn));  // open: Q, preset, reset, en
  T_Flip_Flop t_ff_11 (.clk(t_ff_10_qn), .T(in_1), .Qn(t_ff_11_qn));  // open: Q, preset, reset, en
  T_Flip_Flop t_ff_12 (.clk(t_ff_11_qn), .T(in_1));  // open: Q, Qn, preset, reset, en
endmodule
