// Logisim project shifters.circ as structural Verilog: 1 circuit, main circuit main
module main (
  input  in_1,
  input  in_2,
  input  in_3,
  input  in_4,
  input  in_5,
  input  in_6,
  input  in_7,
  input  in_8,
  input  in_9,
  input  in_10,
  input  in_11,
  input  in_12,
  input  in_13,
  input  in_14,
  input  in_15,
  input  in_16,
  input  in_17,
  input  in_18,
  input  in_19,
  input  in_20,
  input  in_21,
  input  in_22,
  input  in_23,
  input  in_24,
  input  in_25,
  input  in_26,
  input  in_27,
  input  in_28,
  input  in_29,
  input  in_30,
  input  in_31,
  input  in_32,
  input  in_33,
  input  in_34,
  input  in_35,
  input  in_36,
  input  in_37,
  input  in_38,
  input  in_39,
  input  in_40,
  input  in_41,
  input  in_42,
  input  in_43,
  input  in_44,
  input  in_45,
  input  in_46,
  input  in_47,
  input  in_48,
  input  in_49,
  input  in_50,
  input  in_51,
  input  in_52,
  input  in_53,
  input  in_54,
  output out_55,
  output out_56,
  output out_57,
  output out_58,
  output out_59,
  output out_60,
  output out_61,
  output out_62,
  output out_63,
  output out_64,
  output out_65,
  output out_66,
  output out_67,
  output out_68,
  output out_69,
  output out_70,
  output out_71,
  output out_72,
  output out_73,
  output out_74,
  output out_75,
  output out_76,
  output out_77,
  output out_78,
  output out_79,
  output out_80,
  output out_81,
  output out_82,
  output out_83,
  output out_84,
  output out_85,
  output out_86
);

  wire and_1_out, and_2_out, and_3_out, and_4_out, and_5_out, and_6_out, and_7_out, and_8_out, clock_1_out,
       d_ff_1_q, d_ff_2_q, d_ff_3_q, d_ff_4_q, d_ff_5_q, d_ff_6_q, d_ff_7_q, multiplexer_9_out,
       multiplexer_10_out, multiplexer_11_out, multiplexer_12_out, multiplexer_13_out, multiplexer_14_out,
       multiplexer_15_out, multiplexer_16_out, multiplexer_33_out, multiplexer_34_out, multiplexer_36_out,
       multiplexer_37_out, multiplexer_39_out, multiplexer_40_out, multiplexer_42_out, multiplexer_43_out,
       multiplexer_45_out, multiplexer_46_out, multiplexer_48_out, multiplexer_49_out, multiplexer_51_out,
       multiplexer_52_out, multiplexer_54_out, multiplexer_55_out, not_1_out, not_2_out, not_3_out,
       not_4_out, or_1_out;
  wire [1:0] demultiplexer_1_out1, demultiplexer_2_out1, demultiplexer_3_out1;

  Multiplexer multiplexer_1 (.in0(in_1), .in1(in_7), .out(out_55), .sel(in_4));  // open: en
  Multiplexer multiplexer_2 (.in0(in_7), .in1(in_19), .out(out_57), .sel(in_4));  // open: en
  Multiplexer multiplexer_3 (.in0(in_19), .in1(in_24), .out(out_59), .sel(in_4));  // open: en
  Multiplexer multiplexer_4 (.in0(in_24), .in1(in_26), .out(out_61), .sel(in_4));  // open: en
  Multiplexer multiplexer_5 (.in0(in_26), .in1(in_28), .out(out_63), .sel(in_4));  // open: en
  Multiplexer multiplexer_6 (.in0(in_28), .in1(in_30), .out(out_65), .sel(in_4));  // open: en
  Multiplexer multiplexer_7 (.in0(in_30), .in1(in_32), .out(out_67), .sel(in_4));  // open: en
  Multiplexer multiplexer_8 (.in0(in_32), .in1(in_34), .out(out_69), .sel(in_4));  // open: en
  Multiplexer multiplexer_9 (.in0(in_35), .in1(in_42), .out(multiplexer_9_out), .sel(in_40));  // open: en
  Multiplexer multiplexer_10 (.in0(in_42), .in1(in_45), .out(multiplexer_10_out), .sel(in_40));  // open: en
  Multiplexer multiplexer_11 (.in0(in_45), .in1(in_46), .out(multiplexer_11_out), .sel(in_40));  // open: en
  Multiplexer multiplexer_12 (.in0(in_46), .in1(in_47), .out(multiplexer_12_out), .sel(in_40));  // open: en
  Multiplexer multiplexer_13 (.in0(in_47), .in1(in_48), .out(multiplexer_13_out), .sel(in_40));  // open: en
  Multiplexer multiplexer_14 (.in0(in_48), .in1(in_49), .out(multiplexer_14_out), .sel(in_40));  // open: en
  Multiplexer multiplexer_15 (.in0(in_49), .in1(in_52), .out(multiplexer_15_out), .sel(in_40));  // open: en
  Multiplexer multiplexer_16 (.in0(in_52), .in1(in_53), .out(multiplexer_16_out), .sel(in_40));  // open: en
  Multiplexer multiplexer_17 (
    .in0(multiplexer_9_out), .in1(multiplexer_11_out), .out(out_79), .sel(in_41));  // open: en
  Multiplexer multiplexer_18 (
    .in0(multiplexer_10_out), .in1(multiplexer_12_out), .out(out_80), .sel(in_41));  // open: en
  Multiplexer multiplexer_19 (
    .in0(multiplexer_11_out), .in1(multiplexer_13_out), .out(out_81), .sel(in_41));  // open: en
  Multiplexer multiplexer_20 (
    .in0(multiplexer_12_out), .in1(multiplexer_14_out), .out(out_82), .sel(in_41));  // open: en
  Multiplexer multiplexer_21 (
    .in0(multiplexer_13_out), .in1(multiplexer_15_out), .out(out_83), .sel(in_41));  // open: en
  Multiplexer multiplexer_22 (
    .in0(multiplexer_14_out), .in1(multiplexer_16_out), .out(out_84), .sel(in_41));  // open: en
  Multiplexer multiplexer_23 (.in0(multiplexer_15_out), .in1(in_50), .out(out_85), .sel(in_41));  // open: en
  Multiplexer multiplexer_24 (.in0(multiplexer_16_out), .in1(in_54), .out(out_86), .sel(in_41));  // open: en
  Multiplexer multiplexer_25 (.in0(in_2), .in1(in_3), .out(out_56), .sel(in_5));  // open: en
  Multiplexer multiplexer_26 (.in0(in_16), .in1(in_2), .out(out_58), .sel(in_5));  // open: en
  Multiplexer multiplexer_27 (.in0(in_23), .in1(in_16), .out(out_60), .sel(in_5));  // open: en
  Multiplexer multiplexer_28 (.in0(in_25), .in1(in_23), .out(out_62), .sel(in_5));  // open: en
  Multiplexer multiplexer_29 (.in0(in_27), .in1(in_25), .out(out_64), .sel(in_5));  // open: en
  Multiplexer multiplexer_30 (.in0(in_29), .in1(in_27), .out(out_66), .sel(in_5));  // open: en
  Multiplexer multiplexer_31 (.in0(in_31), .in1(in_29), .out(out_68), .sel(in_5));  // open: en
  Multiplexer multiplexer_32 (.in0(in_33), .in1(in_31), .out(out_70), .sel(in_5));  // open: en
  Clock clock_1 (.out(clock_1_out));
  D_Flip_Flop d_ff_1 (.clk(clock_1_out), .D(in_51), .Q(d_ff_1_q));  // open: Qn, preset, en, reset
  Demultiplexer #(.select(2)) demultiplexer_1 (
    .out1(demultiplexer_1_out1[0]), .out2(demultiplexer_1_out1[1]), .in(in_22), .sel({in_17, in_18}),
    .en(in_6));  // open: out0, out3
  Demultiplexer #(.select(2)) demultiplexer_2 (
    .out1(demultiplexer_2_out1[0]), .out2(demultiplexer_2_out1[1]), .in(in_21), .sel({in_17, in_18}),
    .en(in_6));  // open: out0, out3
  Demultiplexer #(.select(2)) demultiplexer_3 (
    .out1(demultiplexer_3_out1[0]), .out2(demultiplexer_3_out1[1]), .in(in_20), .sel({in_17, in_18}),
    .en(in_6));  // open: out0, out3
  not not_1 (not_1_out, in_44);
  not not_2 (not_2_out, in_43);
  not not_3 (not_3_out, in_43);
  not not_4 (not_4_out, in_44);
  D_Flip_Flop d_ff_2 (.clk(clock_1_out), .D(d_ff_1_q), .Q(d_ff_2_q));  // open: Qn, preset, en, reset
  and and_1 (and_1_out, not_1_out, not_2_out);
  and and_2 (and_2_out, not_3_out, in_44);
  and and_3 (and_3_out, not_4_out, in_43);
  and and_4 (and_4_out, in_44, in_43);
  D_Flip_Flop d_ff_3 (.clk(clock_1_out), .D(d_ff_2_q), .Q(d_ff_3_q));  // open: Qn, preset, en, reset
  Multiplexer #(.select(2)) multiplexer_33 (
    .in0(in_8), .in1(1'b0), .in2(in_9), .in3(in_9), .out(multiplexer_33_out), .sel(demultiplexer_1_out1));  // open: en
  Multiplexer #(.select(2)) multiplexer_34 (
    .in0(multiplexer_33_out), .in1(1'b0), .in2(multiplexer_39_out), .in3(multiplexer_39_out),
    .out(multiplexer_34_out), .sel(demultiplexer_2_out1));  // open: en
  Multiplexer #(.select(2)) multiplexer_35 (
    .in0(multiplexer_34_out), .in1(1'b0), .in2(multiplexer_46_out), .in3(multiplexer_46_out), .out(out_71),
    .sel(demultiplexer_3_out1));  // open: en
  and and_5 (and_5_out, in_36, and_1_out);
  and and_6 (and_6_out, in_37, and_2_out);
  and and_7 (and_7_out, in_38, and_3_out);
  and and_8 (and_8_out, in_39, and_4_out);
  D_Flip_Flop d_ff_4 (.clk(clock_1_out), .D(d_ff_3_q), .Q(d_ff_4_q));  // open: Qn, preset, en, reset
  Multiplexer #(.select(2)) multiplexer_36 (
    .in0(in_9), .in1(in_8), .in2(in_10), .in3(in_10), .out(multiplexer_36_out), .sel(demultiplexer_1_out1));  // open: en
  Multiplexer #(.select(2)) multiplexer_37 (
    .in0(multiplexer_36_out), .in1(1'b0), .in2(multiplexer_42_out), .in3(multiplexer_42_out),
    .out(multiplexer_37_out), .sel(demultiplexer_2_out1));  // open: en
  Multiplexer #(.select(2)) multiplexer_38 (
    .in0(multiplexer_37_out), .in1(1'b0), .in2(multiplexer_49_out), .in3(multiplexer_49_out), .out(out_72),
    .sel(demultiplexer_3_out1));  // open: en
  or or_1 (or_1_out, and_5_out, and_6_out, and_7_out, and_8_out);
  Multiplexer #(.select(2)) multiplexer_39 (
    .in0(in_10), .in1(in_9), .in2(in_11), .in3(in_11), .out(multiplexer_39_out), .sel(demultiplexer_1_out1));  // open: en
  Multiplexer #(.select(2)) multiplexer_40 (
    .in0(multiplexer_39_out), .in1(multiplexer_33_out), .in2(multiplexer_45_out), .in3(multiplexer_45_out),
    .out(multiplexer_40_out), .sel(demultiplexer_2_out1));  // open: en
  Multiplexer #(.select(2)) multiplexer_41 (
    .in0(multiplexer_40_out), .in1(1'b0), .in2(multiplexer_52_out), .in3(multiplexer_52_out), .out(out_73),
    .sel(demultiplexer_3_out1));  // open: en
  D_Flip_Flop d_ff_5 (.clk(clock_1_out), .D(d_ff_4_q), .Q(d_ff_5_q));  // open: Qn, preset, en, reset
  Multiplexer #(.select(2)) multiplexer_42 (
    .in0(in_11), .in1(in_10), .in2(in_12), .in3(in_12), .out(multiplexer_42_out), .sel(demultiplexer_1_out1));  // open: en
  Multiplexer #(.select(2)) multiplexer_43 (
    .in0(multiplexer_42_out), .in1(multiplexer_36_out), .in2(multiplexer_48_out), .in3(multiplexer_48_out),
    .out(multiplexer_43_out), .sel(demultiplexer_2_out1));  // open: en
  Multiplexer #(.select(2)) multiplexer_44 (
    .in0(multiplexer_43_out), .in1(1'b0), .in2(multiplexer_55_out), .in3(multiplexer_55_out), .out(out_74),
    .sel(demultiplexer_3_out1));  // open: en
  D_Flip_Flop d_ff_6 (.clk(clock_1_out), .D(d_ff_5_q), .Q(d_ff_6_q));  // open: Qn, preset, en, reset
  Multiplexer #(.select(2)) multiplexer_45 (
    .in0(in_12), .in1(in_11), .in2(in_13), .in3(in_13), .out(multiplexer_45_out), .sel(demultiplexer_1_out1));  // open: en
  Multiplexer #(.select(2)) multiplexer_46 (
    .in0(multiplexer_45_out), .in1(multiplexer_39_out), .in2(multiplexer_51_out), .in3(multiplexer_51_out),
    .out(multiplexer_46_out), .sel(demultiplexer_2_out1));  // open: en
  Multiplexer #(.select(2)) multiplexer_47 (
    .in0(multiplexer_46_out), .in1(multiplexer_34_out), .in2(1'b0), .in3(1'b0), .out(out_75),
    .sel(demultiplexer_3_out1));  // open: en
  D_Flip_Flop d_ff_7 (.clk(clock_1_out), .D(d_ff_6_q), .Q(d_ff_7_q));  // open: Qn, preset, en, reset
  Multiplexer #(.select(2)) multiplexer_48 (
    .in0(in_13), .in1(in_12), .in2(in_14), .in3(in_14), .out(multiplexer_48_out), .sel(demultiplexer_1_out1));  // open: en
  Multiplexer #(.select(2)) multiplexer_49 (
    .in0(multiplexer_48_out), .in1(multiplexer_42_out), .in2(multiplexer_54_out), .in3(multiplexer_54_out),
    .out(multiplexer_49_out), .sel(demultiplexer_2_out1));  // open: en
  Multiplexer #(.select(2)) multiplexer_50 (
    .in0(multiplexer_49_out), .in1(multiplexer_37_out), .in2(1'b0), .in3(1'b0), .out(out_76),
    .sel(demultiplexer_3_out1));  // open: en
  D_Flip_Flop d_ff_8 (.clk(clock_1_out), .D(d_ff_7_q));  // open: Q, Qn, preset, en, reset
  Multiplexer #(.select(2)) multiplexer_51 (
    .in0(in_14), .in1(in_13), .in2(in_15), .in3(in_15), .out(multiplexer_51_out), .sel(demultiplexer_1_out1));  // open: en
  Multiplexer #(.select(2)) multiplexer_52 (
    .in0(multiplexer_51_out), .in1(multiplexer_45_out), .in2(1'b0), .in3(1'b0), .out(multiplexer_52_out),
    .sel(demultiplexer_2_out1));  // open: en
  Multiplexer #(.select(2)) multiplexer_53 (
    .in0(multiplexer_52_out), .in1(multiplexer_40_out), .in2(1'b0), .in3(1'b0), .out(out_77),
    .sel(demultiplexer_3_out1));  // open: en
  Multiplexer #(.select(2)) multiplexer_54 (
    .in0(in_15), .in1(in_14), .in2(1'b0), .in3(1'b0), .out(multiplexer_54_out), .sel(demultiplexer_1_out1));  // open: en
  Multiplexer #(.select(2)) multiplexer_55 (
    .in0(multiplexer_54_out), .in1(multiplexer_48_out), .in2(1'b0), .in3(1'b0), .out(multiplexer_55_out),
    .sel(demultiplexer_2_out1));  // open: en
  Multiplexer #(.select(2)) multiplexer_56 (
    .in0(multiplexer_55_out), .in1(multiplexer_43_out), .in2(1'b0), .in3(1'b0), .out(out_78),
    .sel(demultiplexer_3_out1));  // open: en

  // Notes on the sheet:
  //   Deslocador Barrel
  //   MUX - Multiplexador
endmodule
