// Logisim project memória-4x8-registradores.circ as structural Verilog: 1 circuit, main circuit main
module main (
  input  in_1,
  input  in_2,
  input  in_3,
  input  in_4,
  input  in_5,
  input  in_6,
  input  in_7,
  input  in_8,
  input  in_9,
  input  in_10,
  input  in_11,
  input  in_12,
  input  in_13,
  input  in_14,
  input  in_15,
  input  in_16,
  input  in_17,
  input  in_18,
  input  in_19,
  input  in_20,
  input  in_21,
  input  in_22,
  input  in_23,
  input  in_24,
  input  in_25,
  input  in_26,
  input  in_27,
  input  in_28,
  input  in_29,
  input  in_30,
  input  in_31,
  input  in_32,
  input  in_33,
  input  in_34,
  input  in_35,
  input  in_36,
  output out_37,
  output out_38,
  output out_39,
  output out_40,
  output out_41,
  output out_42,
  output out_43,
  output out_44,
  output out_45,
  output out_46,
  output out_47,
  output out_48,
  output out_49,
  output out_50,
  output out_51,
  output out_52,
  output out_53,
  output out_54,
  output out_55,
  output out_56,
  output out_57,
  output out_58,
  output out_59,
  output out_60,
  output out_61,
  output out_62,
  output out_63,
  output out_64,
  output out_65,
  output out_66,
  output out_67,
  output out_68
);

  wire and_1_out, and_2_out, and_3_out, and_4_out, and_5_out, and_6_out, and_7_out, and_8_out, and_9_out,
       and_10_out, and_11_out, and_12_out, and_13_out, and_14_out, and_15_out, and_16_out, and_17_out,
       and_18_out, and_19_out, and_20_out, and_21_out, and_22_out, and_23_out, and_24_out, and_25_out,
       and_26_out, and_27_out, and_28_out, and_29_out, and_30_out, and_31_out, and_32_out, and_33_out,
       and_34_out, and_35_out, and_36_out, and_37_out, and_38_out, and_39_out, and_40_out, and_41_out,
       and_42_out, and_43_out, and_44_out, and_45_out, and_46_out, and_47_out, and_48_out, and_49_out,
       and_50_out, and_51_out, and_52_out, and_53_out, and_54_out, and_55_out, and_56_out, and_57_out,
       and_58_out, and_59_out, and_60_out, and_61_out, and_62_out, and_63_out, and_64_out, nor_2_out,
       nor_4_out, nor_6_out, nor_8_out, nor_10_out, nor_12_out, nor_14_out, nor_16_out, nor_18_out,
       nor_20_out, nor_22_out, nor_24_out, nor_26_out, nor_28_out, nor_30_out, nor_32_out, nor_34_out,
       nor_36_out, nor_38_out, nor_40_out, nor_42_out, nor_44_out, nor_46_out, nor_48_out, nor_50_out,
       nor_52_out, nor_54_out, nor_56_out, nor_58_out, nor_60_out, nor_62_out, nor_64_out, not_1_out,
       not_2_out, not_3_out, not_4_out, not_5_out, not_6_out, not_7_out, not_8_out, not_9_out, not_10_out,
       not_11_out, not_12_out, not_13_out, not_14_out, not_15_out, not_16_out, not_17_out, not_18_out,
       not_19_out, not_20_out, not_21_out, not_22_out, not_23_out, not_24_out, not_25_out, not_26_out,
       not_27_out, not_28_out, not_29_out, not_30_out, not_31_out, not_32_out;

  not not_1 (not_1_out, in_1);
  not not_2 (not_2_out, in_10);
  not not_3 (not_3_out, in_19);
  not not_4 (not_4_out, in_28);
  and and_1 (and_1_out, not_1_out, in_9);
  and and_2 (and_2_out, in_1, in_9);
  and and_3 (and_3_out, not_3_out, in_27);
  and and_4 (and_4_out, in_19, in_27);
  and and_5 (and_5_out, not_2_out, in_18);
  and and_6 (and_6_out, in_10, in_18);
  and and_7 (and_7_out, not_4_out, in_36);
  and and_8 (and_8_out, in_28, in_36);
  nor nor_1 (out_37, and_1_out, nor_2_out);
  nor nor_2 (nor_2_out, out_37, and_2_out);
  nor nor_3 (out_45, and_5_out, nor_4_out);
  nor nor_4 (nor_4_out, out_45, and_6_out);
  nor nor_5 (out_53, and_3_out, nor_6_out);
  nor nor_6 (nor_6_out, out_53, and_4_out);
  nor nor_7 (out_61, and_7_out, nor_8_out);
  nor nor_8 (nor_8_out, out_61, and_8_out);
  not not_5 (not_5_out, in_2);
  not not_6 (not_6_out, in_11);
  not not_7 (not_7_out, in_20);
  not not_8 (not_8_out, in_29);
  and and_9 (and_9_out, not_5_out, in_9);
  and and_10 (and_10_out, in_2, in_9);
  and and_11 (and_11_out, not_7_out, in_27);
  and and_12 (and_12_out, in_20, in_27);
  nor nor_9 (out_38, and_9_out, nor_10_out);
  nor nor_10 (nor_10_out, out_38, and_10_out);
  and and_13 (and_13_out, not_6_out, in_18);
  and and_14 (and_14_out, in_11, in_18);
  nor nor_11 (out_54, and_11_out, nor_12_out);
  nor nor_12 (nor_12_out, out_54, and_12_out);
  and and_15 (and_15_out, not_8_out, in_36);
  and and_16 (and_16_out, in_29, in_36);
  nor nor_13 (out_46, and_13_out, nor_14_out);
  nor nor_14 (nor_14_out, out_46, and_14_out);
  nor nor_15 (out_62, and_15_out, nor_16_out);
  nor nor_16 (nor_16_out, out_62, and_16_out);
  not not_9 (not_9_out, in_3);
  not not_10 (not_10_out, in_12);
  not not_11 (not_11_out, in_21);
  not not_12 (not_12_out, in_30);
  and and_17 (and_17_out, not_9_out, in_9);
  and and_18 (and_18_out, in_3, in_9);
  and and_19 (and_19_out, not_10_out, in_18);
  and and_20 (and_20_out, in_12, in_18);
  and and_21 (and_21_out, not_11_out, in_27);
  and and_22 (and_22_out, in_21, in_27);
  and and_23 (and_23_out, not_12_out, in_36);
  and and_24 (and_24_out, in_30, in_36);
  nor nor_17 (out_39, and_17_out, nor_18_out);
  nor nor_18 (nor_18_out, out_39, and_18_out);
  nor nor_19 (out_47, and_19_out, nor_20_out);
  nor nor_20 (nor_20_out, out_47, and_20_out);
  nor nor_21 (out_55, and_21_out, nor_22_out);
  nor nor_22 (nor_22_out, out_55, and_22_out);
  nor nor_23 (out_63, and_23_out, nor_24_out);
  nor nor_24 (nor_24_out, out_63, and_24_out);
  not not_13 (not_13_out, in_4);
  not not_14 (not_14_out, in_22);
  not not_15 (not_15_out, in_13);
  not not_16 (not_16_out, in_31);
  and and_25 (and_25_out, not_13_out, in_9);
  and and_26 (and_26_out, in_4, in_9);
  and and_27 (and_27_out, not_15_out, in_18);
  and and_28 (and_28_out, in_13, in_18);
  and and_29 (and_29_out, not_14_out, in_27);
  and and_30 (and_30_out, in_22, in_27);
  and and_31 (and_31_out, not_16_out, in_36);
  and and_32 (and_32_out, in_31, in_36);
  nor nor_25 (out_40, and_25_out, nor_26_out);
  nor nor_26 (nor_26_out, out_40, and_26_out);
  nor nor_27 (out_48, and_27_out, nor_28_out);
  nor nor_28 (nor_28_out, out_48, and_28_out);
  nor nor_29 (out_56, and_29_out, nor_30_out);
  nor nor_30 (nor_30_out, out_56, and_30_out);
  nor nor_31 (out_64, and_31_out, nor_32_out);
  nor nor_32 (nor_32_out, out_64, and_32_out);
  not not_17 (not_17_out, in_5);
  not not_18 (not_18_out, in_14);
  not not_19 (not_19_out, in_23);
  not not_20 (not_20_out, in_32);
  and and_33 (and_33_out, not_17_out, in_9);
  and and_34 (and_34_out, in_5, in_9);
  and and_35 (and_35_out, not_18_out, in_18);
  and and_36 (and_36_out, in_14, in_18);
  and and_37 (and_37_out, not_19_out, in_27);
  and and_38 (and_38_out, in_23, in_27);
  and and_39 (and_39_out, not_20_out, in_36);
  and and_40 (and_40_out, in_32, in_36);
  nor nor_33 (out_41, and_33_out, nor_34_out);
  nor nor_34 (nor_34_out, out_41, and_34_out);
  nor nor_35 (out_49, and_35_out, nor_36_out);
  nor nor_36 (nor_36_out, out_49, and_36_out);
  nor nor_37 (out_57, and_37_out, nor_38_out);
  nor nor_38 (nor_38_out, out_57, and_38_out);
  nor nor_39 (out_65, and_39_out, nor_40_out);
  nor nor_40 (nor_40_out, out_65, and_40_out);
  not not_21 (not_21_out, in_6);
  not not_22 (not_22_out, in_15);
  not not_23 (not_23_out, in_24);
  not not_24 (not_24_out, in_33);
  and and_41 (and_41_out, not_21_out, in_9);
  and and_42 (and_42_out, in_6, in_9);
  and and_43 (and_43_out, not_22_out, in_18);
  and and_44 (and_44_out, in_15, in_18);
  and and_45 (and_45_out, not_23_out, in_27);
  and and_46 (and_46_out, in_24, in_27);
  and and_47 (and_47_out, not_24_out, in_36);
  and and_48 (and_48_out, in_33, in_36);
  nor nor_41 (out_42, and_41_out, nor_42_out);
  nor nor_42 (nor_42_out, out_42, and_42_out);
  nor nor_43 (out_50, and_43_out, nor_44_out);
  nor nor_44 (nor_44_out, out_50, and_44_out);
  nor nor_45 (out_58, and_45_out, nor_46_out);
  nor nor_46 (nor_46_out, out_58, and_46_out);
  nor nor_47 (out_66, and_47_out, nor_48_out);
  nor nor_48 (nor_48_out, out_66, and_48_out);
  not not_25 (not_25_out, in_7);
  not not_26 (not_26_out, in_16);
  not not_27 (not_27_out, in_25);
  not not_28 (not_28_out, in_34);
  and and_49 (and_49_out, not_25_out, in_9);
  and and_50 (and_50_out, in_7, in_9);
  and and_51 (and_51_out, not_26_out, in_18);
  and and_52 (and_52_out, in_16, in_18);
  and and_53 (and_53_out, not_27_out, in_27);
  and and_54 (and_54_out, in_25, in_27);
  and and_55 (and_55_out, not_28_out, in_36);
  and and_56 (and_56_out, in_34, in_36);
  nor nor_49 (out_43, and_49_out, nor_50_out);
  nor nor_50 (nor_50_out, out_43, and_50_out);
  nor nor_51 (out_51, and_51_out, nor_52_out);
  nor nor_52 (nor_52_out, out_51, and_52_out);
  nor nor_53 (out_59, and_53_out, nor_54_out);
  nor nor_54 (nor_54_out, out_59, and_54_out);
  nor nor_55 (out_67, and_55_out, nor_56_out);
  nor nor_56 (nor_56_out, out_67, and_56_out);
  not not_29 (not_29_out, in_8);
  not not_30 (not_30_out, in_17);
  not not_31 (not_31_out, in_26);
  not not_32 (not_32_out, in_35);
  and and_57 (and_57_out, not_29_out, in_9);
  and and_58 (and_58_out, in_8, in_9);
  and and_59 (and_59_out, not_31_out, in_27);
  and and_60 (and_60_out, in_26, in_27);
  and and_61 (and_61_out, not_30_out, in_18);
  and and_62 (and_62_out, in_17, in_18);
  and and_63 (and_63_out, not_32_out, in_36);
  and and_64 (and_64_out, in_35, in_36);
  nor nor_57 (out_44, and_57_out, nor_58_out);
  nor nor_58 (nor_58_out, out_44, and_58_out);
  nor nor_59 (out_52, and_61_out, nor_60_out);
  nor nor_60 (nor_60_out, out_52, and_62_out);
  nor nor_61 (out_60, and_59_out, nor_62_out);
  nor nor_62 (nor_62_out, out_60, and_60_out);
  nor nor_63 (out_68, and_63_out, nor_64_out);
  nor nor_64 (nor_64_out, out_68, and_64_out);
endmodule
