// Logisim project mux-demux.circ as structural Verilog: 1 circuit, main circuit main
module main (
  input  in_1,
  input  in_2,
  input  in_3,
  input  in_4,
  input  [1:0] in_5,
  input  in_6,
  input  [1:0] in_7,
  output out_8,
  output out_9,
  output out_10,
  output out_11,
  output out_12
);

  Demultiplexer #(.select(2)) demultiplexer_1 (
    .out0(out_9), .out1(out_10), .out2(out_11), .out3(out_12), .in(in_6), .sel(in_7));  // open: en
  Multiplexer #(.select(2)) multiplexer_1 (
    .in0(in_1), .in1(in_2), .in2(in_3), .in3(in_4), .out(out_8), .sel(in_5));  // open: en
endmodule
