// Logisim project contador.circ as structural Verilog: 1 circuit, main circuit main
module main (
  input  in_1,
  input  in_2,
  input  in_3,
  output out_4,
  output out_5,
  output out_6,
  output out_7,
  output out_8
);

  wire and_1_out, and_2_out, and_3_out, clock_1_out, nand_1_out, or_1_out;

  Clock clock_1 (.out(clock_1_out));
  nand nand_1 (nand_1_out, in_2, out_4);
  T_Flip_Flop t_ff_1 (.clk(clock_1_out), .T(nand_1_out), .Q(out_8), .reset(in_3), .en(nand_1_out));  // open: Qn, preset
  and and_1 (and_1_out, out_8, out_7);
  T_Flip_Flop t_ff_2 (.clk(clock_1_out), .T(out_8), .Q(out_7), .reset(in_3), .en(nand_1_out));  // open: Qn, preset
  T_Flip_Flop t_ff_3 (.clk(clock_1_out), .T(and_1_out), .Q(out_6), .reset(in_3), .en(nand_1_out));  // open: Qn, preset
  and and_2 (and_2_out, out_8, out_7, out_6);
  T_Flip_Flop t_ff_4 (.clk(clock_1_out), .T(and_2_out), .Q(out_5), .reset(in_3), .en(nand_1_out));  // open: Qn, preset
  and and_3 (and_3_out, out_8, out_7, out_6, out_5);
  or or_1 (or_1_out, in_1, and_3_out);
  T_Flip_Flop t_ff_5 (.clk(clock_1_out), .T(or_1_out), .Q(out_4), .reset(in_3), .en(nand_1_out));  // open: Qn, preset
endmodule
