// Logisim project decoding_register.circ as structural Verilog: 2 circuits, main circuit main
module main (
  input  in_1,
  output out_2,
  output out_3
);

  wire clock_1_out;

  Clock clock_1 (.out(clock_1_out));
  decoding_register decoding_register_1 (.dec_signal(clock_1_out), .inst(in_1), .inst_dec(out_2), .inst_exec(out_3));
endmodule

module decoding_register (
  input  dec_signal,
  input  inst,
  output inst_dec,
  output inst_exec
);

  D_Flip_Flop #(.trigger("falling")) d_ff_1 (.clk(dec_signal), .D(inst), .Q(inst_dec));  // open: Qn, preset, en, reset
  D_Flip_Flop #(.trigger("falling")) d_ff_2 (
    .clk(dec_signal), .D(inst_dec), .Q(inst_exec));  // open: Qn, preset, en, reset
endmodule
