// Logisim project seletor_paralelo_estágios.circ as structural Verilog: 1 circuit, main circuit main
module main (
  input  in_1,
  input  in_2,
  input  in_3
);

  wire and_1_out, and_2_out, and_3_out, and_4_out, multiplexer_1_out, multiplexer_2_out, multiplexer_3_out,
       multiplexer_4_out, multiplexer_5_out, multiplexer_6_out, multiplexer_7_out, multiplexer_8_out,
       multiplexer_9_out, multiplexer_10_out, multiplexer_11_out, multiplexer_12_out, not_1_out, not_2_out,
       not_3_out, not_4_out;

  not not_1 (not_1_out, in_2);
  not not_2 (not_2_out, in_1);
  not not_3 (not_3_out, in_1);
  not not_4 (not_4_out, in_2);
  and and_1 (and_1_out, not_1_out, not_2_out);
  LED led_1 (.in(and_1_out));
  and and_2 (and_2_out, not_3_out, in_2);
  LED led_2 (.in(and_2_out));
  and and_3 (and_3_out, not_4_out, in_1);
  LED led_3 (.in(and_3_out));
  and and_4 (and_4_out, in_2, in_1);
  LED led_4 (.in(and_4_out));
  Multiplexer multiplexer_1 (.in0(and_1_out), .in1(and_2_out), .out(multiplexer_1_out), .sel(in_3));  // open: en
  Multiplexer multiplexer_2 (.in0(and_2_out), .in1(and_3_out), .out(multiplexer_2_out), .sel(in_3));  // open: en
  Multiplexer multiplexer_3 (.in0(and_3_out), .in1(and_4_out), .out(multiplexer_3_out), .sel(in_3));  // open: en
  Multiplexer multiplexer_4 (.in0(and_4_out), .in1(and_1_out), .out(multiplexer_4_out), .sel(in_3));  // open: en
  LED led_5 (.in(multiplexer_1_out));
  LED led_6 (.in(multiplexer_2_out));
  LED led_7 (.in(multiplexer_3_out));
  LED led_8 (.in(multiplexer_4_out));
  Multiplexer multiplexer_5 (
    .in0(multiplexer_1_out), .in1(multiplexer_2_out), .out(multiplexer_5_out), .sel(in_3));  // open: en
  LED led_9 (.in(multiplexer_5_out));
  Multiplexer multiplexer_6 (
    .in0(multiplexer_2_out), .in1(multiplexer_3_out), .out(multiplexer_6_out), .sel(in_3));  // open: en
  LED led_10 (.in(multiplexer_6_out));
  Multiplexer multiplexer_7 (
    .in0(multiplexer_3_out), .in1(multiplexer_4_out), .out(multiplexer_7_out), .sel(in_3));  // open: en
  LED led_11 (.in(multiplexer_7_out));
  Multiplexer multiplexer_8 (
    .in0(multiplexer_4_out), .in1(multiplexer_1_out), .out(multiplexer_8_out), .sel(in_3));  // open: en
  LED led_12 (.in(multiplexer_8_out));
  Multiplexer multiplexer_9 (
    .in0(multiplexer_5_out), .in1(multiplexer_6_out), .out(multiplexer_9_out), .sel(in_3));  // open: en
  LED led_13 (.in(multiplexer_9_out));
  Multiplexer multiplexer_10 (
    .in0(multiplexer_6_out), .in1(multiplexer_7_out), .out(multiplexer_10_out), .sel(in_3));  // open: en
  LED led_14 (.in(multiplexer_10_out));
  Multiplexer multiplexer_11 (
    .in0(multiplexer_7_out), .in1(multiplexer_8_out), .out(multiplexer_11_out), .sel(in_3));  // open: en
  LED led_15 (.in(multiplexer_11_out));
  Multiplexer multiplexer_12 (
    .in0(multiplexer_8_out), .in1(multiplexer_5_out), .out(multiplexer_12_out), .sel(in_3));  // open: en
  LED led_16 (.in(multiplexer_12_out));

  // Notes on the sheet:
  //   Decodificador Paralelo de Estágios
endmodule
