// Logisim project Dispositivos Externos (TESTES).circ as structural Verilog: 4 circuits, main circuit main
module main (
  input  in_1,
  input  in_2,
  input  in_3,
  input  in_4,
  input  in_5,
  input  in_6,
  input  in_7,
  input  in_8,
  input  in_9,
  input  in_10,
  input  in_11,
  input  in_12,
  input  in_13,
  input  in_14,
  input  in_15,
  input  in_16,
  input  in_17,
  input  in_18,
  input  in_19,
  input  in_20,
  input  in_21,
  input  in_22,
  input  in_23,
  input  in_24,
  input  in_25,
  input  P0_6,
  input  in_27,
  input  in_28,
  input  in_29,
  input  in_30,
  input  in_31,
  input  in_32,
  input  in_33,
  input  in_34,
  input  P0_7,
  input  in_36,
  input  in_37,
  input  in_38,
  input  in_39,
  input  in_40,
  input  in_41,
  input  in_42,
  input  in_43,
  output out_44,
  output out_45,
  output out_46,
  output out_47,
  output out_48,
  output out_49,
  output out_50,
  output out_51,
  output out_52,
  output out_53,
  output out_54,
  output out_55,
  output out_56,
  output out_57,
  output out_58,
  output out_59,
  output out_60,
  output out_61,
  output out_62,
  output out_63,
  output out_64,
  output out_65,
  output out_66,
  output out_67
);

  wire _0_out, _1_out, _2_out, _3_out, _4_out, _5_out, _6_out, _7_out, clock_1_out, controlled_buffer_25_out,
       controlled_buffer_26_out, controlled_buffer_27_out, controlled_buffer_28_out,
       controlled_buffer_29_out, controlled_buffer_30_out, controlled_buffer_31_out,
       controlled_buffer_32_out, not_1_out, not_2_out, not_3_out, not_4_out, not_5_out, not_6_out, not_7_out,
       not_8_out, not_9_out, not_10_out, not_11_out, not_12_out, not_13_out, not_14_out, not_15_out,
       or_1_out, or_2_out, or_3_out, undriven, undriven_2, undriven_3, undriven_4, undriven_5, undriven_6,
       undriven_7, undriven_8;
  wire [2:0] and_1_out;
  wire [7:0] controlled_buffer_9_out, ram_1_data;

  Button _0 (.out(_0_out));
  Button _1 (.out(_1_out));
  Button _2 (.out(_2_out));
  Button _3 (.out(_3_out));
  Button _4 (.out(_4_out));
  Button _5 (.out(_5_out));
  Button _6 (.out(_6_out));
  Button _7 (.out(_7_out));
  Clock clock_1 (.out(clock_1_out));
  TTY tty_1 (.data({in_23, in_22, in_19, in_15, and_1_out}), .clk(clock_1_out), .we(in_16), .clr(in_13));
  not not_1 (not_1_out, _0_out);
  not not_2 (not_2_out, _2_out);
  not not_3 (not_3_out, _4_out);
  not not_4 (not_4_out, _6_out);
  or or_1 (or_1_out, _1_out, _3_out, _5_out, _7_out);
  not not_5 (not_5_out, _0_out);
  not not_6 (not_6_out, _0_out);
  not not_7 (not_7_out, _4_out);
  not not_8 (not_8_out, _5_out);
  or or_2 (or_2_out, _2_out, _3_out, _6_out, _7_out);
  not not_9 (not_9_out, _0_out);
  not not_10 (not_10_out, _1_out);
  not not_11 (not_11_out, _2_out);
  not not_12 (not_12_out, _3_out);
  or or_3 (or_3_out, _4_out, _5_out, _6_out, _7_out);
  and and_1 (and_1_out[0], not_1_out, not_2_out, not_3_out, not_4_out, or_1_out);
  and and_2 (and_1_out[1], not_5_out, not_6_out, not_7_out, not_8_out, or_2_out);
  and and_3 (and_1_out[2], not_9_out, not_10_out, not_11_out, not_12_out, or_3_out);
  LED led_1 (.in(and_1_out[0]));
  LED led_2 (.in(and_1_out[1]));
  LED led_3 (.in(and_1_out[2]));
  instruction_decode instruction_decode_1 (
    .in_1(in_12), .in_2(in_14), .in_3(in_17), .in_4(in_20), .out_5(out_49), .out_6(out_50), .out_7(out_51));
  binary_counter binary_counter_1 (
    .in_1(in_8), .in_2(in_10), .in_3(in_11), .out_4(out_44), .out_5(out_45), .out_6(out_46), .out_7(out_47),
    .out_8(out_48));
  TTY tty_2 (.data({in_23, in_22, in_19, out_45, out_46, out_47, out_48}), .clk(clock_1_out), .we(in_25), .clr(in_24));
  not not_13 (not_13_out, P0_6);
  not not_14 (not_14_out, P0_7);
  assign out_52 = not_13_out ? controlled_buffer_9_out[0] : 1'bz;  // Controlled_Buffer controlled_buffer_1
  assign out_53 = not_13_out ? controlled_buffer_9_out[1] : 1'bz;  // Controlled_Buffer controlled_buffer_2
  assign out_54 = not_13_out ? controlled_buffer_9_out[2] : 1'bz;  // Controlled_Buffer controlled_buffer_3
  assign out_55 = not_13_out ? controlled_buffer_9_out[3] : 1'bz;  // Controlled_Buffer controlled_buffer_4
  assign out_56 = not_13_out ? controlled_buffer_9_out[4] : 1'bz;  // Controlled_Buffer controlled_buffer_5
  assign out_57 = not_13_out ? controlled_buffer_9_out[5] : 1'bz;  // Controlled_Buffer controlled_buffer_6
  assign out_58 = not_13_out ? controlled_buffer_9_out[6] : 1'bz;  // Controlled_Buffer controlled_buffer_7
  assign out_59 = not_13_out ? controlled_buffer_9_out[7] : 1'bz;  // Controlled_Buffer controlled_buffer_8
  assign controlled_buffer_9_out[0] = P0_6 ? in_27 : 1'bz;  // Controlled_Buffer controlled_buffer_9
  assign controlled_buffer_9_out[1] = P0_6 ? in_28 : 1'bz;  // Controlled_Buffer controlled_buffer_10
  assign controlled_buffer_9_out[2] = P0_6 ? in_29 : 1'bz;  // Controlled_Buffer controlled_buffer_11
  assign controlled_buffer_9_out[3] = P0_6 ? in_30 : 1'bz;  // Controlled_Buffer controlled_buffer_12
  assign controlled_buffer_9_out[4] = P0_6 ? in_31 : 1'bz;  // Controlled_Buffer controlled_buffer_13
  assign controlled_buffer_9_out[5] = P0_6 ? in_32 : 1'bz;  // Controlled_Buffer controlled_buffer_14
  assign controlled_buffer_9_out[6] = P0_6 ? in_33 : 1'bz;  // Controlled_Buffer controlled_buffer_15
  assign controlled_buffer_9_out[7] = P0_6 ? in_34 : 1'bz;  // Controlled_Buffer controlled_buffer_16
  assign out_60 = not_14_out ? controlled_buffer_25_out : 1'bz;  // Controlled_Buffer controlled_buffer_17
  assign out_61 = not_14_out ? controlled_buffer_26_out : 1'bz;  // Controlled_Buffer controlled_buffer_18
  assign out_62 = not_14_out ? controlled_buffer_27_out : 1'bz;  // Controlled_Buffer controlled_buffer_19
  assign out_63 = not_14_out ? controlled_buffer_28_out : 1'bz;  // Controlled_Buffer controlled_buffer_20
  assign out_64 = not_14_out ? controlled_buffer_29_out : 1'bz;  // Controlled_Buffer controlled_buffer_21
  assign out_65 = not_14_out ? controlled_buffer_30_out : 1'bz;  // Controlled_Buffer controlled_buffer_22
  assign out_66 = not_14_out ? controlled_buffer_31_out : 1'bz;  // Controlled_Buffer controlled_buffer_23
  assign out_67 = not_14_out ? controlled_buffer_32_out : 1'bz;  // Controlled_Buffer controlled_buffer_24
  ROM rom_1 ();  // open: addr, data, sel
  assign controlled_buffer_25_out = P0_7 ? in_36 : 1'bz;  // Controlled_Buffer controlled_buffer_25
  assign controlled_buffer_26_out = P0_7 ? in_37 : 1'bz;  // Controlled_Buffer controlled_buffer_26
  assign controlled_buffer_27_out = P0_7 ? in_38 : 1'bz;  // Controlled_Buffer controlled_buffer_27
  assign controlled_buffer_28_out = P0_7 ? in_39 : 1'bz;  // Controlled_Buffer controlled_buffer_28
  assign controlled_buffer_29_out = P0_7 ? in_40 : 1'bz;  // Controlled_Buffer controlled_buffer_29
  assign controlled_buffer_30_out = P0_7 ? in_41 : 1'bz;  // Controlled_Buffer controlled_buffer_30
  assign controlled_buffer_31_out = P0_7 ? in_42 : 1'bz;  // Controlled_Buffer controlled_buffer_31
  assign controlled_buffer_32_out = P0_7 ? in_43 : 1'bz;  // Controlled_Buffer controlled_buffer_32
  RAM #(.bus("separate")) ram_1 (
    .addr({in_9, in_7, in_6, in_5, in_4, in_3, in_2, in_1}), .din(controlled_buffer_9_out),
    .data(ram_1_data), .str(not_15_out), .sel(in_18), .clk(in_21));  // open: ld, clr
  not not_15 (not_15_out, not_13_out);
  assign controlled_buffer_9_out[0] = not_13_out ? ram_1_data[0] : 1'bz;  // Controlled_Buffer controlled_buffer_33
  assign controlled_buffer_9_out[1] = not_13_out ? ram_1_data[1] : 1'bz;  // Controlled_Buffer controlled_buffer_34
  assign controlled_buffer_9_out[2] = not_13_out ? ram_1_data[2] : 1'bz;  // Controlled_Buffer controlled_buffer_35
  assign controlled_buffer_9_out[3] = not_13_out ? ram_1_data[3] : 1'bz;  // Controlled_Buffer controlled_buffer_36
  assign controlled_buffer_9_out[4] = not_13_out ? ram_1_data[4] : 1'bz;  // Controlled_Buffer controlled_buffer_37
  assign controlled_buffer_9_out[5] = not_13_out ? ram_1_data[5] : 1'bz;  // Controlled_Buffer controlled_buffer_38
  assign controlled_buffer_9_out[6] = not_13_out ? ram_1_data[6] : 1'bz;  // Controlled_Buffer controlled_buffer_39
  assign controlled_buffer_9_out[7] = not_13_out ? ram_1_data[7] : 1'bz;  // Controlled_Buffer controlled_buffer_40
  switcher switcher_1 (
    .out_10(controlled_buffer_25_out), .out_11(controlled_buffer_26_out), .out_12(controlled_buffer_27_out),
    .out_13(controlled_buffer_28_out), .out_14(controlled_buffer_29_out), .out_15(controlled_buffer_30_out),
    .out_16(controlled_buffer_31_out), .out_17(controlled_buffer_32_out), .in_1(not_14_out), .in_2(undriven),
    .in_3(undriven_2), .in_4(undriven_3), .in_5(undriven_4), .in_6(undriven_5), .in_7(undriven_6),
    .in_8(undriven_7), .in_9(undriven_8));

  // Notes on the sheet:
  //   contents of rom_1 (hex, n*v repeats v):
  //   1 2 3 4 8 9 11
  //   P2 PORT
  //   P3 PORT
endmodule

module binary_counter (
  input  in_1,
  input  in_2,
  input  in_3,
  output out_4,
  output out_5,
  output out_6,
  output out_7,
  output out_8
);

  wire and_1_out, and_2_out, and_3_out, clock_1_out, nand_1_out, or_1_out;

  Clock clock_1 (.out(clock_1_out));
  nand nand_1 (nand_1_out, in_2, out_4);
  T_Flip_Flop t_ff_1 (.clk(clock_1_out), .T(nand_1_out), .Q(out_8), .reset(in_3), .en(nand_1_out));  // open: Qn, preset
  and and_1 (and_1_out, out_8, out_7);
  T_Flip_Flop t_ff_2 (.clk(clock_1_out), .T(out_8), .Q(out_7), .reset(in_3), .en(nand_1_out));  // open: Qn, preset
  T_Flip_Flop t_ff_3 (.clk(clock_1_out), .T(and_1_out), .Q(out_6), .reset(in_3), .en(nand_1_out));  // open: Qn, preset
  and and_2 (and_2_out, out_8, out_7, out_6);
  T_Flip_Flop t_ff_4 (.clk(clock_1_out), .T(and_2_out), .Q(out_5), .reset(in_3), .en(nand_1_out));  // open: Qn, preset
  and and_3 (and_3_out, out_8, out_7, out_6, out_5);
  or or_1 (or_1_out, in_1, and_3_out);
  T_Flip_Flop t_ff_5 (.clk(clock_1_out), .T(or_1_out), .Q(out_4), .reset(in_3), .en(nand_1_out));  // open: Qn, preset
endmodule

module instruction_decode (
  input  in_1,
  input  in_2,
  input  in_3,
  input  in_4,
  output out_5,
  output out_6,
  output out_7
);

  wire and_4_out, and_5_out, and_6_out, and_7_out, and_8_out, not_1_out, not_2_out, not_3_out, not_4_out,
       not_5_out, not_6_out, not_7_out, not_8_out, not_9_out, not_10_out, not_11_out, not_12_out, not_13_out,
       not_14_out, not_15_out, not_16_out, not_17_out, not_18_out, not_19_out, not_20_out;

  not not_1 (not_1_out, in_1);
  not not_2 (not_2_out, in_2);
  not not_3 (not_3_out, in_3);
  not not_4 (not_4_out, in_4);
  not not_5 (not_5_out, in_1);
  not not_6 (not_6_out, in_2);
  not not_7 (not_7_out, in_3);
  not not_8 (not_8_out, in_1);
  not not_9 (not_9_out, in_2);
  not not_10 (not_10_out, in_4);
  not not_11 (not_11_out, in_1);
  not not_12 (not_12_out, in_2);
  not not_13 (not_13_out, in_1);
  not not_14 (not_14_out, in_3);
  not not_15 (not_15_out, in_4);
  not not_16 (not_16_out, in_1);
  not not_17 (not_17_out, in_3);
  not not_18 (not_18_out, in_1);
  not not_19 (not_19_out, in_4);
  not not_20 (not_20_out, in_1);
  and and_1 (out_5, not_1_out, not_2_out, not_3_out, not_4_out);
  and and_2 (out_6, not_5_out, not_6_out, not_7_out, in_4);
  and and_3 (out_7, not_8_out, not_9_out, in_3, not_10_out);
  LED led_1 (.in(and_4_out));
  and and_4 (and_4_out, not_11_out, not_12_out, in_3, in_4);
  LED led_2 (.in(and_5_out));
  and and_5 (and_5_out, not_13_out, in_2, not_14_out, not_15_out);
  and and_6 (and_6_out, not_16_out, in_2, not_17_out, in_4);
  LED led_3 (.in(and_6_out));
  and and_7 (and_7_out, not_18_out, in_2, in_3, not_19_out);
  LED led_4 (.in(and_7_out));
  LED led_5 (.in(and_8_out));
  and and_8 (and_8_out, not_20_out, in_2, in_3, in_4);
endmodule

module switcher (
  input  in_1,
  input  in_2,
  input  in_3,
  input  in_4,
  input  in_5,
  input  in_6,
  input  in_7,
  input  in_8,
  input  in_9,
  output out_10,
  output out_11,
  output out_12,
  output out_13,
  output out_14,
  output out_15,
  output out_16,
  output out_17
);

  assign out_10 = in_1 ? in_2 : 1'bz;  // Controlled_Buffer controlled_buffer_1
  assign out_11 = in_1 ? in_3 : 1'bz;  // Controlled_Buffer controlled_buffer_2
  assign out_12 = in_1 ? in_4 : 1'bz;  // Controlled_Buffer controlled_buffer_3
  assign out_13 = in_1 ? in_5 : 1'bz;  // Controlled_Buffer controlled_buffer_4
  assign out_14 = in_1 ? in_6 : 1'bz;  // Controlled_Buffer controlled_buffer_5
  assign out_15 = in_1 ? in_7 : 1'bz;  // Controlled_Buffer controlled_buffer_6
  assign out_16 = in_1 ? in_8 : 1'bz;  // Controlled_Buffer controlled_buffer_7
  assign out_17 = in_1 ? in_9 : 1'bz;  // Controlled_Buffer controlled_buffer_8
endmodule
