// Logisim project Full-Adder_Subtractor.circ as structural Verilog: 1 circuit, main circuit full_adder_12
module full_adder_12 (
  input  ci,
  input  a11,
  input  a10,
  input  a9,
  input  a8,
  input  a7,
  input  a6,
  input  a5,
  input  a4,
  input  a3,
  input  a2,
  input  a1,
  input  a0,
  input  b11,
  input  b10,
  input  b9,
  input  b8,
  input  b7,
  input  b6,
  input  b5,
  input  b4,
  input  b3,
  input  b2,
  input  b1,
  input  b0,
  output out_26,
  output out_27,
  output out_28,
  output out_29,
  output out_30,
  output out_31,
  output out_32,
  output out_33,
  output out_34,
  output out_35,
  output out_36,
  output out_37,
  output out_38,
  output out_39
);

  wire and_1_out, and_2_out, and_3_out, and_4_out, and_5_out, and_6_out, and_7_out, and_8_out, and_9_out,
       and_10_out, and_11_out, and_12_out, and_13_out, and_14_out, and_15_out, and_16_out, and_17_out,
       and_18_out, and_19_out, and_20_out, and_21_out, and_22_out, and_23_out, and_24_out, or_1_out,
       or_2_out, or_3_out, or_4_out, or_5_out, or_6_out, or_7_out, or_9_out, or_10_out, or_11_out, xor_1_out,
       xor_2_out, xor_3_out, xor_4_out, xor_5_out, xor_6_out, xor_9_out, xor_10_out, xor_13_out, xor_14_out,
       xor_15_out, xor_16_out, xor_17_out, xor_18_out, xor_21_out, xor_22_out, xor_25_out, xor_26_out,
       xor_27_out, xor_28_out, xor_29_out, xor_30_out, xor_33_out, xor_34_out;

  xor xor_1 (xor_1_out, a0, xor_2_out);
  xor xor_2 (xor_2_out, b0, ci);
  xor xor_3 (xor_3_out, a1, xor_4_out);
  xor xor_4 (xor_4_out, ci, b1);
  xor xor_5 (xor_5_out, ci, b2);
  xor xor_6 (xor_6_out, ci, b3);
  xor xor_7 (out_37, ci, xor_1_out);
  and and_1 (and_1_out, a0, xor_2_out);
  xor xor_8 (out_36, or_1_out, xor_3_out);
  and and_2 (and_2_out, a1, xor_4_out);
  xor xor_9 (xor_9_out, a2, xor_5_out);
  and and_3 (and_3_out, a2, xor_5_out);
  xor xor_10 (xor_10_out, a3, xor_6_out);
  and and_4 (and_4_out, a3, xor_6_out);
  and and_5 (and_5_out, ci, xor_1_out);
  or or_1 (or_1_out, and_5_out, and_1_out);
  and and_6 (and_6_out, or_1_out, xor_3_out);
  or or_2 (or_2_out, and_6_out, and_2_out);
  xor xor_11 (out_35, or_2_out, xor_9_out);
  and and_7 (and_7_out, or_2_out, xor_9_out);
  or or_3 (or_3_out, and_7_out, and_3_out);
  xor xor_12 (out_34, or_3_out, xor_10_out);
  and and_8 (and_8_out, or_3_out, xor_10_out);
  or or_4 (or_4_out, and_8_out, and_4_out);
  xor xor_13 (xor_13_out, a4, xor_14_out);
  xor xor_14 (xor_14_out, b4, ci);
  xor xor_15 (xor_15_out, a5, xor_16_out);
  xor xor_16 (xor_16_out, ci, b5);
  xor xor_17 (xor_17_out, ci, b6);
  xor xor_18 (xor_18_out, ci, b7);
  xor xor_19 (out_33, or_4_out, xor_13_out);
  and and_9 (and_9_out, a4, xor_14_out);
  xor xor_20 (out_32, or_5_out, xor_15_out);
  and and_10 (and_10_out, a5, xor_16_out);
  xor xor_21 (xor_21_out, a6, xor_17_out);
  and and_11 (and_11_out, a6, xor_17_out);
  xor xor_22 (xor_22_out, a7, xor_18_out);
  and and_12 (and_12_out, a7, xor_18_out);
  and and_13 (and_13_out, or_4_out, xor_13_out);
  or or_5 (or_5_out, and_13_out, and_9_out);
  and and_14 (and_14_out, or_5_out, xor_15_out);
  or or_6 (or_6_out, and_14_out, and_10_out);
  xor xor_23 (out_31, or_6_out, xor_21_out);
  and and_15 (and_15_out, or_6_out, xor_21_out);
  or or_7 (or_7_out, and_15_out, and_11_out);
  xor xor_24 (out_30, or_7_out, xor_22_out);
  and and_16 (and_16_out, or_7_out, xor_22_out);
  or or_8 (out_38, and_16_out, and_12_out);
  xor xor_25 (xor_25_out, a8, xor_26_out);
  xor xor_26 (xor_26_out, b8, ci);
  xor xor_27 (xor_27_out, a9, xor_28_out);
  xor xor_28 (xor_28_out, ci, b9);
  xor xor_29 (xor_29_out, ci, b10);
  xor xor_30 (xor_30_out, ci, b11);
  xor xor_31 (out_29, out_38, xor_25_out);
  and and_17 (and_17_out, a8, xor_26_out);
  xor xor_32 (out_28, or_9_out, xor_27_out);
  and and_18 (and_18_out, a9, xor_28_out);
  xor xor_33 (xor_33_out, a10, xor_29_out);
  and and_19 (and_19_out, a10, xor_29_out);
  xor xor_34 (xor_34_out, a11, xor_30_out);
  and and_20 (and_20_out, a11, xor_30_out);
  and and_21 (and_21_out, out_38, xor_25_out);
  or or_9 (or_9_out, and_21_out, and_17_out);
  and and_22 (and_22_out, or_9_out, xor_27_out);
  or or_10 (or_10_out, and_22_out, and_18_out);
  xor xor_35 (out_27, or_10_out, xor_33_out);
  and and_23 (and_23_out, or_10_out, xor_33_out);
  or or_11 (or_11_out, and_23_out, and_19_out);
  xor xor_36 (out_26, or_11_out, xor_34_out);
  and and_24 (and_24_out, or_11_out, xor_34_out);
  or or_12 (out_39, and_24_out, and_20_out);

  // Notes on the sheet:
  //   x0
  //   x0
  //   x0
  //   x0
  //   c0
  //   c0
  //   c0
  //   c0
  //   s0
  //   s0
  //   s0
  //   s0
  //   x0
  //   x0
  //   x0
  //   x0
  //   c0
  //   c0
  //   c0
  //   c0
  //   s0
  //   s0
  //   s0
  //   s0
  //   x0
  //   x0
  //   x0
  //   x0
  //   c0
  //   c0
  //   c0
  //   c0
  //   s0
  //   s0
  //   s0
  //   s0
endmodule
