// Logisim project wr80v3.0-test.circ as structural Verilog: 16 circuits, main circuit main
// WR80
module main (
  input  ON,
  input  RESET,
  input  CLK_IN,
  input  CLK_EN,
  input  OVERFLOW_EN,
  input  [7:0] P2_IN,
  input  [7:0] P3_IN,
  output out_8,
  output out_9,
  output out_10,
  output out_11,
  output out_12,
  output out_13,
  output out_14,
  output out_15,
  output out_16,
  output out_17,
  output [7:0] P2_OUT,
  output out_19,
  output out_20,
  output out_21,
  output MEM_EN,
  output P6S,
  output P7S,
  output CLK_OUT,
  output [7:0] P3_OUT
);

  wire ADD_out, alternador_5_out_10, alternador_5_out_11, alternador_5_out_12, alternador_5_out_13,
       alternador_5_out_14, alternador_5_out_15, alternador_5_out_16, alternador_5_out_17,
       alternador_12_4_out_14, alternador_12_4_out_15, alternador_12_4_out_16, alternador_12_4_out_17,
       and_1_out, and_2_out, and_3_out, and_4_out, and_5_out, and_6_out, and_7_out, and_8_out, and_9_out,
       and_10_out, and_11_out, and_12_out, and_13_out, and_14_out, and_15_out, and_16_out, and_17_out,
       and_18_out, and_19_out, and_20_out, and_21_out, and_22_out, and_23_out, and_24_out, and_25_out,
       and_27_out, and_28_out, and_29_out, and_30_out, and_31_out, and_32_out, and_33_out, and_34_out,
       and_35_out, AND_36_out, and_37_out, and_40_out, and_41_out, and_42_out, and_43_out, and_44_out,
       and_45_out, and_46_out, and_47_out, and_48_out, and_49_out, and_50_out, and_51_out, and_52_out,
       and_53_out, and_54_out, and_55_out, and_56_out, and_57_out, and_58_out, and_59_out, and_60_out,
       and_61_out, and_62_out, and_63_out, and_64_out, and_65_out, and_66_out, and_67_out, and_68_out,
       and_69_out, and_70_out, and_71_out, and_72_out, and_73_out, and_74_out, and_75_out, and_76_out,
       and_77_out, and_78_out, and_79_out, and_80_out, and_81_out, clock_1_out, d_ff_4_q, d_ff_7_q,
       d_ff_11_q, d_ff_13_q, d_ff_14_q, d_ff_16_q, d_ff_17_q, d_ff_18_q, d_ff_19_q, d_ff_20_q, d_ff_21_q,
       d_ff_22_q, d_ff_23_q, d_ff_24_q, d_ff_25_q, d_ff_59_q, d_ff_60_q, d_ff_61_q, detector_borda_1_out_3,
       detector_borda_2_out_3, detector_borda_3_out_3, detector_borda_4_out_3, IN_P0_out, IN_P1_out,
       IN_P2_out, IN_P3_out, JC_out, JP_out, JZ_out, LD_out, mixador_1_out_5, mixador_1_out_6,
       mixador_1_out_7, mixador_1_out_8, mixador_1_out_9, mixador_1_out_10, mixador_1_out_11,
       mixador_1_out_12, mixador_1_out_13, mixador_1_out_14, mixador_1_out_15, mixador_1_out_16,
       mixador_2_out_5, mixador_2_out_6, mixador_2_out_7, mixador_2_out_8, mixador_2_out_9, mixador_2_out_10,
       mixador_2_out_11, mixador_2_out_12, mixador_2_out_13, mixador_2_out_14, mixador_2_out_15,
       mixador_2_out_16, multiplexer_1_out, multiplexer_2_out, multiplexer_3_out, multiplexer_4_out,
       multiplexer_5_out, multiplexer_6_out, multiplexer_7_out, multiplexer_8_out, multiplexer_9_out,
       multiplexer_10_out, multiplexer_11_out, multiplexer_12_out, multiplexer_13_out, multiplexer_14_out,
       multiplexer_15_out, multiplexer_16_out, multiplexer_17_out, multiplexer_18_out, multiplexer_19_out,
       multiplexer_20_out, multiplexer_21_out, multiplexer_22_out, multiplexer_23_out, multiplexer_24_out,
       nand_1_out, nor_1_out, nor_2_out, nor_3_out, nor_4_out, nor_5_out, nor_6_out, not_1_out, not_2_out,
       not_3_out, not_4_out, not_5_out, not_6_out, not_7_out, not_8_out, not_9_out, not_10_out, not_11_out,
       not_12_out, not_13_out, not_14_out, not_15_out, not_16_out, not_17_out, not_18_out, not_19_out,
       not_20_out, not_21_out, not_22_out, not_23_out, not_24_out, not_25_out, not_26_out, not_27_out,
       not_28_out, not_29_out, not_30_out, not_31_out, not_32_out, not_33_out, not_34_out, not_35_out,
       not_36_out, not_37_out, not_38_out, not_39_out, not_40_out, not_41_out, not_42_out, NOT_43_out,
       not_44_out, not_45_out, not_46_out, not_47_out, not_48_out, not_49_out, not_50_out, not_51_out,
       not_52_out, not_53_out, not_54_out, not_55_out, or_1_out, or_2_out, or_3_out, or_4_out, or_5_out,
       or_6_out, or_7_out, or_8_out, or_9_out, or_11_out, OR_12_out, or_13_out, or_15_out, or_16_out,
       or_17_out, or_18_out, or_19_out, or_20_out, or_21_out, or_22_out, or_23_out, or_24_out, or_25_out,
       or_26_out, or_27_out, or_28_out, or_29_out, or_30_out, or_31_out, or_32_out, or_33_out, or_34_out,
       or_35_out, or_36_out, or_37_out, or_38_out, or_39_out, or_40_out, or_41_out, or_42_out, or_43_out,
       or_44_out, or_45_out, or_46_out, or_buffer_1_out_6, or_buffer_2_out_6, OUT_P0_out, OUT_P1_out,
       OUT_P2_out, OUT_P3_out, parallel_selector_1_out_4, parallel_selector_1_out_5,
       parallel_selector_1_out_6, parallel_selector_1_out_7, parallel_selector_1_out_8,
       parallel_selector_1_out_9, parallel_selector_1_out_10, parallel_selector_1_out_11,
       parallel_selector_1_out_12, parallel_selector_1_out_13, parallel_selector_1_out_14,
       parallel_selector_1_out_15, parallel_selector_1_out_16, parallel_selector_1_out_17,
       parallel_selector_1_out_18, parallel_selector_1_out_19, pc_input_1_out_4, pc_input_1_out_5,
       pc_input_2_out_4, pc_input_2_out_5, pc_input_3_out_4, pc_input_3_out_5, pc_input_4_out_4,
       pc_input_4_out_5, pc_input_5_out_4, pc_input_5_out_5, pc_input_6_out_4, pc_input_6_out_5,
       pc_input_7_out_4, pc_input_7_out_5, pc_input_8_out_4, pc_input_8_out_5, pc_input_9_out_4,
       pc_input_9_out_5, pc_input_10_out_4, pc_input_10_out_5, pc_input_11_out_4, pc_input_11_out_5,
       pc_input_12_out_4, pc_input_12_out_5, ST_out, SUB_out, t_ff_1_q, t_ff_1_qn, t_ff_2_q, t_ff_3_qn,
       t_ff_4_qn, t_ff_5_q, t_ff_6_qn, t_ff_7_qn, t_ff_8_qn, t_ff_9_qn, t_ff_10_qn, t_ff_11_qn, t_ff_12_qn,
       t_ff_13_qn, t_ff_14_qn, t_ff_15_qn, t_ff_16_q, xor_2_out, xor_3_out, xor_4_out, xor_5_out, xor_6_out,
       xor_7_out, xor_8_out, xor_9_out, xor_10_out, xor_11_out, xor_12_out, xor_13_out, xor_14_out,
       xor_15_out, xor_16_out, xor_17_out, xor_18_out, xor_19_out, xor_20_out, xor_21_out, xor_22_out,
       xor_23_out, xor_24_out, xor_25_out, xor_26_out, xor_27_out, xor_28_out, xor_29_out, xor_30_out,
       xor_31_out, xor_32_out, xor_33_out, xor_34_out, xor_35_out, xor_36_out, xor_37_out, xor_38_out,
       xor_39_out, xor_40_out, xor_41_out, xor_42_out, xor_43_out, xor_44_out, xor_45_out, XOR_out;
  wire [1:0] demultiplexer_1_out1, demultiplexer_2_out1, demultiplexer_3_out1;
  wire [5:0] IN_out;
  wire [7:0] alternador_12_1_out_14, buffer_register_1_out_18, d_ff_15_q, decoding_register_1_inst_dec,
       habilitador8_1_out_10, habilitador8_2_out_10, habilitador8_3_out_10, habilitador8_4_out_10,
       habilitador8_5_out_10, habilitador8_6_out_10, habilitador8_7_out_10, habilitador8_8_out_10,
       habilitador8_9_out_10, habilitador8_10_out_10, habilitador8_11_out_10, habilitador8_12_out_10,
       habilitador8_13_out_10, habilitador8_14_out_10, habilitador8_15_out_10, habilitador8_16_out_10,
       habilitador8_17_out_10, habilitador8_18_out_10, habilitador8_19_out_10, registro_portas_1_out_18,
       registro_portas_1_out_19, registro_portas_1_out_27, registro_usuario_1_out_23;
  wire [11:0] d_ff_48_q, d_ff_63_q, habilitador12_1_out_14, habilitador12_2_out_14, t_ff_3_q;
  wire [18:0] decoding_register_1_inst_exec;

  D_Flip_Flop d_ff_1 (.clk(and_18_out), .D(d_ff_63_q[7]), .Q(d_ff_15_q[7]), .reset(RESET));  // open: Qn, preset, en
  registro_usuario registro_usuario_1 (
    .in_1(or_17_out), .in_2(and_23_out), .in_3(d_ff_63_q[7]), .in_4(d_ff_63_q[6]), .in_5(d_ff_63_q[5]),
    .in_6(d_ff_63_q[4]), .in_7(d_ff_63_q[3]), .in_8(d_ff_63_q[2]), .in_9(d_ff_63_q[1]), .in_10(d_ff_63_q[0]),
    .in_11(RESET), .in_12(d_ff_18_q), .in_13(d_ff_19_q), .in_14(d_ff_20_q), .in_15(d_ff_21_q),
    .out_16(registro_usuario_1_out_23[7]), .out_17(registro_usuario_1_out_23[6]),
    .out_18(registro_usuario_1_out_23[5]), .out_19(registro_usuario_1_out_23[4]),
    .out_20(registro_usuario_1_out_23[3]), .out_21(registro_usuario_1_out_23[2]),
    .out_22(registro_usuario_1_out_23[1]), .out_23(registro_usuario_1_out_23[0]));
  and OUT_P3 (OUT_P3_out, or_18_out, d_ff_21_q, decoding_register_1_inst_exec[9]);
  and OUT_P2 (OUT_P2_out, or_18_out, d_ff_20_q, decoding_register_1_inst_exec[9]);
  and IN_P3 (IN_P3_out, decoding_register_1_inst_exec[8], d_ff_21_q, or_17_out);
  and IN_P2 (IN_P2_out, decoding_register_1_inst_exec[8], d_ff_20_q, or_17_out);
  and IN_P0 (IN_P0_out, decoding_register_1_inst_exec[8], d_ff_18_q, or_17_out);
  and OUT_P0 (OUT_P0_out, or_18_out, d_ff_18_q, decoding_register_1_inst_exec[9]);
  D_Flip_Flop d_ff_2 (.clk(and_18_out), .D(d_ff_63_q[6]), .Q(d_ff_15_q[6]), .reset(RESET));  // open: Qn, preset, en
  not not_1 (not_1_out, CLK_OUT);
  and and_1 (and_1_out, or_18_out, decoding_register_1_inst_exec[9]);
  or or_1 (or_1_out, OUT_P2_out, OUT_P3_out, or_2_out, OUT_P1_out, OUT_P0_out);
  or or_2 (or_2_out, IN_P3_out, IN_P2_out);
  and IN_P1 (IN_P1_out, decoding_register_1_inst_exec[8], d_ff_19_q, or_17_out);
  and OUT_P1 (OUT_P1_out, or_18_out, d_ff_19_q, decoding_register_1_inst_exec[9]);
  D_Flip_Flop d_ff_3 (.clk(and_18_out), .D(d_ff_63_q[5]), .Q(d_ff_15_q[5]), .reset(RESET));  // open: Qn, preset, en
  and and_2 (and_2_out, or_17_out, not_1_out);
  or or_3 (or_3_out, or_2_out, OUT_P3_out, OUT_P2_out, IN_P0_out, IN_P1_out);
  or or_4 (or_4_out, IN_P2_out, OUT_P2_out);
  buffer_register buffer_register_1 (
    .in_9(or_16_out), .in_10(detector_borda_3_out_3), .in_8(d_ff_24_q), .in_7(d_ff_23_q), .in_6(d_ff_22_q),
    .in_5(d_ff_16_q), .in_4(d_ff_14_q), .in_3(d_ff_11_q), .in_2(d_ff_7_q), .in_1(d_ff_4_q),
    .out_18(buffer_register_1_out_18[0]), .out_17(buffer_register_1_out_18[1]),
    .out_16(buffer_register_1_out_18[2]), .out_15(buffer_register_1_out_18[3]),
    .out_14(buffer_register_1_out_18[4]), .out_13(buffer_register_1_out_18[5]),
    .out_12(buffer_register_1_out_18[6]), .out_11(buffer_register_1_out_18[7]));
  D_Flip_Flop d_ff_4 (
    .clk(detector_borda_3_out_3), .D(P2_IN[7]), .Q(d_ff_4_q), .en(or_15_out), .reset(RESET));  // open: Qn, preset
  D_Flip_Flop d_ff_5 (.clk(and_18_out), .D(d_ff_63_q[4]), .Q(d_ff_15_q[4]), .reset(RESET));  // open: Qn, preset, en
  D_Flip_Flop #(.trigger("falling")) d_ff_6 (.clk(and_20_out), .reset(RESET));  // open: D, Q, Qn, preset, en
  and and_3 (and_3_out, and_2_out, decoding_register_1_inst_exec[8]);
  and and_4 (and_4_out, not_1_out, or_4_out);
  D_Flip_Flop d_ff_7 (
    .clk(detector_borda_3_out_3), .D(P2_IN[6]), .Q(d_ff_7_q), .en(or_15_out), .reset(RESET));  // open: Qn, preset
  D_Flip_Flop d_ff_8 (
    .clk(detector_borda_1_out_3), .D(d_ff_63_q[3]), .Q(d_ff_15_q[3]), .reset(RESET));  // open: Qn, preset, en
  D_Flip_Flop d_ff_9 (
    .clk(detector_borda_1_out_3), .D(d_ff_63_q[2]), .Q(d_ff_15_q[2]), .reset(RESET));  // open: Qn, preset, en
  D_Flip_Flop #(.trigger("falling")) d_ff_10 (
    .clk(and_20_out), .D(d_ff_60_q), .reset(RESET));  // open: Q, Qn, preset, en
  and and_5 (and_5_out, decoding_register_1_inst_exec[8], or_18_out);
  not not_2 (not_2_out, d_ff_24_q);
  not not_3 (not_3_out, d_ff_23_q);
  not not_4 (not_4_out, d_ff_23_q);
  not not_5 (not_5_out, d_ff_24_q);
  D_Flip_Flop d_ff_11 (
    .clk(detector_borda_3_out_3), .D(P2_IN[5]), .Q(d_ff_11_q), .en(or_15_out), .reset(RESET));  // open: Qn, preset
  D_Flip_Flop d_ff_12 (
    .clk(detector_borda_1_out_3), .D(d_ff_63_q[1]), .Q(d_ff_15_q[1]), .reset(RESET));  // open: Qn, preset, en
  D_Flip_Flop #(.trigger("falling")) d_ff_13 (
    .clk(and_21_out), .D(d_ff_61_q), .Q(d_ff_13_q), .reset(RESET));  // open: Qn, preset, en
  or or_5 (or_5_out, and_5_out, and_3_out, and_1_out);
  or or_6 (or_6_out, OUT_P3_out, OUT_P2_out, OUT_P0_out, OUT_P1_out);
  not not_6 (not_6_out, d_ff_7_q);
  not not_7 (not_7_out, d_ff_11_q);
  not not_8 (not_8_out, d_ff_14_q);
  not not_9 (not_9_out, d_ff_7_q);
  not not_10 (not_10_out, d_ff_11_q);
  not not_11 (not_11_out, d_ff_7_q);
  not not_12 (not_12_out, d_ff_14_q);
  not not_13 (not_13_out, d_ff_7_q);
  not not_14 (not_14_out, d_ff_11_q);
  not not_15 (not_15_out, d_ff_14_q);
  not not_16 (not_16_out, d_ff_11_q);
  not not_17 (not_17_out, d_ff_14_q);
  and and_6 (and_6_out, not_2_out, not_3_out, and_22_out);
  and and_7 (and_7_out, not_4_out, d_ff_24_q, and_22_out);
  and and_8 (and_8_out, not_5_out, d_ff_23_q, and_22_out);
  and and_9 (and_9_out, d_ff_24_q, d_ff_23_q, and_22_out);
  D_Flip_Flop d_ff_14 (
    .clk(detector_borda_3_out_3), .D(P2_IN[4]), .Q(d_ff_14_q), .en(or_15_out), .reset(RESET));  // open: Qn, preset
  D_Flip_Flop d_ff_15 (
    .clk(detector_borda_1_out_3), .D(d_ff_63_q[0]), .Q(d_ff_15_q[0]), .reset(RESET));  // open: Qn, preset, en
  alternador_12 alternador_12_1 (
    .in_1(or_6_out), .in_2(d_ff_63_q[0]), .in_3(d_ff_63_q[1]), .in_4(d_ff_63_q[2]), .in_5(d_ff_63_q[3]),
    .in_6(d_ff_63_q[4]), .in_7(d_ff_63_q[5]), .in_8(d_ff_63_q[6]), .in_9(d_ff_63_q[7]),
    .out_14(alternador_12_1_out_14[0]), .out_15(alternador_12_1_out_14[1]),
    .out_16(alternador_12_1_out_14[2]), .out_17(alternador_12_1_out_14[3]),
    .out_18(alternador_12_1_out_14[4]), .out_19(alternador_12_1_out_14[5]),
    .out_20(alternador_12_1_out_14[6]), .out_21(alternador_12_1_out_14[7]));  // open: in_10, in_11, in_12, in_13, out_22, out_23, out_24, out_25
  not not_18 (not_18_out, d_ff_4_q);
  not not_19 (not_19_out, d_ff_4_q);
  not not_20 (not_20_out, d_ff_4_q);
  not not_21 (not_21_out, d_ff_4_q);
  not not_22 (not_22_out, d_ff_4_q);
  not not_23 (not_23_out, d_ff_4_q);
  not not_24 (not_24_out, d_ff_4_q);
  not not_25 (not_25_out, d_ff_4_q);
  LED led_1 (.in(and_6_out));
  LED led_2 (.in(and_7_out));
  LED led_3 (.in(and_8_out));
  LED led_4 (.in(and_9_out));
  D_Flip_Flop d_ff_16 (
    .clk(detector_borda_3_out_3), .D(P2_IN[3]), .Q(d_ff_16_q), .en(or_15_out), .reset(RESET));  // open: Qn, preset
  detector_borda detector_borda_1 (.in_1(and_19_out), .in_2(detector_borda_3_out_3), .out_3(detector_borda_1_out_3));
  D_Flip_Flop #(.trigger("falling")) d_ff_17 (
    .clk(and_20_out), .D(d_ff_59_q), .Q(d_ff_17_q), .reset(RESET));  // open: Qn, preset, en
  and and_10 (and_10_out, not_18_out, not_6_out, not_7_out, not_8_out, and_24_out);
  and and_11 (and_11_out, not_19_out, not_9_out, not_10_out, d_ff_14_q, and_24_out);
  and and_12 (and_12_out, not_20_out, not_11_out, d_ff_11_q, not_12_out, and_24_out);
  and and_13 (and_13_out, not_21_out, not_13_out, d_ff_11_q, d_ff_14_q, and_24_out);
  and and_14 (and_14_out, not_22_out, d_ff_7_q, not_14_out, not_15_out, and_24_out);
  and and_15 (and_15_out, not_23_out, d_ff_7_q, not_16_out, d_ff_14_q, and_24_out);
  and and_16 (and_16_out, not_24_out, d_ff_7_q, d_ff_11_q, not_17_out, and_24_out);
  and and_17 (and_17_out, not_25_out, d_ff_7_q, d_ff_11_q, d_ff_14_q, and_24_out);
  D_Flip_Flop #(.trigger("falling")) d_ff_18 (
    .clk(detector_borda_2_out_3), .D(and_6_out), .Q(d_ff_18_q));  // open: Qn, preset, en, reset
  D_Flip_Flop #(.trigger("falling")) d_ff_19 (
    .clk(detector_borda_2_out_3), .D(and_7_out), .Q(d_ff_19_q));  // open: Qn, preset, en, reset
  D_Flip_Flop #(.trigger("falling")) d_ff_20 (
    .clk(detector_borda_2_out_3), .D(and_8_out), .Q(d_ff_20_q));  // open: Qn, preset, en, reset
  D_Flip_Flop #(.trigger("falling")) d_ff_21 (
    .clk(detector_borda_2_out_3), .D(and_9_out), .Q(d_ff_21_q));  // open: Qn, preset, en, reset
  D_Flip_Flop d_ff_22 (
    .clk(detector_borda_3_out_3), .D(P2_IN[2]), .Q(d_ff_22_q), .en(or_15_out), .reset(RESET));  // open: Qn, preset
  and and_18 (and_18_out, not_26_out, and_19_out);
  and and_19 (and_19_out, nor_1_out, or_18_out);
  and and_20 (and_20_out, nor_3_out, nor_2_out, or_18_out);
  and and_21 (and_21_out, or_18_out, nor_3_out);
  registro_portas registro_portas_1 (
    .out_18(registro_portas_1_out_18), .out_19(registro_portas_1_out_19), .in_1(OUT_P3_out),
    .in_2(OUT_P2_out), .in_4(RESET), .in_5(or_3_out), .in_6(or_1_out), .in_8(buffer_register_1_out_18[1]),
    .in_9(buffer_register_1_out_18[0]), .in_10(alternador_12_1_out_14[7]), .in_11(alternador_12_1_out_14[6]),
    .in_12(alternador_12_1_out_14[5]), .in_13(alternador_12_1_out_14[4]), .in_14(alternador_12_1_out_14[3]),
    .in_15(alternador_12_1_out_14[2]), .in_16(alternador_12_1_out_14[1]), .in_17(alternador_12_1_out_14[0]),
    .out_20(registro_portas_1_out_27[7]), .out_21(registro_portas_1_out_27[6]),
    .out_22(registro_portas_1_out_27[5]), .out_23(registro_portas_1_out_27[4]),
    .out_24(registro_portas_1_out_27[3]), .out_25(registro_portas_1_out_27[2]),
    .out_26(registro_portas_1_out_27[1]), .out_27(registro_portas_1_out_27[0]), .in_7(or_5_out),
    .in_3(and_4_out));
  detector_borda detector_borda_2 (.in_1(or_16_out), .in_2(detector_borda_3_out_3), .out_3(detector_borda_2_out_3));
  LED led_5 (.in(and_10_out));
  decoding_register decoding_register_1 (
    .dec_signal(detector_borda_2_out_3), .inst(and_10_out), .inst_dec(decoding_register_1_inst_dec[0]),
    .inst_exec(decoding_register_1_inst_exec[0]));
  LED led_6 (.in(and_11_out));
  decoding_register decoding_register_2 (
    .dec_signal(detector_borda_2_out_3), .inst(and_11_out), .inst_dec(decoding_register_1_inst_dec[1]),
    .inst_exec(decoding_register_1_inst_exec[1]));
  LED led_7 (.in(and_12_out));
  decoding_register decoding_register_3 (
    .dec_signal(detector_borda_2_out_3), .inst(and_12_out), .inst_dec(decoding_register_1_inst_dec[2]),
    .inst_exec(decoding_register_1_inst_exec[2]));
  LED led_8 (.in(and_13_out));
  decoding_register decoding_register_4 (
    .dec_signal(detector_borda_2_out_3), .inst(and_13_out), .inst_dec(decoding_register_1_inst_dec[3]),
    .inst_exec(decoding_register_1_inst_exec[3]));
  LED led_9 (.in(and_14_out));
  decoding_register decoding_register_5 (
    .dec_signal(detector_borda_2_out_3), .inst(and_14_out), .inst_dec(decoding_register_1_inst_dec[4]),
    .inst_exec(decoding_register_1_inst_exec[4]));
  LED led_10 (.in(and_15_out));
  decoding_register decoding_register_6 (
    .dec_signal(detector_borda_2_out_3), .inst(and_15_out), .inst_dec(decoding_register_1_inst_dec[5]),
    .inst_exec(decoding_register_1_inst_exec[5]));
  LED led_11 (.in(and_16_out));
  decoding_register decoding_register_7 (
    .dec_signal(detector_borda_2_out_3), .inst(and_16_out), .inst_dec(decoding_register_1_inst_dec[6]),
    .inst_exec(decoding_register_1_inst_exec[6]));
  LED led_12 (.in(and_17_out));
  decoding_register decoding_register_8 (
    .dec_signal(detector_borda_2_out_3), .inst(and_17_out), .inst_dec(decoding_register_1_inst_dec[7]),
    .inst_exec(decoding_register_1_inst_exec[7]));
  and and_22 (and_22_out, and_24_out, nor_4_out);
  D_Flip_Flop d_ff_23 (
    .clk(detector_borda_3_out_3), .D(P2_IN[1]), .Q(d_ff_23_q), .en(or_15_out), .reset(RESET));  // open: Qn, preset
  not not_26 (not_26_out, decoding_register_1_inst_exec[6]);
  nor nor_1 (nor_1_out, decoding_register_1_inst_exec[7], decoding_register_1_inst_exec[9], decoding_register_1_inst_exec[12], or_8_out);
  nor nor_2 (nor_2_out, decoding_register_1_inst_exec[0], decoding_register_1_inst_exec[1], decoding_register_1_inst_exec[2], decoding_register_1_inst_exec[3], decoding_register_1_inst_exec[8]);
  nor nor_3 (nor_3_out, decoding_register_1_inst_exec[7], decoding_register_1_inst_exec[9], or_8_out, decoding_register_1_inst_exec[8]);
  and and_23 (and_23_out, or_18_out, decoding_register_1_inst_exec[7]);
  and and_24 (and_24_out, or_16_out, not_40_out);
  D_Flip_Flop d_ff_24 (
    .clk(detector_borda_3_out_3), .D(P2_IN[0]), .Q(d_ff_24_q), .en(or_15_out), .reset(RESET));  // open: Qn, preset
  Clock clock_1 (.out(clock_1_out));
  and and_25 (and_25_out, CLK_IN, not_27_out);
  not not_27 (not_27_out, CLK_EN);
  and and_26 (CLK_OUT, CLK_EN, clock_1_out);
  not not_28 (not_28_out, d_ff_7_q);
  not not_29 (not_29_out, d_ff_11_q);
  not not_30 (not_30_out, d_ff_14_q);
  not not_31 (not_31_out, d_ff_7_q);
  not not_32 (not_32_out, d_ff_11_q);
  not not_33 (not_33_out, d_ff_7_q);
  not not_34 (not_34_out, d_ff_14_q);
  not not_35 (not_35_out, d_ff_7_q);
  not not_36 (not_36_out, d_ff_11_q);
  not not_37 (not_37_out, d_ff_14_q);
  not not_38 (not_38_out, d_ff_11_q);
  not not_39 (not_39_out, d_ff_14_q);
  nor nor_4 (nor_4_out, and_34_out, and_33_out, and_32_out);
  not not_40 (not_40_out, or_11_out);
  or or_7 (or_7_out, and_25_out, CLK_OUT);
  and and_27 (and_27_out, d_ff_4_q, not_28_out, not_29_out, not_30_out, and_24_out);
  and and_28 (and_28_out, d_ff_4_q, not_31_out, not_32_out, d_ff_14_q, and_24_out);
  and and_29 (and_29_out, d_ff_4_q, not_33_out, d_ff_11_q, not_34_out, and_24_out);
  and and_30 (and_30_out, d_ff_4_q, not_35_out, d_ff_11_q, d_ff_14_q, and_24_out);
  and and_31 (and_31_out, d_ff_4_q, d_ff_7_q, not_36_out, not_37_out, and_24_out);
  and and_32 (and_32_out, d_ff_4_q, d_ff_7_q, not_38_out, d_ff_14_q, and_24_out);
  and and_33 (and_33_out, d_ff_4_q, d_ff_7_q, d_ff_11_q, not_39_out, and_24_out);
  and and_34 (and_34_out, d_ff_4_q, d_ff_7_q, d_ff_11_q, d_ff_14_q, and_24_out);
  D_Flip_Flop d_ff_25 (.clk(ON), .D(1'b1), .Q(d_ff_25_q));  // open: Qn, preset, en, reset
  detector_borda detector_borda_3 (.in_1(CLK_EN), .in_2(or_7_out), .out_3(detector_borda_3_out_3));
  or or_8 (or_8_out, decoding_register_1_inst_exec[13], decoding_register_1_inst_exec[14], decoding_register_1_inst_exec[15], decoding_register_1_inst_exec[16], decoding_register_1_inst_exec[17], decoding_register_1_inst_exec[18]);
  not not_41 (not_41_out, or_9_out);
  or or_9 (or_9_out, decoding_register_1_inst_exec[9], decoding_register_1_inst_exec[8]);
  LED led_13 (.in(and_27_out));
  LED led_14 (.in(and_28_out));
  LED led_15 (.in(and_29_out));
  LED led_16 (.in(and_30_out));
  LED led_17 (.in(and_31_out));
  and and_35 (and_35_out, d_ff_25_q, nand_1_out);
  nand nand_1 (nand_1_out, OVERFLOW_EN, d_ff_25_q, t_ff_16_q);
  alternador_12 alternador_12_2 (
    .in_1(not_41_out), .in_2(t_ff_3_q[0]), .in_3(t_ff_3_q[1]), .in_4(t_ff_3_q[2]), .in_5(t_ff_3_q[3]),
    .in_6(t_ff_3_q[4]), .in_7(t_ff_3_q[5]), .in_8(t_ff_3_q[6]), .in_9(t_ff_3_q[7]), .in_10(t_ff_3_q[8]),
    .in_11(t_ff_3_q[9]), .in_12(t_ff_3_q[10]), .in_13(t_ff_3_q[11]), .out_14(out_8), .out_15(out_9),
    .out_16(out_10), .out_17(out_11), .out_18(out_12), .out_19(out_13), .out_20(out_14), .out_21(out_15),
    .out_22(out_16), .out_23(out_17), .out_24(out_19), .out_25(out_20));
  alternador_12 alternador_12_3 (
    .in_1(or_9_out), .in_2(registro_portas_1_out_19[0]), .in_3(registro_portas_1_out_19[1]),
    .in_4(registro_portas_1_out_19[2]), .in_5(registro_portas_1_out_19[3]),
    .in_6(registro_portas_1_out_19[4]), .in_7(registro_portas_1_out_19[5]),
    .in_8(registro_portas_1_out_19[6]), .in_9(registro_portas_1_out_19[7]),
    .in_10(registro_portas_1_out_18[0]), .in_11(registro_portas_1_out_18[1]),
    .in_12(registro_portas_1_out_18[2]), .in_13(registro_portas_1_out_18[3]), .out_14(out_8), .out_15(out_9),
    .out_16(out_10), .out_17(out_11), .out_18(out_12), .out_19(out_13), .out_20(out_14), .out_21(out_15),
    .out_22(out_16), .out_23(out_17), .out_24(out_19), .out_25(out_20));
  not not_42 (not_42_out, or_9_out);
  D_Flip_Flop #(.trigger("falling")) d_ff_26 (
    .clk(and_24_out), .D(and_27_out), .Q(decoding_register_1_inst_exec[8]), .reset(or_15_out));  // open: Qn, preset, en
  D_Flip_Flop #(.trigger("falling")) d_ff_27 (
    .clk(and_24_out), .D(and_28_out), .Q(decoding_register_1_inst_exec[9]), .reset(or_15_out));  // open: Qn, preset, en
  D_Flip_Flop #(.trigger("falling")) d_ff_28 (
    .clk(and_24_out), .D(and_29_out), .Q(decoding_register_1_inst_exec[10]), .reset(or_15_out));  // open: Qn, preset, en
  D_Flip_Flop #(.trigger("falling")) d_ff_29 (
    .clk(and_24_out), .D(and_30_out), .Q(decoding_register_1_inst_exec[11]), .reset(or_15_out));  // open: Qn, preset, en
  D_Flip_Flop #(.trigger("falling")) d_ff_30 (
    .clk(and_24_out), .D(and_31_out), .Q(decoding_register_1_inst_exec[12]), .reset(or_15_out));  // open: Qn, preset, en
  D_Flip_Flop #(.trigger("falling")) d_ff_31 (
    .clk(or_16_out), .D(and_32_out), .Q(decoding_register_1_inst_exec[13]));  // open: Qn, preset, en, reset
  D_Flip_Flop #(.trigger("falling")) d_ff_32 (
    .clk(or_16_out), .D(and_33_out), .Q(decoding_register_1_inst_exec[14]));  // open: Qn, preset, en, reset
  D_Flip_Flop #(.trigger("falling")) d_ff_33 (
    .clk(or_16_out), .D(and_34_out), .Q(decoding_register_1_inst_exec[15]));  // open: Qn, preset, en, reset
  T_Flip_Flop t_ff_1 (
    .clk(detector_borda_3_out_3), .T(and_35_out), .Q(t_ff_1_q), .Qn(t_ff_1_qn), .reset(RESET), .en(and_35_out));  // open: preset
  assign out_21 = not_42_out ? 1'b0 : 1'bz;  // Controlled_Buffer controlled_buffer_1
  assign out_21 = or_9_out ? registro_portas_1_out_18[4] : 1'bz;  // Controlled_Buffer controlled_buffer_2
  T_Flip_Flop t_ff_2 (
    .clk(t_ff_1_qn), .T(and_35_out), .Q(t_ff_2_q), .reset(RESET), .en(and_35_out));  // open: Qn, preset
  or or_10 (MEM_EN, or_15_out, registro_portas_1_out_18[5]);
  D_Flip_Flop #(.trigger("falling")) d_ff_34 (
    .clk(or_16_out), .D(decoding_register_1_inst_exec[13]), .Q(decoding_register_1_inst_exec[16]),
    .reset(or_15_out));  // open: Qn, preset, en
  D_Flip_Flop #(.trigger("falling")) d_ff_35 (
    .clk(or_16_out), .D(decoding_register_1_inst_exec[14]), .Q(decoding_register_1_inst_exec[17]),
    .reset(or_15_out));  // open: Qn, preset, en
  D_Flip_Flop #(.trigger("falling")) d_ff_36 (
    .clk(or_16_out), .D(decoding_register_1_inst_exec[15]), .Q(decoding_register_1_inst_exec[18]),
    .reset(or_15_out));  // open: Qn, preset, en
  or or_11 (or_11_out, decoding_register_1_inst_exec[13], decoding_register_1_inst_exec[14], decoding_register_1_inst_exec[15]);
  T_Flip_Flop t_ff_3 (
    .clk(detector_borda_3_out_3), .T(and_35_out), .Q(t_ff_3_q[0]), .Qn(t_ff_3_qn), .preset(pc_input_1_out_4),
    .reset(pc_input_1_out_5), .en(and_35_out));
  pc_input pc_input_1 (
    .in_1(and_37_out), .in_2(d_ff_63_q[0]), .in_3(RESET), .out_4(pc_input_1_out_4), .out_5(pc_input_1_out_5));
  T_Flip_Flop t_ff_4 (
    .clk(t_ff_3_qn), .T(and_35_out), .Q(t_ff_3_q[1]), .Qn(t_ff_4_qn), .preset(pc_input_2_out_4),
    .reset(pc_input_2_out_5), .en(and_35_out));
  pc_input pc_input_2 (
    .in_1(and_37_out), .in_2(d_ff_63_q[1]), .in_3(RESET), .out_4(pc_input_2_out_4), .out_5(pc_input_2_out_5));
  T_Flip_Flop #(.trigger("falling")) t_ff_5 (
    .clk(CLK_OUT), .T(d_ff_25_q), .Q(t_ff_5_q), .preset(ON));  // open: Qn, reset, en
  nor nor_5 (nor_5_out, or_8_out, decoding_register_1_inst_exec[9], decoding_register_1_inst_exec[8]);
  and AND_36 (AND_36_out, decoding_register_1_inst_dec[0], or_17_out);
  and OR_12 (OR_12_out, decoding_register_1_inst_dec[1], or_17_out);
  and NOT_43 (NOT_43_out, decoding_register_1_inst_dec[2], or_17_out);
  and XOR (XOR_out, decoding_register_1_inst_dec[3], or_17_out);
  and ADD (ADD_out, decoding_register_1_inst_dec[4], or_17_out);
  and SUB (SUB_out, decoding_register_1_inst_dec[5], or_17_out);
  and ST (ST_out, decoding_register_1_inst_dec[6], or_17_out);
  and LD (LD_out, decoding_register_1_inst_dec[7], or_17_out);
  and IN (IN_out[0], decoding_register_1_inst_exec[8], or_17_out);
  and OUT (IN_out[1], decoding_register_1_inst_exec[9], or_17_out);
  and SHR (IN_out[2], decoding_register_1_inst_exec[10], or_17_out);
  and SHL (IN_out[3], decoding_register_1_inst_exec[11], or_17_out);
  and BT (IN_out[4], decoding_register_1_inst_exec[12], or_17_out);
  and JC (JC_out, decoding_register_1_inst_exec[16], or_17_out);
  and JZ (JZ_out, decoding_register_1_inst_exec[17], or_17_out);
  and JP (JP_out, decoding_register_1_inst_exec[18], or_17_out);
  or or_13 (or_13_out, decoding_register_1_inst_exec[16], decoding_register_1_inst_exec[17], decoding_register_1_inst_exec[18]);
  T_Flip_Flop t_ff_6 (
    .clk(t_ff_4_qn), .T(and_35_out), .Q(t_ff_3_q[2]), .Qn(t_ff_6_qn), .preset(pc_input_3_out_4),
    .reset(pc_input_3_out_5), .en(and_35_out));
  pc_input pc_input_3 (
    .in_1(and_37_out), .in_2(d_ff_63_q[2]), .in_3(RESET), .out_4(pc_input_3_out_4), .out_5(pc_input_3_out_5));
  and and_37 (and_37_out, t_ff_5_q, and_42_out);
  parallel_selector parallel_selector_1 (
    .in_1(t_ff_1_q), .in_2(t_ff_2_q), .in_3(nor_5_out), .out_4(parallel_selector_1_out_4),
    .out_5(parallel_selector_1_out_5), .out_6(parallel_selector_1_out_6), .out_7(parallel_selector_1_out_7),
    .out_8(parallel_selector_1_out_8), .out_9(parallel_selector_1_out_9),
    .out_10(parallel_selector_1_out_10), .out_11(parallel_selector_1_out_11),
    .out_12(parallel_selector_1_out_12), .out_13(parallel_selector_1_out_13),
    .out_14(parallel_selector_1_out_14), .out_15(parallel_selector_1_out_15),
    .out_16(parallel_selector_1_out_16), .out_17(parallel_selector_1_out_17),
    .out_18(parallel_selector_1_out_18), .out_19(parallel_selector_1_out_19));
  or or_14 (IN_out[5], JC_out, JZ_out, JP_out);
  T_Flip_Flop t_ff_7 (
    .clk(t_ff_6_qn), .T(and_35_out), .Q(t_ff_3_q[3]), .Qn(t_ff_7_qn), .preset(pc_input_4_out_4),
    .reset(pc_input_4_out_5), .en(and_35_out));
  pc_input pc_input_4 (
    .in_1(and_37_out), .in_2(d_ff_63_q[3]), .in_3(RESET), .out_4(pc_input_4_out_4), .out_5(pc_input_4_out_5));
  T_Flip_Flop t_ff_8 (
    .clk(t_ff_7_qn), .T(and_35_out), .Q(t_ff_3_q[4]), .Qn(t_ff_8_qn), .preset(pc_input_5_out_4),
    .reset(pc_input_5_out_5), .en(and_35_out));
  pc_input pc_input_5 (
    .in_1(and_37_out), .in_2(d_ff_63_q[4]), .in_3(RESET), .out_4(pc_input_5_out_4), .out_5(pc_input_5_out_5));
  not not_44 (not_44_out, registro_portas_1_out_18[6]);
  alternador alternador_1 (
    .in_1(and_40_out), .in_2(P2_IN[7]), .in_3(P2_IN[6]), .in_4(P2_IN[5]), .in_5(P2_IN[4]), .in_6(P2_IN[3]),
    .in_7(P2_IN[2]), .in_8(P2_IN[1]), .in_9(P2_IN[0]), .out_10(alternador_12_1_out_14[7]),
    .out_11(alternador_12_1_out_14[6]), .out_12(alternador_12_1_out_14[5]),
    .out_13(alternador_12_1_out_14[4]), .out_14(alternador_12_1_out_14[3]),
    .out_15(alternador_12_1_out_14[2]), .out_16(alternador_12_1_out_14[1]), .out_17(alternador_12_1_out_14[0]));
  and and_38 (P6S, d_ff_20_q, registro_portas_1_out_18[6], registro_portas_1_out_18[5]);
  not not_45 (not_45_out, registro_portas_1_out_18[7]);
  alternador alternador_2 (
    .in_1(and_41_out), .in_2(P3_IN[7]), .in_3(P3_IN[6]), .in_4(P3_IN[5]), .in_5(P3_IN[4]), .in_6(P3_IN[3]),
    .in_7(P3_IN[2]), .in_8(P3_IN[1]), .in_9(P3_IN[0]), .out_10(alternador_12_1_out_14[7]),
    .out_11(alternador_12_1_out_14[6]), .out_12(alternador_12_1_out_14[5]),
    .out_13(alternador_12_1_out_14[4]), .out_14(alternador_12_1_out_14[3]),
    .out_15(alternador_12_1_out_14[2]), .out_16(alternador_12_1_out_14[1]), .out_17(alternador_12_1_out_14[0]));
  and and_39 (P7S, d_ff_21_q, registro_portas_1_out_18[7]);
  T_Flip_Flop t_ff_9 (
    .clk(t_ff_8_qn), .T(and_35_out), .Q(t_ff_3_q[5]), .Qn(t_ff_9_qn), .preset(pc_input_6_out_4),
    .reset(pc_input_6_out_5), .en(and_35_out));
  pc_input pc_input_6 (
    .in_1(and_37_out), .in_2(d_ff_63_q[5]), .in_3(RESET), .out_4(pc_input_6_out_4), .out_5(pc_input_6_out_5));
  or or_15 (or_15_out, parallel_selector_1_out_4, parallel_selector_1_out_8, parallel_selector_1_out_12, parallel_selector_1_out_16);
  or or_16 (or_16_out, parallel_selector_1_out_5, parallel_selector_1_out_9, parallel_selector_1_out_13, parallel_selector_1_out_17);
  or or_17 (or_17_out, parallel_selector_1_out_10, parallel_selector_1_out_6, parallel_selector_1_out_14, parallel_selector_1_out_18);
  or or_18 (or_18_out, parallel_selector_1_out_7, parallel_selector_1_out_11, parallel_selector_1_out_15, parallel_selector_1_out_19);
  and and_40 (and_40_out, registro_portas_1_out_18[5], not_44_out, d_ff_20_q);
  alternador alternador_3 (
    .in_1(P6S), .in_2(registro_portas_1_out_27[0]), .in_3(registro_portas_1_out_27[1]),
    .in_4(registro_portas_1_out_27[2]), .in_5(registro_portas_1_out_27[3]),
    .in_6(registro_portas_1_out_27[4]), .in_7(registro_portas_1_out_27[5]),
    .in_8(registro_portas_1_out_27[6]), .in_9(registro_portas_1_out_27[7]), .out_10(P2_OUT[0]),
    .out_11(P2_OUT[1]), .out_12(P2_OUT[2]), .out_13(P2_OUT[3]), .out_14(P2_OUT[4]), .out_15(P2_OUT[5]),
    .out_16(P2_OUT[6]), .out_17(P2_OUT[7]));
  and and_41 (and_41_out, not_45_out, d_ff_21_q);
  alternador alternador_4 (
    .in_1(P7S), .in_2(registro_portas_1_out_27[0]), .in_3(registro_portas_1_out_27[1]),
    .in_4(registro_portas_1_out_27[2]), .in_5(registro_portas_1_out_27[3]),
    .in_6(registro_portas_1_out_27[4]), .in_7(registro_portas_1_out_27[5]),
    .in_8(registro_portas_1_out_27[6]), .in_9(registro_portas_1_out_27[7]), .out_10(P3_OUT[0]),
    .out_11(P3_OUT[1]), .out_12(P3_OUT[2]), .out_13(P3_OUT[3]), .out_14(P3_OUT[4]), .out_15(P3_OUT[5]),
    .out_16(P3_OUT[6]), .out_17(P3_OUT[7]));
  D_Flip_Flop d_ff_37 (.clk(or_11_out), .D(d_ff_16_q), .Q(d_ff_48_q[11]), .reset(RESET));  // open: Qn, preset, en
  T_Flip_Flop t_ff_10 (
    .clk(t_ff_9_qn), .T(and_35_out), .Q(t_ff_3_q[6]), .Qn(t_ff_10_qn), .preset(pc_input_7_out_4),
    .reset(pc_input_7_out_5), .en(and_35_out));
  pc_input pc_input_7 (
    .in_1(and_37_out), .in_2(d_ff_63_q[6]), .in_3(RESET), .out_4(pc_input_7_out_4), .out_5(pc_input_7_out_5));
  and and_42 (and_42_out, or_19_out, or_18_out);
  habilitador8 habilitador8_1 (
    .in_1(AND_36_out), .in_2(d_ff_15_q[0]), .in_3(d_ff_15_q[1]), .in_4(d_ff_15_q[2]), .in_5(d_ff_15_q[3]),
    .in_6(d_ff_15_q[4]), .in_7(d_ff_15_q[5]), .in_8(d_ff_15_q[6]), .in_9(d_ff_15_q[7]),
    .out_10(habilitador8_1_out_10[0]), .out_11(habilitador8_1_out_10[1]), .out_12(habilitador8_1_out_10[2]),
    .out_13(habilitador8_1_out_10[3]), .out_14(habilitador8_1_out_10[4]), .out_15(habilitador8_1_out_10[5]),
    .out_16(habilitador8_1_out_10[6]), .out_17(habilitador8_1_out_10[7]));
  habilitador8 habilitador8_2 (
    .in_1(OR_12_out), .in_2(d_ff_15_q[0]), .in_3(d_ff_15_q[1]), .in_4(d_ff_15_q[2]), .in_5(d_ff_15_q[3]),
    .in_6(d_ff_15_q[4]), .in_7(d_ff_15_q[5]), .in_8(d_ff_15_q[6]), .in_9(d_ff_15_q[7]),
    .out_10(habilitador8_2_out_10[0]), .out_11(habilitador8_2_out_10[1]), .out_12(habilitador8_2_out_10[2]),
    .out_13(habilitador8_2_out_10[3]), .out_14(habilitador8_2_out_10[4]), .out_15(habilitador8_2_out_10[5]),
    .out_16(habilitador8_2_out_10[6]), .out_17(habilitador8_2_out_10[7]));
  habilitador8 habilitador8_3 (
    .in_1(ST_out), .in_2(buffer_register_1_out_18[0]), .in_3(buffer_register_1_out_18[1]),
    .in_4(buffer_register_1_out_18[2]), .in_5(buffer_register_1_out_18[3]),
    .in_6(buffer_register_1_out_18[4]), .in_7(buffer_register_1_out_18[5]),
    .in_8(buffer_register_1_out_18[6]), .in_9(buffer_register_1_out_18[7]),
    .out_10(habilitador8_3_out_10[0]), .out_11(habilitador8_3_out_10[1]), .out_12(habilitador8_3_out_10[2]),
    .out_13(habilitador8_3_out_10[3]), .out_14(habilitador8_3_out_10[4]), .out_15(habilitador8_3_out_10[5]),
    .out_16(habilitador8_3_out_10[6]), .out_17(habilitador8_3_out_10[7]));
  habilitador8 habilitador8_4 (
    .in_1(XOR_out), .in_2(d_ff_15_q[0]), .in_3(d_ff_15_q[1]), .in_4(d_ff_15_q[2]), .in_5(d_ff_15_q[3]),
    .in_6(d_ff_15_q[4]), .in_7(d_ff_15_q[5]), .in_8(d_ff_15_q[6]), .in_9(d_ff_15_q[7]),
    .out_10(habilitador8_4_out_10[0]), .out_11(habilitador8_4_out_10[1]), .out_12(habilitador8_4_out_10[2]),
    .out_13(habilitador8_4_out_10[3]), .out_14(habilitador8_4_out_10[4]), .out_15(habilitador8_4_out_10[5]),
    .out_16(habilitador8_4_out_10[6]), .out_17(habilitador8_4_out_10[7]));
  habilitador8 habilitador8_5 (
    .in_1(ADD_out), .in_2(d_ff_15_q[0]), .in_3(d_ff_15_q[1]), .in_4(d_ff_15_q[2]), .in_5(d_ff_15_q[3]),
    .in_6(d_ff_15_q[4]), .in_7(d_ff_15_q[5]), .in_8(d_ff_15_q[6]), .in_9(d_ff_15_q[7]),
    .out_10(habilitador8_5_out_10[0]), .out_11(habilitador8_5_out_10[1]), .out_12(habilitador8_5_out_10[2]),
    .out_13(habilitador8_5_out_10[3]), .out_14(habilitador8_5_out_10[4]), .out_15(habilitador8_5_out_10[5]),
    .out_16(habilitador8_5_out_10[6]), .out_17(habilitador8_5_out_10[7]));
  habilitador8 habilitador8_6 (
    .in_1(SUB_out), .in_2(d_ff_15_q[0]), .in_3(d_ff_15_q[1]), .in_4(d_ff_15_q[2]), .in_5(d_ff_15_q[3]),
    .in_6(d_ff_15_q[4]), .in_7(d_ff_15_q[5]), .in_8(d_ff_15_q[6]), .in_9(d_ff_15_q[7]),
    .out_10(habilitador8_6_out_10[0]), .out_11(habilitador8_6_out_10[1]), .out_12(habilitador8_6_out_10[2]),
    .out_13(habilitador8_6_out_10[3]), .out_14(habilitador8_6_out_10[4]), .out_15(habilitador8_6_out_10[5]),
    .out_16(habilitador8_6_out_10[6]), .out_17(habilitador8_6_out_10[7]));
  habilitador8 habilitador8_7 (
    .in_1(LD_out), .in_2(d_ff_15_q[0]), .in_3(d_ff_15_q[1]), .in_4(d_ff_15_q[2]), .in_5(d_ff_15_q[3]),
    .in_6(d_ff_15_q[4]), .in_7(d_ff_15_q[5]), .in_8(d_ff_15_q[6]), .in_9(d_ff_15_q[7]),
    .out_10(habilitador8_7_out_10[0]), .out_11(habilitador8_7_out_10[1]), .out_12(habilitador8_7_out_10[2]),
    .out_13(habilitador8_7_out_10[3]), .out_14(habilitador8_7_out_10[4]), .out_15(habilitador8_7_out_10[5]),
    .out_16(habilitador8_7_out_10[6]), .out_17(habilitador8_7_out_10[7]));
  D_Flip_Flop d_ff_38 (.clk(or_11_out), .D(d_ff_22_q), .Q(d_ff_48_q[10]), .reset(RESET));  // open: Qn, preset, en
  T_Flip_Flop t_ff_11 (
    .clk(t_ff_10_qn), .T(and_35_out), .Q(t_ff_3_q[7]), .Qn(t_ff_11_qn), .preset(pc_input_8_out_4),
    .reset(pc_input_8_out_5), .en(and_35_out));
  pc_input pc_input_8 (
    .in_1(and_37_out), .in_2(d_ff_63_q[7]), .in_3(RESET), .out_4(pc_input_8_out_4), .out_5(pc_input_8_out_5));
  not not_46 (not_46_out, and_42_out);
  or or_19 (or_19_out, and_43_out, and_44_out, decoding_register_1_inst_exec[18]);
  D_Flip_Flop d_ff_39 (.clk(or_11_out), .D(d_ff_23_q), .Q(d_ff_48_q[9]), .reset(RESET));  // open: Qn, preset, en
  T_Flip_Flop t_ff_12 (
    .clk(t_ff_11_qn), .T(and_35_out), .Q(t_ff_3_q[8]), .Qn(t_ff_12_qn), .preset(pc_input_9_out_4),
    .reset(pc_input_9_out_5), .en(and_35_out));
  pc_input pc_input_9 (
    .in_1(and_37_out), .in_2(d_ff_63_q[8]), .in_3(RESET), .out_4(pc_input_9_out_4), .out_5(pc_input_9_out_5));
  and and_43 (and_43_out, d_ff_17_q, decoding_register_1_inst_exec[16]);
  and and_44 (and_44_out, d_ff_13_q, decoding_register_1_inst_exec[17]);
  habilitador8 habilitador8_8 (
    .in_1(AND_36_out), .in_2(registro_usuario_1_out_23[0]), .in_3(registro_usuario_1_out_23[1]),
    .in_4(registro_usuario_1_out_23[2]), .in_5(registro_usuario_1_out_23[3]),
    .in_6(registro_usuario_1_out_23[4]), .in_7(registro_usuario_1_out_23[5]),
    .in_8(registro_usuario_1_out_23[6]), .in_9(registro_usuario_1_out_23[7]),
    .out_10(habilitador8_8_out_10[0]), .out_11(habilitador8_8_out_10[1]), .out_12(habilitador8_8_out_10[2]),
    .out_13(habilitador8_8_out_10[3]), .out_14(habilitador8_8_out_10[4]), .out_15(habilitador8_8_out_10[5]),
    .out_16(habilitador8_8_out_10[6]), .out_17(habilitador8_8_out_10[7]));
  habilitador8 habilitador8_9 (
    .in_1(OR_12_out), .in_2(registro_usuario_1_out_23[0]), .in_3(registro_usuario_1_out_23[1]),
    .in_4(registro_usuario_1_out_23[2]), .in_5(registro_usuario_1_out_23[3]),
    .in_6(registro_usuario_1_out_23[4]), .in_7(registro_usuario_1_out_23[5]),
    .in_8(registro_usuario_1_out_23[6]), .in_9(registro_usuario_1_out_23[7]),
    .out_10(habilitador8_9_out_10[0]), .out_11(habilitador8_9_out_10[1]), .out_12(habilitador8_9_out_10[2]),
    .out_13(habilitador8_9_out_10[3]), .out_14(habilitador8_9_out_10[4]), .out_15(habilitador8_9_out_10[5]),
    .out_16(habilitador8_9_out_10[6]), .out_17(habilitador8_9_out_10[7]));
  habilitador8 habilitador8_10 (
    .in_1(NOT_43_out), .in_2(registro_usuario_1_out_23[0]), .in_3(registro_usuario_1_out_23[1]),
    .in_4(registro_usuario_1_out_23[2]), .in_5(registro_usuario_1_out_23[3]),
    .in_6(registro_usuario_1_out_23[4]), .in_7(registro_usuario_1_out_23[5]),
    .in_8(registro_usuario_1_out_23[6]), .in_9(registro_usuario_1_out_23[7]),
    .out_10(habilitador8_10_out_10[0]), .out_11(habilitador8_10_out_10[1]),
    .out_12(habilitador8_10_out_10[2]), .out_13(habilitador8_10_out_10[3]),
    .out_14(habilitador8_10_out_10[4]), .out_15(habilitador8_10_out_10[5]),
    .out_16(habilitador8_10_out_10[6]), .out_17(habilitador8_10_out_10[7]));
  habilitador8 habilitador8_11 (
    .in_1(XOR_out), .in_2(registro_usuario_1_out_23[0]), .in_3(registro_usuario_1_out_23[1]),
    .in_4(registro_usuario_1_out_23[2]), .in_5(registro_usuario_1_out_23[3]),
    .in_6(registro_usuario_1_out_23[4]), .in_7(registro_usuario_1_out_23[5]),
    .in_8(registro_usuario_1_out_23[6]), .in_9(registro_usuario_1_out_23[7]),
    .out_10(habilitador8_11_out_10[0]), .out_11(habilitador8_11_out_10[1]),
    .out_12(habilitador8_11_out_10[2]), .out_13(habilitador8_11_out_10[3]),
    .out_14(habilitador8_11_out_10[4]), .out_15(habilitador8_11_out_10[5]),
    .out_16(habilitador8_11_out_10[6]), .out_17(habilitador8_11_out_10[7]));
  habilitador8 habilitador8_12 (
    .in_1(ADD_out), .in_2(registro_usuario_1_out_23[0]), .in_3(registro_usuario_1_out_23[1]),
    .in_4(registro_usuario_1_out_23[2]), .in_5(registro_usuario_1_out_23[3]),
    .in_6(registro_usuario_1_out_23[4]), .in_7(registro_usuario_1_out_23[5]),
    .in_8(registro_usuario_1_out_23[6]), .in_9(registro_usuario_1_out_23[7]),
    .out_10(habilitador8_12_out_10[0]), .out_11(habilitador8_12_out_10[1]),
    .out_12(habilitador8_12_out_10[2]), .out_13(habilitador8_12_out_10[3]),
    .out_14(habilitador8_12_out_10[4]), .out_15(habilitador8_12_out_10[5]),
    .out_16(habilitador8_12_out_10[6]), .out_17(habilitador8_12_out_10[7]));
  habilitador8 habilitador8_13 (
    .in_1(SUB_out), .in_2(registro_usuario_1_out_23[0]), .in_3(registro_usuario_1_out_23[1]),
    .in_4(registro_usuario_1_out_23[2]), .in_5(registro_usuario_1_out_23[3]),
    .in_6(registro_usuario_1_out_23[4]), .in_7(registro_usuario_1_out_23[5]),
    .in_8(registro_usuario_1_out_23[6]), .in_9(registro_usuario_1_out_23[7]),
    .out_10(habilitador8_13_out_10[0]), .out_11(habilitador8_13_out_10[1]),
    .out_12(habilitador8_13_out_10[2]), .out_13(habilitador8_13_out_10[3]),
    .out_14(habilitador8_13_out_10[4]), .out_15(habilitador8_13_out_10[5]),
    .out_16(habilitador8_13_out_10[6]), .out_17(habilitador8_13_out_10[7]));
  D_Flip_Flop d_ff_40 (.clk(or_11_out), .D(d_ff_24_q), .Q(d_ff_48_q[8]), .reset(RESET));  // open: Qn, preset, en
  T_Flip_Flop t_ff_13 (
    .clk(t_ff_12_qn), .T(and_35_out), .Q(t_ff_3_q[9]), .Qn(t_ff_13_qn), .preset(pc_input_10_out_4),
    .reset(pc_input_10_out_5), .en(and_35_out));
  pc_input pc_input_10 (
    .in_1(and_37_out), .in_2(d_ff_63_q[9]), .in_3(RESET), .out_4(pc_input_10_out_4), .out_5(pc_input_10_out_5));
  D_Flip_Flop d_ff_41 (.clk(or_13_out), .D(d_ff_4_q), .Q(d_ff_48_q[7]), .reset(RESET));  // open: Qn, preset, en
  T_Flip_Flop t_ff_14 (
    .clk(t_ff_13_qn), .T(and_35_out), .Q(t_ff_3_q[10]), .Qn(t_ff_14_qn), .preset(pc_input_11_out_4),
    .reset(pc_input_11_out_5));  // open: en
  pc_input pc_input_11 (
    .in_1(and_37_out), .in_2(d_ff_63_q[10]), .in_3(RESET), .out_4(pc_input_11_out_4),
    .out_5(pc_input_11_out_5));
  D_Flip_Flop d_ff_42 (.clk(or_13_out), .D(d_ff_7_q), .Q(d_ff_48_q[6]), .reset(RESET));  // open: Qn, preset, en
  T_Flip_Flop t_ff_15 (
    .clk(t_ff_14_qn), .T(and_35_out), .Q(t_ff_3_q[11]), .Qn(t_ff_15_qn), .preset(pc_input_12_out_4),
    .reset(pc_input_12_out_5));  // open: en
  pc_input pc_input_12 (
    .in_1(and_37_out), .in_2(d_ff_63_q[11]), .in_3(RESET), .out_4(pc_input_12_out_4),
    .out_5(pc_input_12_out_5));
  habilitador8 habilitador8_14 (
    .in_1(IN_out[0]), .in_2(registro_portas_1_out_27[0]), .in_3(registro_portas_1_out_27[1]),
    .in_4(registro_portas_1_out_27[2]), .in_5(registro_portas_1_out_27[3]),
    .in_6(registro_portas_1_out_27[4]), .in_7(registro_portas_1_out_27[5]),
    .in_8(registro_portas_1_out_27[6]), .in_9(registro_portas_1_out_27[7]),
    .out_10(habilitador8_14_out_10[0]), .out_11(habilitador8_14_out_10[1]),
    .out_12(habilitador8_14_out_10[2]), .out_13(habilitador8_14_out_10[3]),
    .out_14(habilitador8_14_out_10[4]), .out_15(habilitador8_14_out_10[5]),
    .out_16(habilitador8_14_out_10[6]), .out_17(habilitador8_14_out_10[7]));
  habilitador8 habilitador8_15 (
    .in_1(IN_out[1]), .in_2(d_ff_15_q[0]), .in_3(d_ff_15_q[1]), .in_4(d_ff_15_q[2]), .in_5(d_ff_15_q[3]),
    .in_6(d_ff_15_q[4]), .in_7(d_ff_15_q[5]), .in_8(d_ff_15_q[6]), .in_9(d_ff_15_q[7]),
    .out_10(habilitador8_15_out_10[0]), .out_11(habilitador8_15_out_10[1]),
    .out_12(habilitador8_15_out_10[2]), .out_13(habilitador8_15_out_10[3]),
    .out_14(habilitador8_15_out_10[4]), .out_15(habilitador8_15_out_10[5]),
    .out_16(habilitador8_15_out_10[6]), .out_17(habilitador8_15_out_10[7]));
  habilitador8 habilitador8_16 (
    .in_1(or_20_out), .in_2(d_ff_15_q[0]), .in_3(d_ff_15_q[1]), .in_4(d_ff_15_q[2]), .in_5(d_ff_15_q[3]),
    .in_6(d_ff_15_q[4]), .in_7(d_ff_15_q[5]), .in_8(d_ff_15_q[6]), .in_9(d_ff_15_q[7]),
    .out_10(habilitador8_16_out_10[0]), .out_11(habilitador8_16_out_10[1]),
    .out_12(habilitador8_16_out_10[2]), .out_13(habilitador8_16_out_10[3]),
    .out_14(habilitador8_16_out_10[4]), .out_15(habilitador8_16_out_10[5]),
    .out_16(habilitador8_16_out_10[6]), .out_17(habilitador8_16_out_10[7]));
  habilitador8 habilitador8_17 (
    .in_1(IN_out[4]), .in_2(d_ff_15_q[0]), .in_3(d_ff_15_q[1]), .in_4(d_ff_15_q[2]), .in_5(d_ff_15_q[3]),
    .in_6(d_ff_15_q[4]), .in_7(d_ff_15_q[5]), .in_8(d_ff_15_q[6]), .in_9(d_ff_15_q[7]),
    .out_10(habilitador8_17_out_10[0]), .out_11(habilitador8_17_out_10[1]),
    .out_12(habilitador8_17_out_10[2]), .out_13(habilitador8_17_out_10[3]),
    .out_14(habilitador8_17_out_10[4]), .out_15(habilitador8_17_out_10[5]),
    .out_16(habilitador8_17_out_10[6]), .out_17(habilitador8_17_out_10[7]));
  habilitador12 habilitador12_1 (
    .in_1(IN_out[5]), .in_2(t_ff_3_q[0]), .in_3(t_ff_3_q[1]), .in_4(t_ff_3_q[2]), .in_5(t_ff_3_q[3]),
    .in_6(t_ff_3_q[4]), .in_7(t_ff_3_q[5]), .in_8(t_ff_3_q[6]), .in_9(t_ff_3_q[7]), .in_10(t_ff_3_q[8]),
    .in_11(t_ff_3_q[9]), .in_12(t_ff_3_q[10]), .in_13(t_ff_3_q[11]), .out_14(habilitador12_1_out_14[0]),
    .out_15(habilitador12_1_out_14[1]), .out_16(habilitador12_1_out_14[2]),
    .out_17(habilitador12_1_out_14[3]), .out_18(habilitador12_1_out_14[4]),
    .out_19(habilitador12_1_out_14[5]), .out_20(habilitador12_1_out_14[6]),
    .out_21(habilitador12_1_out_14[7]), .out_22(habilitador12_1_out_14[8]),
    .out_23(habilitador12_1_out_14[9]), .out_24(habilitador12_1_out_14[10]),
    .out_25(habilitador12_1_out_14[11]));
  D_Flip_Flop d_ff_43 (.clk(or_13_out), .D(d_ff_11_q), .Q(d_ff_48_q[5]), .reset(RESET));  // open: Qn, preset, en
  T_Flip_Flop t_ff_16 (
    .clk(t_ff_15_qn), .T(and_45_out), .Q(t_ff_16_q), .reset(RESET), .en(and_35_out));  // open: Qn, preset
  and and_45 (and_45_out, and_35_out, not_46_out);
  mixador mixador_1 (
    .in_1(habilitador8_17_out_10), .in_2(habilitador12_1_out_14), .in_3(habilitador8_5_out_10),
    .in_4(habilitador8_6_out_10), .out_5(mixador_1_out_5), .out_6(mixador_1_out_6), .out_7(mixador_1_out_7),
    .out_8(mixador_1_out_8), .out_9(mixador_1_out_9), .out_10(mixador_1_out_10), .out_11(mixador_1_out_11),
    .out_12(mixador_1_out_12), .out_13(mixador_1_out_13), .out_14(mixador_1_out_14),
    .out_15(mixador_1_out_15), .out_16(mixador_1_out_16));
  mixador mixador_2 (
    .in_1(habilitador8_19_out_10), .in_2(habilitador12_2_out_14), .in_3(habilitador8_12_out_10),
    .in_4(habilitador8_13_out_10), .out_5(mixador_2_out_5), .out_6(mixador_2_out_6), .out_7(mixador_2_out_7),
    .out_8(mixador_2_out_8), .out_9(mixador_2_out_9), .out_10(mixador_2_out_10), .out_11(mixador_2_out_11),
    .out_12(mixador_2_out_12), .out_13(mixador_2_out_13), .out_14(mixador_2_out_14),
    .out_15(mixador_2_out_15), .out_16(mixador_2_out_16));
  or or_20 (or_20_out, IN_out[2], IN_out[3]);
  D_Flip_Flop d_ff_44 (.clk(or_13_out), .D(d_ff_14_q), .Q(d_ff_48_q[4]), .reset(RESET));  // open: Qn, preset, en
  D_Flip_Flop d_ff_45 (.clk(or_13_out), .D(d_ff_16_q), .Q(d_ff_48_q[3]), .reset(RESET));  // open: Qn, preset, en
  habilitador8 habilitador8_18 (
    .in_1(or_20_out), .in_2(buffer_register_1_out_18[0]), .in_3(buffer_register_1_out_18[1]),
    .in_4(buffer_register_1_out_18[2]), .in_5(buffer_register_1_out_18[3]),
    .in_6(buffer_register_1_out_18[4]), .in_7(buffer_register_1_out_18[5]),
    .in_8(buffer_register_1_out_18[6]), .in_9(buffer_register_1_out_18[7]),
    .out_10(habilitador8_18_out_10[0]), .out_11(habilitador8_18_out_10[1]),
    .out_12(habilitador8_18_out_10[2]), .out_13(habilitador8_18_out_10[3]),
    .out_14(habilitador8_18_out_10[4]), .out_15(habilitador8_18_out_10[5]),
    .out_16(habilitador8_18_out_10[6]), .out_17(habilitador8_18_out_10[7]));
  habilitador8 habilitador8_19 (
    .in_1(IN_out[4]), .in_2(registro_usuario_1_out_23[0]), .in_3(registro_usuario_1_out_23[1]),
    .in_4(registro_usuario_1_out_23[2]), .in_5(registro_usuario_1_out_23[3]),
    .in_6(registro_usuario_1_out_23[4]), .in_7(registro_usuario_1_out_23[5]),
    .in_8(registro_usuario_1_out_23[6]), .in_9(registro_usuario_1_out_23[7]),
    .out_10(habilitador8_19_out_10[0]), .out_11(habilitador8_19_out_10[1]),
    .out_12(habilitador8_19_out_10[2]), .out_13(habilitador8_19_out_10[3]),
    .out_14(habilitador8_19_out_10[4]), .out_15(habilitador8_19_out_10[5]),
    .out_16(habilitador8_19_out_10[6]), .out_17(habilitador8_19_out_10[7]));
  habilitador12 habilitador12_2 (
    .in_1(IN_out[5]), .in_2(d_ff_48_q[0]), .in_3(d_ff_48_q[1]), .in_4(d_ff_48_q[2]), .in_5(d_ff_48_q[3]),
    .in_6(d_ff_48_q[4]), .in_7(d_ff_48_q[5]), .in_8(d_ff_48_q[6]), .in_9(d_ff_48_q[7]), .in_10(d_ff_48_q[8]),
    .in_11(d_ff_48_q[9]), .in_12(d_ff_48_q[10]), .in_13(d_ff_48_q[11]), .out_14(habilitador12_2_out_14[0]),
    .out_15(habilitador12_2_out_14[1]), .out_16(habilitador12_2_out_14[2]),
    .out_17(habilitador12_2_out_14[3]), .out_18(habilitador12_2_out_14[4]),
    .out_19(habilitador12_2_out_14[5]), .out_20(habilitador12_2_out_14[6]),
    .out_21(habilitador12_2_out_14[7]), .out_22(habilitador12_2_out_14[8]),
    .out_23(habilitador12_2_out_14[9]), .out_24(habilitador12_2_out_14[10]),
    .out_25(habilitador12_2_out_14[11]));
  D_Flip_Flop d_ff_46 (.clk(or_13_out), .D(d_ff_22_q), .Q(d_ff_48_q[2]), .reset(RESET));  // open: Qn, preset, en
  xor xor_2 (xor_2_out, mixador_2_out_16, or_25_out);
  xor xor_3 (xor_3_out, or_25_out, mixador_2_out_15);
  xor xor_4 (xor_4_out, or_25_out, mixador_2_out_14);
  xor xor_5 (xor_5_out, or_25_out, mixador_2_out_13);
  D_Flip_Flop d_ff_47 (.clk(or_13_out), .D(d_ff_23_q), .Q(d_ff_48_q[1]), .reset(RESET));  // open: Qn, preset, en
  xor xor_6 (xor_6_out, mixador_1_out_16, xor_2_out);
  and and_46 (and_46_out, mixador_1_out_16, xor_2_out);
  xor xor_7 (xor_7_out, mixador_1_out_15, xor_3_out);
  and and_47 (and_47_out, mixador_1_out_15, xor_3_out);
  xor xor_8 (xor_8_out, mixador_1_out_14, xor_4_out);
  and and_48 (and_48_out, mixador_1_out_14, xor_4_out);
  xor xor_9 (xor_9_out, mixador_1_out_13, xor_5_out);
  and and_49 (and_49_out, mixador_1_out_13, xor_5_out);
  D_Flip_Flop d_ff_48 (.clk(or_13_out), .D(d_ff_24_q), .Q(d_ff_48_q[0]), .reset(RESET));  // open: Qn, preset, en
  xor xor_10 (xor_10_out, or_25_out, xor_6_out);
  and and_50 (and_50_out, or_25_out, xor_6_out);
  or or_21 (or_21_out, and_50_out, and_46_out);
  xor xor_11 (xor_11_out, or_21_out, xor_7_out);
  and and_51 (and_51_out, or_21_out, xor_7_out);
  or or_22 (or_22_out, and_51_out, and_47_out);
  xor xor_12 (xor_12_out, or_22_out, xor_8_out);
  or or_23 (or_23_out, and_52_out, and_48_out);
  xor xor_13 (xor_13_out, or_23_out, xor_9_out);
  or or_24 (or_24_out, and_53_out, and_49_out);
  and and_52 (and_52_out, or_22_out, xor_8_out);
  and and_53 (and_53_out, or_23_out, xor_9_out);
  and and_54 (and_54_out, habilitador8_1_out_10[0], habilitador8_8_out_10[0]);
  and and_55 (and_55_out, habilitador8_1_out_10[1], habilitador8_8_out_10[1]);
  and and_56 (and_56_out, habilitador8_1_out_10[2], habilitador8_8_out_10[2]);
  and and_57 (and_57_out, habilitador8_1_out_10[3], habilitador8_8_out_10[3]);
  and and_58 (and_58_out, habilitador8_1_out_10[4], habilitador8_8_out_10[4]);
  and and_59 (and_59_out, habilitador8_1_out_10[5], habilitador8_8_out_10[5]);
  and and_60 (and_60_out, habilitador8_1_out_10[6], habilitador8_8_out_10[6]);
  and and_61 (and_61_out, habilitador8_1_out_10[7], habilitador8_8_out_10[7]);
  or or_25 (or_25_out, IN_out[4], SUB_out);
  xor xor_14 (xor_14_out, mixador_2_out_12, or_25_out);
  xor xor_15 (xor_15_out, or_25_out, mixador_2_out_11);
  alternador alternador_5 (
    .in_1(AND_36_out), .in_2(and_54_out), .in_3(and_55_out), .in_4(and_56_out), .in_5(and_57_out),
    .in_6(and_58_out), .in_7(and_59_out), .in_8(and_60_out), .in_9(and_61_out), .out_10(alternador_5_out_10),
    .out_11(alternador_5_out_11), .out_12(alternador_5_out_12), .out_13(alternador_5_out_13),
    .out_14(alternador_5_out_14), .out_15(alternador_5_out_15), .out_16(alternador_5_out_16),
    .out_17(alternador_5_out_17));
  xor xor_16 (xor_16_out, mixador_1_out_12, xor_14_out);
  and and_62 (and_62_out, mixador_1_out_12, xor_14_out);
  xor xor_17 (xor_17_out, mixador_1_out_11, xor_15_out);
  and and_63 (and_63_out, mixador_1_out_11, xor_15_out);
  xor xor_18 (xor_18_out, mixador_1_out_10, xor_19_out);
  and and_64 (and_64_out, mixador_1_out_10, xor_19_out);
  xor xor_19 (xor_19_out, or_25_out, mixador_2_out_10);
  xor xor_20 (xor_20_out, mixador_1_out_9, xor_21_out);
  and and_65 (and_65_out, mixador_1_out_9, xor_21_out);
  xor xor_21 (xor_21_out, or_25_out, mixador_2_out_9);
  alternador alternador_6 (
    .in_1(ST_out), .in_2(habilitador8_3_out_10[0]), .in_3(habilitador8_3_out_10[1]),
    .in_4(habilitador8_3_out_10[2]), .in_5(habilitador8_3_out_10[3]), .in_6(habilitador8_3_out_10[4]),
    .in_7(habilitador8_3_out_10[5]), .in_8(habilitador8_3_out_10[6]), .in_9(habilitador8_3_out_10[7]),
    .out_10(alternador_5_out_10), .out_11(alternador_5_out_11), .out_12(alternador_5_out_12),
    .out_13(alternador_5_out_13), .out_14(alternador_5_out_14), .out_15(alternador_5_out_15),
    .out_16(alternador_5_out_16), .out_17(alternador_5_out_17));
  alternador alternador_7 (
    .in_1(LD_out), .in_2(habilitador8_7_out_10[0]), .in_3(habilitador8_7_out_10[1]),
    .in_4(habilitador8_7_out_10[2]), .in_5(habilitador8_7_out_10[3]), .in_6(habilitador8_7_out_10[4]),
    .in_7(habilitador8_7_out_10[5]), .in_8(habilitador8_7_out_10[6]), .in_9(habilitador8_7_out_10[7]),
    .out_10(alternador_5_out_10), .out_11(alternador_5_out_11), .out_12(alternador_5_out_12),
    .out_13(alternador_5_out_13), .out_14(alternador_5_out_14), .out_15(alternador_5_out_15),
    .out_16(alternador_5_out_16), .out_17(alternador_5_out_17));
  alternador alternador_8 (
    .in_1(IN_out[0]), .in_2(habilitador8_14_out_10[0]), .in_3(habilitador8_14_out_10[1]),
    .in_4(habilitador8_14_out_10[2]), .in_5(habilitador8_14_out_10[3]), .in_6(habilitador8_14_out_10[4]),
    .in_7(habilitador8_14_out_10[5]), .in_8(habilitador8_14_out_10[6]), .in_9(habilitador8_14_out_10[7]),
    .out_10(alternador_5_out_10), .out_11(alternador_5_out_11), .out_12(alternador_5_out_12),
    .out_13(alternador_5_out_13), .out_14(alternador_5_out_14), .out_15(alternador_5_out_15),
    .out_16(alternador_5_out_16), .out_17(alternador_5_out_17));
  alternador alternador_9 (
    .in_1(IN_out[1]), .in_2(habilitador8_15_out_10[0]), .in_3(habilitador8_15_out_10[1]),
    .in_4(habilitador8_15_out_10[2]), .in_5(habilitador8_15_out_10[3]), .in_6(habilitador8_15_out_10[4]),
    .in_7(habilitador8_15_out_10[5]), .in_8(habilitador8_15_out_10[6]), .in_9(habilitador8_15_out_10[7]),
    .out_10(alternador_5_out_10), .out_11(alternador_5_out_11), .out_12(alternador_5_out_12),
    .out_13(alternador_5_out_13), .out_14(alternador_5_out_14), .out_15(alternador_5_out_15),
    .out_16(alternador_5_out_16), .out_17(alternador_5_out_17));
  xor xor_22 (xor_22_out, or_24_out, xor_16_out);
  or or_26 (or_26_out, and_66_out, and_62_out);
  xor xor_23 (xor_23_out, or_26_out, xor_17_out);
  or or_27 (or_27_out, and_67_out, and_63_out);
  xor xor_24 (xor_24_out, or_27_out, xor_18_out);
  or or_28 (or_28_out, and_68_out, and_64_out);
  xor xor_25 (xor_25_out, or_28_out, xor_20_out);
  or or_29 (or_29_out, and_69_out, and_65_out);
  and and_66 (and_66_out, or_24_out, xor_16_out);
  and and_67 (and_67_out, or_26_out, xor_17_out);
  and and_68 (and_68_out, or_27_out, xor_18_out);
  and and_69 (and_69_out, or_28_out, xor_20_out);
  or or_30 (or_30_out, habilitador8_2_out_10[0], habilitador8_9_out_10[0]);
  or or_31 (or_31_out, habilitador8_2_out_10[1], habilitador8_9_out_10[1]);
  or or_32 (or_32_out, habilitador8_2_out_10[2], habilitador8_9_out_10[2]);
  or or_33 (or_33_out, habilitador8_2_out_10[3], habilitador8_9_out_10[3]);
  or or_34 (or_34_out, habilitador8_2_out_10[4], habilitador8_9_out_10[4]);
  or or_35 (or_35_out, habilitador8_2_out_10[5], habilitador8_9_out_10[5]);
  or or_36 (or_36_out, habilitador8_2_out_10[6], habilitador8_9_out_10[6]);
  or or_37 (or_37_out, habilitador8_2_out_10[7], habilitador8_9_out_10[7]);
  detector_borda detector_borda_4 (.in_1(or_17_out), .in_2(detector_borda_3_out_3), .out_3(detector_borda_4_out_3));
  or or_38 (or_38_out, and_70_out, and_71_out, and_72_out);
  D_Flip_Flop d_ff_49 (
    .clk(detector_borda_4_out_3), .D(alternador_12_4_out_14), .Q(d_ff_63_q[11]));  // open: Qn, preset, en, reset
  and and_70 (and_70_out, habilitador8_16_out_10[7], not_47_out, IN_out[3], habilitador8_18_out_10[0]);
  and and_71 (and_71_out, IN_out[3], not_47_out, or_buffer_1_out_6, habilitador8_18_out_10[1]);
  and and_72 (and_72_out, IN_out[3], not_47_out, or_buffer_2_out_6, habilitador8_18_out_10[2]);
  alternador alternador_10 (
    .in_1(OR_12_out), .in_2(or_30_out), .in_3(or_31_out), .in_4(or_32_out), .in_5(or_33_out),
    .in_6(or_34_out), .in_7(or_35_out), .in_8(or_36_out), .in_9(or_37_out), .out_10(alternador_5_out_10),
    .out_11(alternador_5_out_11), .out_12(alternador_5_out_12), .out_13(alternador_5_out_13),
    .out_14(alternador_5_out_14), .out_15(alternador_5_out_15), .out_16(alternador_5_out_16),
    .out_17(alternador_5_out_17));
  D_Flip_Flop d_ff_50 (
    .clk(detector_borda_4_out_3), .D(alternador_12_4_out_15), .Q(d_ff_63_q[10]));  // open: Qn, preset, en, reset
  not not_47 (not_47_out, IN_out[2]);
  xor xor_26 (xor_26_out, mixador_1_out_8, xor_27_out);
  xor xor_27 (xor_27_out, mixador_2_out_8, or_25_out);
  xor xor_28 (xor_28_out, mixador_1_out_7, xor_29_out);
  xor xor_29 (xor_29_out, or_25_out, mixador_2_out_7);
  xor xor_30 (xor_30_out, or_25_out, mixador_2_out_6);
  xor xor_31 (xor_31_out, or_25_out, mixador_2_out_5);
  D_Flip_Flop d_ff_51 (
    .clk(detector_borda_4_out_3), .D(alternador_12_4_out_16), .Q(d_ff_63_q[9]));  // open: Qn, preset, en, reset
  and and_73 (and_73_out, mixador_1_out_8, xor_27_out);
  and and_74 (and_74_out, mixador_1_out_7, xor_29_out);
  xor xor_32 (xor_32_out, mixador_1_out_6, xor_30_out);
  and and_75 (and_75_out, mixador_1_out_6, xor_30_out);
  xor xor_33 (xor_33_out, mixador_1_out_5, xor_31_out);
  and and_76 (and_76_out, mixador_1_out_5, xor_31_out);
  not not_48 (not_48_out, habilitador8_10_out_10[0]);
  not not_49 (not_49_out, habilitador8_10_out_10[1]);
  not not_50 (not_50_out, habilitador8_10_out_10[2]);
  not not_51 (not_51_out, habilitador8_10_out_10[3]);
  not not_52 (not_52_out, habilitador8_10_out_10[4]);
  not not_53 (not_53_out, habilitador8_10_out_10[5]);
  not not_54 (not_54_out, habilitador8_10_out_10[6]);
  not not_55 (not_55_out, habilitador8_10_out_10[7]);
  D_Flip_Flop d_ff_52 (
    .clk(detector_borda_4_out_3), .D(alternador_12_4_out_17), .Q(d_ff_63_q[8]));  // open: Qn, preset, en, reset
  or or_39 (or_39_out, IN_out[2], IN_out[3]);
  Demultiplexer #(.select(2)) demultiplexer_1 (
    .out1(demultiplexer_1_out1[0]), .out2(demultiplexer_1_out1[1]), .in(habilitador8_18_out_10[0]),
    .sel(IN_out[3:2]), .en(or_39_out));  // open: out0, out3
  Demultiplexer #(.select(2)) demultiplexer_2 (
    .out1(demultiplexer_2_out1[0]), .out2(demultiplexer_2_out1[1]), .in(habilitador8_18_out_10[1]),
    .sel(IN_out[3:2]), .en(or_39_out));  // open: out0, out3
  Demultiplexer #(.select(2)) demultiplexer_3 (
    .out1(demultiplexer_3_out1[0]), .out2(demultiplexer_3_out1[1]), .in(habilitador8_18_out_10[2]),
    .sel(IN_out[3:2]), .en(or_39_out));  // open: out0, out3
  xor xor_34 (xor_34_out, or_29_out, xor_26_out);
  and and_77 (and_77_out, or_29_out, xor_26_out);
  or or_40 (or_40_out, and_77_out, and_73_out);
  xor xor_35 (xor_35_out, or_40_out, xor_28_out);
  and and_78 (and_78_out, or_40_out, xor_28_out);
  or or_41 (or_41_out, and_78_out, and_74_out);
  xor xor_36 (xor_36_out, or_41_out, xor_32_out);
  or or_42 (or_42_out, and_79_out, and_75_out);
  xor xor_37 (xor_37_out, or_42_out, xor_33_out);
  or or_43 (or_43_out, and_80_out, and_76_out);
  D_Flip_Flop d_ff_53 (
    .clk(detector_borda_4_out_3), .D(alternador_5_out_17), .Q(d_ff_63_q[7]));  // open: Qn, preset, en, reset
  or_buffer or_buffer_1 (
    .out_6(or_buffer_1_out_6), .in_1(or_39_out), .in_2(multiplexer_1_out), .in_3(multiplexer_4_out),
    .in_4(1'b0), .in_5(1'b0));
  or_buffer or_buffer_2 (
    .out_6(or_buffer_2_out_6), .in_1(or_39_out), .in_2(multiplexer_2_out), .in_3(multiplexer_5_out),
    .in_4(multiplexer_8_out), .in_5(multiplexer_11_out));
  and and_79 (and_79_out, or_41_out, xor_32_out);
  and and_80 (and_80_out, or_42_out, xor_33_out);
  alternador alternador_11 (
    .in_1(NOT_43_out), .in_2(not_48_out), .in_3(not_49_out), .in_4(not_50_out), .in_5(not_51_out),
    .in_6(not_52_out), .in_7(not_53_out), .in_8(not_54_out), .in_9(not_55_out), .out_10(alternador_5_out_10),
    .out_11(alternador_5_out_11), .out_12(alternador_5_out_12), .out_13(alternador_5_out_13),
    .out_14(alternador_5_out_14), .out_15(alternador_5_out_15), .out_16(alternador_5_out_16),
    .out_17(alternador_5_out_17));
  D_Flip_Flop d_ff_54 (
    .clk(detector_borda_4_out_3), .D(alternador_5_out_16), .Q(d_ff_63_q[6]));  // open: Qn, preset, en, reset
  Multiplexer #(.select(2)) multiplexer_1 (
    .in0(habilitador8_16_out_10[7]), .in1(1'b0), .in2(habilitador8_16_out_10[6]),
    .in3(habilitador8_16_out_10[6]), .out(multiplexer_1_out), .sel(demultiplexer_1_out1));  // open: en
  Multiplexer #(.select(2)) multiplexer_2 (
    .in0(multiplexer_1_out), .in1(1'b0), .in2(multiplexer_7_out), .in3(multiplexer_7_out),
    .out(multiplexer_2_out), .sel(demultiplexer_2_out1));  // open: en
  Multiplexer #(.select(2)) multiplexer_3 (
    .in0(multiplexer_2_out), .in1(1'b0), .in2(multiplexer_14_out), .in3(multiplexer_14_out),
    .out(multiplexer_3_out), .sel(demultiplexer_3_out1));  // open: en
  D_Flip_Flop d_ff_55 (
    .clk(detector_borda_4_out_3), .D(alternador_5_out_15), .Q(d_ff_63_q[5]));  // open: Qn, preset, en, reset
  Multiplexer #(.select(2)) multiplexer_4 (
    .in0(habilitador8_16_out_10[6]), .in1(habilitador8_16_out_10[7]), .in2(habilitador8_16_out_10[5]),
    .in3(habilitador8_16_out_10[5]), .out(multiplexer_4_out), .sel(demultiplexer_1_out1));  // open: en
  Multiplexer #(.select(2)) multiplexer_5 (
    .in0(multiplexer_4_out), .in1(1'b0), .in2(multiplexer_10_out), .in3(multiplexer_10_out),
    .out(multiplexer_5_out), .sel(demultiplexer_2_out1));  // open: en
  Multiplexer #(.select(2)) multiplexer_6 (
    .in0(multiplexer_5_out), .in1(1'b0), .in2(multiplexer_17_out), .in3(multiplexer_17_out),
    .out(multiplexer_6_out), .sel(demultiplexer_3_out1));  // open: en
  D_Flip_Flop d_ff_56 (
    .clk(detector_borda_4_out_3), .D(alternador_5_out_14), .Q(d_ff_63_q[4]));  // open: Qn, preset, en, reset
  Multiplexer #(.select(2)) multiplexer_7 (
    .in0(habilitador8_16_out_10[5]), .in1(habilitador8_16_out_10[6]), .in2(habilitador8_16_out_10[4]),
    .in3(habilitador8_16_out_10[4]), .out(multiplexer_7_out), .sel(demultiplexer_1_out1));  // open: en
  Multiplexer #(.select(2)) multiplexer_8 (
    .in0(multiplexer_7_out), .in1(multiplexer_1_out), .in2(multiplexer_13_out), .in3(multiplexer_13_out),
    .out(multiplexer_8_out), .sel(demultiplexer_2_out1));  // open: en
  Multiplexer #(.select(2)) multiplexer_9 (
    .in0(multiplexer_8_out), .in1(1'b0), .in2(multiplexer_20_out), .in3(multiplexer_20_out),
    .out(multiplexer_9_out), .sel(demultiplexer_3_out1));  // open: en
  or or_44 (or_44_out, IN_out[5], ADD_out, SUB_out, IN_out[4]);
  xor xor_38 (xor_38_out, habilitador8_4_out_10[0], habilitador8_11_out_10[0]);
  xor xor_39 (xor_39_out, habilitador8_4_out_10[1], habilitador8_11_out_10[1]);
  xor xor_40 (xor_40_out, habilitador8_4_out_10[2], habilitador8_11_out_10[2]);
  xor xor_41 (xor_41_out, habilitador8_4_out_10[3], habilitador8_11_out_10[3]);
  xor xor_42 (xor_42_out, habilitador8_4_out_10[4], habilitador8_11_out_10[4]);
  xor xor_43 (xor_43_out, habilitador8_4_out_10[5], habilitador8_11_out_10[5]);
  xor xor_44 (xor_44_out, habilitador8_4_out_10[6], habilitador8_11_out_10[6]);
  xor xor_45 (xor_45_out, habilitador8_4_out_10[7], habilitador8_11_out_10[7]);
  D_Flip_Flop d_ff_57 (
    .clk(detector_borda_4_out_3), .D(alternador_5_out_13), .Q(d_ff_63_q[3]));  // open: Qn, preset, en, reset
  Multiplexer #(.select(2)) multiplexer_10 (
    .in0(habilitador8_16_out_10[4]), .in1(habilitador8_16_out_10[5]), .in2(habilitador8_16_out_10[3]),
    .in3(habilitador8_16_out_10[3]), .out(multiplexer_10_out), .sel(demultiplexer_1_out1));  // open: en
  Multiplexer #(.select(2)) multiplexer_11 (
    .in0(multiplexer_10_out), .in1(multiplexer_4_out), .in2(multiplexer_16_out), .in3(multiplexer_16_out),
    .out(multiplexer_11_out), .sel(demultiplexer_2_out1));  // open: en
  Multiplexer #(.select(2)) multiplexer_12 (
    .in0(multiplexer_11_out), .in1(1'b0), .in2(multiplexer_23_out), .in3(multiplexer_23_out),
    .out(multiplexer_12_out), .sel(demultiplexer_3_out1));  // open: en
  alternador_12 alternador_12_4 (
    .in_1(or_44_out), .in_2(xor_37_out), .in_3(xor_36_out), .in_4(xor_35_out), .in_5(xor_34_out),
    .in_6(xor_25_out), .in_7(xor_24_out), .in_8(xor_23_out), .in_9(xor_22_out), .in_10(xor_13_out),
    .in_11(xor_12_out), .in_12(xor_11_out), .in_13(xor_10_out), .out_14(alternador_12_4_out_14),
    .out_15(alternador_12_4_out_15), .out_16(alternador_12_4_out_16), .out_17(alternador_12_4_out_17),
    .out_18(alternador_5_out_17), .out_19(alternador_5_out_16), .out_20(alternador_5_out_15),
    .out_21(alternador_5_out_14), .out_22(alternador_5_out_13), .out_23(alternador_5_out_12),
    .out_24(alternador_5_out_11), .out_25(alternador_5_out_10));
  or or_45 (or_45_out, or_38_out, or_29_out);
  nor nor_6 (nor_6_out, d_ff_63_q[0], d_ff_63_q[1], d_ff_63_q[2], d_ff_63_q[3], d_ff_63_q[4], d_ff_63_q[5], d_ff_63_q[6], d_ff_63_q[7]);
  D_Flip_Flop d_ff_58 (
    .clk(detector_borda_4_out_3), .D(alternador_5_out_12), .Q(d_ff_63_q[2]));  // open: Qn, preset, en, reset
  Multiplexer #(.select(2)) multiplexer_13 (
    .in0(habilitador8_16_out_10[3]), .in1(habilitador8_16_out_10[4]), .in2(habilitador8_16_out_10[2]),
    .in3(habilitador8_16_out_10[2]), .out(multiplexer_13_out), .sel(demultiplexer_1_out1));  // open: en
  Multiplexer #(.select(2)) multiplexer_14 (
    .in0(multiplexer_13_out), .in1(multiplexer_7_out), .in2(multiplexer_19_out), .in3(multiplexer_19_out),
    .out(multiplexer_14_out), .sel(demultiplexer_2_out1));  // open: en
  Multiplexer #(.select(2)) multiplexer_15 (
    .in0(multiplexer_14_out), .in1(multiplexer_2_out), .in2(1'b0), .in3(1'b0), .out(multiplexer_15_out),
    .sel(demultiplexer_3_out1));  // open: en
  D_Flip_Flop #(.trigger("falling")) d_ff_59 (
    .clk(and_81_out), .D(or_45_out), .Q(d_ff_59_q));  // open: Qn, preset, en, reset
  D_Flip_Flop #(.trigger("falling")) d_ff_60 (
    .clk(and_81_out), .D(or_43_out), .Q(d_ff_60_q));  // open: Qn, preset, en, reset
  D_Flip_Flop #(.trigger("high")) d_ff_61 (
    .clk(or_18_out), .D(nor_6_out), .Q(d_ff_61_q));  // open: Qn, preset, en, reset
  alternador alternador_12 (
    .in_1(XOR_out), .in_2(xor_38_out), .in_3(xor_39_out), .in_4(xor_40_out), .in_5(xor_41_out),
    .in_6(xor_42_out), .in_7(xor_43_out), .in_8(xor_44_out), .in_9(xor_45_out), .out_10(alternador_5_out_10),
    .out_11(alternador_5_out_11), .out_12(alternador_5_out_12), .out_13(alternador_5_out_13),
    .out_14(alternador_5_out_14), .out_15(alternador_5_out_15), .out_16(alternador_5_out_16),
    .out_17(alternador_5_out_17));
  D_Flip_Flop d_ff_62 (
    .clk(detector_borda_4_out_3), .D(alternador_5_out_11), .Q(d_ff_63_q[1]));  // open: Qn, preset, en, reset
  Multiplexer #(.select(2)) multiplexer_16 (
    .in0(habilitador8_16_out_10[2]), .in1(habilitador8_16_out_10[3]), .in2(habilitador8_16_out_10[1]),
    .in3(habilitador8_16_out_10[1]), .out(multiplexer_16_out), .sel(demultiplexer_1_out1));  // open: en
  Multiplexer #(.select(2)) multiplexer_17 (
    .in0(multiplexer_16_out), .in1(multiplexer_10_out), .in2(multiplexer_22_out), .in3(multiplexer_22_out),
    .out(multiplexer_17_out), .sel(demultiplexer_2_out1));  // open: en
  Multiplexer #(.select(2)) multiplexer_18 (
    .in0(multiplexer_17_out), .in1(multiplexer_5_out), .in2(1'b0), .in3(1'b0), .out(multiplexer_18_out),
    .sel(demultiplexer_3_out1));  // open: en
  and and_81 (and_81_out, detector_borda_4_out_3, or_46_out);
  D_Flip_Flop d_ff_63 (
    .clk(detector_borda_4_out_3), .D(alternador_5_out_10), .Q(d_ff_63_q[0]));  // open: Qn, preset, en, reset
  Multiplexer #(.select(2)) multiplexer_19 (
    .in0(habilitador8_16_out_10[1]), .in1(habilitador8_16_out_10[2]), .in2(habilitador8_16_out_10[0]),
    .in3(habilitador8_16_out_10[0]), .out(multiplexer_19_out), .sel(demultiplexer_1_out1));  // open: en
  Multiplexer #(.select(2)) multiplexer_20 (
    .in0(multiplexer_19_out), .in1(multiplexer_13_out), .in2(1'b0), .in3(1'b0), .out(multiplexer_20_out),
    .sel(demultiplexer_2_out1));  // open: en
  Multiplexer #(.select(2)) multiplexer_21 (
    .in0(multiplexer_20_out), .in1(multiplexer_8_out), .in2(1'b0), .in3(1'b0), .out(multiplexer_21_out),
    .sel(demultiplexer_3_out1));  // open: en
  or or_46 (or_46_out, or_39_out, ADD_out, SUB_out, IN_out[4]);
  Multiplexer #(.select(2)) multiplexer_22 (
    .in0(habilitador8_16_out_10[0]), .in1(habilitador8_16_out_10[1]), .in2(1'b0), .in3(1'b0),
    .out(multiplexer_22_out), .sel(demultiplexer_1_out1));  // open: en
  Multiplexer #(.select(2)) multiplexer_23 (
    .in0(multiplexer_22_out), .in1(multiplexer_16_out), .in2(1'b0), .in3(1'b0), .out(multiplexer_23_out),
    .sel(demultiplexer_2_out1));  // open: en
  Multiplexer #(.select(2)) multiplexer_24 (
    .in0(multiplexer_23_out), .in1(multiplexer_11_out), .in2(1'b0), .in3(1'b0), .out(multiplexer_24_out),
    .sel(demultiplexer_3_out1));  // open: en
  alternador alternador_13 (
    .in_1(or_39_out), .in_2(multiplexer_24_out), .in_3(multiplexer_21_out), .in_4(multiplexer_18_out),
    .in_5(multiplexer_15_out), .in_6(multiplexer_12_out), .in_7(multiplexer_9_out), .in_8(multiplexer_6_out),
    .in_9(multiplexer_3_out), .out_10(alternador_5_out_10), .out_11(alternador_5_out_11),
    .out_12(alternador_5_out_12), .out_13(alternador_5_out_13), .out_14(alternador_5_out_14),
    .out_15(alternador_5_out_15), .out_16(alternador_5_out_16), .out_17(alternador_5_out_17));

  // Notes on the sheet:
  //   P1 PORT
  //   P0 PORT
  //   P0<6>
  //   P0<7>
  //   P2 PORT
  //   P3 PORT
  //   x0
  //   x0
  //   c0
  //   c0
  //   x0
  //   x0
  //   s0
  //   s0
  //   s0
  //   c0
  //   s0
  //   c0
  //   x0
  //   x0
  //   x0
  //   x0
  //   s0
  //   c0
  //   s0
  //   c0
  //   s0
  //   c0
  //   s0
  //   c0
  //   x0
  //   x0
  //   x0
  //   x0
  //   c0
  //   c0
  //   c0
  //   c0
  //   s0
  //   s0
  //   s0
  //   s0
endmodule

module alternador (
  input  in_1,
  input  in_2,
  input  in_3,
  input  in_4,
  input  in_5,
  input  in_6,
  input  in_7,
  input  in_8,
  input  in_9,
  output out_10,
  output out_11,
  output out_12,
  output out_13,
  output out_14,
  output out_15,
  output out_16,
  output out_17
);

  assign out_10 = in_1 ? in_2 : 1'bz;  // Controlled_Buffer controlled_buffer_1
  assign out_11 = in_1 ? in_3 : 1'bz;  // Controlled_Buffer controlled_buffer_2
  assign out_12 = in_1 ? in_4 : 1'bz;  // Controlled_Buffer controlled_buffer_3
  assign out_13 = in_1 ? in_5 : 1'bz;  // Controlled_Buffer controlled_buffer_4
  assign out_14 = in_1 ? in_6 : 1'bz;  // Controlled_Buffer controlled_buffer_5
  assign out_15 = in_1 ? in_7 : 1'bz;  // Controlled_Buffer controlled_buffer_6
  assign out_16 = in_1 ? in_8 : 1'bz;  // Controlled_Buffer controlled_buffer_7
  assign out_17 = in_1 ? in_9 : 1'bz;  // Controlled_Buffer controlled_buffer_8
endmodule

module registro_portas (
  input  in_1,
  input  in_2,
  input  in_3,
  input  in_4,
  input  in_5,
  input  in_6,
  input  in_7,
  input  in_8,
  input  in_9,
  input  in_10,
  input  in_11,
  input  in_12,
  input  in_13,
  input  in_14,
  input  in_15,
  input  in_16,
  input  in_17,
  output [7:0] out_18,
  output [7:0] out_19,
  output out_20,
  output out_21,
  output out_22,
  output out_23,
  output out_24,
  output out_25,
  output out_26,
  output out_27
);

  wire and_1_out, and_2_out, and_3_out, and_4_out, d_ff_3_q, d_ff_4_q, d_ff_7_q, d_ff_8_q, d_ff_11_q,
       d_ff_12_q, d_ff_15_q, d_ff_16_q, d_ff_19_q, d_ff_20_q, d_ff_23_q, d_ff_24_q, d_ff_27_q, d_ff_28_q,
       d_ff_31_q, d_ff_32_q, not_1_out, not_2_out, not_3_out, not_4_out, P0_R_out, P0_W_out, P1_R_out,
       P1_W_out, P2_R_out, P2_W_out, P3_R_out, P3_W_out, pc_input_1_out_4, pc_input_1_out_5,
       pc_input_2_out_4, pc_input_2_out_5, pc_input_3_out_4, pc_input_3_out_5;

  not not_1 (not_1_out, in_9);
  not not_2 (not_2_out, in_8);
  not not_3 (not_3_out, in_8);
  not not_4 (not_4_out, in_9);
  and and_1 (and_1_out, not_1_out, not_2_out);
  and and_2 (and_2_out, not_3_out, in_9);
  and and_3 (and_3_out, not_4_out, in_8);
  and and_4 (and_4_out, in_9, in_8);
  and P0_R (P0_R_out, in_5, and_1_out);
  and P1_R (P1_R_out, in_5, and_2_out);
  and P2_R (P2_R_out, in_5, and_3_out);
  and P3_R (P3_R_out, in_5, and_4_out);
  and P0_W (P0_W_out, in_6, and_1_out);
  and P1_W (P1_W_out, in_6, and_2_out);
  and P2_W (P2_W_out, in_6, and_3_out);
  and P3_W (P3_W_out, in_6, and_4_out);
  pc_input pc_input_1 (.in_1(in_7), .in_2(in_1), .in_3(in_4), .out_4(pc_input_1_out_4), .out_5(pc_input_1_out_5));
  D_Flip_Flop #(.trigger("high")) d_ff_1 (
    .clk(P0_W_out), .D(in_10), .Q(out_18[7]), .preset(pc_input_1_out_4), .reset(pc_input_1_out_5));  // open: Qn, en
  pc_input pc_input_2 (.in_1(in_7), .in_2(in_2), .in_3(in_4), .out_4(pc_input_2_out_4), .out_5(pc_input_2_out_5));
  D_Flip_Flop #(.trigger("high")) d_ff_2 (
    .clk(P1_W_out), .D(in_10), .Q(out_19[7]), .reset(in_4));  // open: Qn, preset, en
  D_Flip_Flop #(.trigger("high")) d_ff_3 (
    .clk(P2_W_out), .D(in_10), .Q(d_ff_3_q), .reset(in_4));  // open: Qn, preset, en
  D_Flip_Flop #(.trigger("high")) d_ff_4 (
    .clk(P3_W_out), .D(in_10), .Q(d_ff_4_q), .reset(in_4));  // open: Qn, preset, en
  D_Flip_Flop #(.trigger("high")) d_ff_5 (
    .clk(P0_W_out), .D(in_11), .Q(out_18[6]), .preset(pc_input_2_out_4), .reset(pc_input_2_out_5));  // open: Qn, en
  pc_input pc_input_3 (.in_1(in_7), .in_2(in_3), .in_3(in_4), .out_4(pc_input_3_out_4), .out_5(pc_input_3_out_5));
  D_Flip_Flop #(.trigger("high")) d_ff_6 (
    .clk(P1_W_out), .D(in_11), .Q(out_19[6]), .reset(in_4));  // open: Qn, preset, en
  D_Flip_Flop #(.trigger("high")) d_ff_7 (
    .clk(P2_W_out), .D(in_11), .Q(d_ff_7_q), .reset(in_4));  // open: Qn, preset, en
  D_Flip_Flop #(.trigger("high")) d_ff_8 (
    .clk(P3_W_out), .D(in_11), .Q(d_ff_8_q), .reset(in_4));  // open: Qn, preset, en
  D_Flip_Flop #(.trigger("high")) d_ff_9 (
    .clk(P0_W_out), .D(in_12), .Q(out_18[5]), .preset(pc_input_3_out_4), .reset(pc_input_3_out_5));  // open: Qn, en
  D_Flip_Flop #(.trigger("high")) d_ff_10 (
    .clk(P1_W_out), .D(in_12), .Q(out_19[5]), .reset(in_4));  // open: Qn, preset, en
  D_Flip_Flop #(.trigger("high")) d_ff_11 (
    .clk(P2_W_out), .D(in_12), .Q(d_ff_11_q), .reset(in_4));  // open: Qn, preset, en
  D_Flip_Flop #(.trigger("high")) d_ff_12 (
    .clk(P3_W_out), .D(in_12), .Q(d_ff_12_q), .reset(in_4));  // open: Qn, preset, en
  D_Flip_Flop #(.trigger("high")) d_ff_13 (.clk(P0_W_out), .D(in_13), .Q(out_18[4]));  // open: Qn, preset, en, reset
  D_Flip_Flop #(.trigger("high")) d_ff_14 (
    .clk(P1_W_out), .D(in_13), .Q(out_19[4]), .reset(in_4));  // open: Qn, preset, en
  D_Flip_Flop #(.trigger("high")) d_ff_15 (
    .clk(P2_W_out), .D(in_13), .Q(d_ff_15_q), .reset(in_4));  // open: Qn, preset, en
  D_Flip_Flop #(.trigger("high")) d_ff_16 (
    .clk(P3_W_out), .D(in_13), .Q(d_ff_16_q), .reset(in_4));  // open: Qn, preset, en
  D_Flip_Flop #(.trigger("high")) d_ff_17 (
    .clk(P0_W_out), .D(in_14), .Q(out_18[3]), .reset(in_4));  // open: Qn, preset, en
  D_Flip_Flop #(.trigger("high")) d_ff_18 (
    .clk(P1_W_out), .D(in_14), .Q(out_19[3]), .reset(in_4));  // open: Qn, preset, en
  D_Flip_Flop #(.trigger("high")) d_ff_19 (
    .clk(P2_W_out), .D(in_14), .Q(d_ff_19_q), .reset(in_4));  // open: Qn, preset, en
  D_Flip_Flop #(.trigger("high")) d_ff_20 (
    .clk(P3_W_out), .D(in_14), .Q(d_ff_20_q), .reset(in_4));  // open: Qn, preset, en
  D_Flip_Flop #(.trigger("high")) d_ff_21 (
    .clk(P0_W_out), .D(in_15), .Q(out_18[2]), .reset(in_4));  // open: Qn, preset, en
  D_Flip_Flop #(.trigger("high")) d_ff_22 (
    .clk(P1_W_out), .D(in_15), .Q(out_19[2]), .reset(in_4));  // open: Qn, preset, en
  D_Flip_Flop #(.trigger("high")) d_ff_23 (
    .clk(P2_W_out), .D(in_15), .Q(d_ff_23_q), .reset(in_4));  // open: Qn, preset, en
  D_Flip_Flop #(.trigger("high")) d_ff_24 (
    .clk(P3_W_out), .D(in_15), .Q(d_ff_24_q), .reset(in_4));  // open: Qn, preset, en
  D_Flip_Flop #(.trigger("high")) d_ff_25 (
    .clk(P0_W_out), .D(in_16), .Q(out_18[1]), .reset(in_4));  // open: Qn, preset, en
  D_Flip_Flop #(.trigger("high")) d_ff_26 (
    .clk(P1_W_out), .D(in_16), .Q(out_19[1]), .reset(in_4));  // open: Qn, preset, en
  D_Flip_Flop #(.trigger("high")) d_ff_27 (
    .clk(P2_W_out), .D(in_16), .Q(d_ff_27_q), .reset(in_4));  // open: Qn, preset, en
  D_Flip_Flop #(.trigger("high")) d_ff_28 (
    .clk(P3_W_out), .D(in_16), .Q(d_ff_28_q), .reset(in_4));  // open: Qn, preset, en
  D_Flip_Flop #(.trigger("high")) d_ff_29 (
    .clk(P0_W_out), .D(in_17), .Q(out_18[0]), .reset(in_4));  // open: Qn, preset, en
  D_Flip_Flop #(.trigger("high")) d_ff_30 (
    .clk(P1_W_out), .D(in_17), .Q(out_19[0]), .reset(in_4));  // open: Qn, preset, en
  D_Flip_Flop #(.trigger("high")) d_ff_31 (
    .clk(P2_W_out), .D(in_17), .Q(d_ff_31_q), .reset(in_4));  // open: Qn, preset, en
  D_Flip_Flop #(.trigger("high")) d_ff_32 (
    .clk(P3_W_out), .D(in_17), .Q(d_ff_32_q), .reset(in_4));  // open: Qn, preset, en
  alternador alternador_1 (
    .in_1(P2_R_out), .in_2(d_ff_31_q), .in_3(d_ff_27_q), .in_4(d_ff_23_q), .in_5(d_ff_19_q),
    .in_6(d_ff_15_q), .in_7(d_ff_11_q), .in_8(d_ff_7_q), .in_9(d_ff_3_q), .out_10(out_27), .out_11(out_26),
    .out_12(out_25), .out_13(out_24), .out_14(out_23), .out_15(out_22), .out_16(out_21), .out_17(out_20));
  alternador alternador_2 (
    .in_1(P3_R_out), .in_2(d_ff_32_q), .in_3(d_ff_28_q), .in_4(d_ff_24_q), .in_5(d_ff_20_q),
    .in_6(d_ff_16_q), .in_7(d_ff_12_q), .in_8(d_ff_8_q), .in_9(d_ff_4_q), .out_10(out_27), .out_11(out_26),
    .out_12(out_25), .out_13(out_24), .out_14(out_23), .out_15(out_22), .out_16(out_21), .out_17(out_20));
  alternador alternador_3 (
    .in_1(P0_R_out), .in_2(out_18[0]), .in_3(out_18[1]), .in_4(out_18[2]), .in_5(out_18[3]),
    .in_6(out_18[4]), .in_7(out_18[5]), .in_8(out_18[6]), .in_9(out_18[7]), .out_10(out_27), .out_11(out_26),
    .out_12(out_25), .out_13(out_24), .out_14(out_23), .out_15(out_22), .out_16(out_21), .out_17(out_20));
  alternador alternador_4 (
    .in_1(P1_R_out), .in_2(out_19[0]), .in_3(out_19[1]), .in_4(out_19[2]), .in_5(out_19[3]),
    .in_6(out_19[4]), .in_7(out_19[5]), .in_8(out_19[6]), .in_9(out_19[7]), .out_10(out_27), .out_11(out_26),
    .out_12(out_25), .out_13(out_24), .out_14(out_23), .out_15(out_22), .out_16(out_21), .out_17(out_20));
endmodule

module registro_usuario (
  input  in_1,
  input  in_2,
  input  in_3,
  input  in_4,
  input  in_5,
  input  in_6,
  input  in_7,
  input  in_8,
  input  in_9,
  input  in_10,
  input  in_11,
  input  in_12,
  input  in_13,
  input  in_14,
  input  in_15,
  output out_16,
  output out_17,
  output out_18,
  output out_19,
  output out_20,
  output out_21,
  output out_22,
  output out_23
);

  wire and_1_out, and_2_out, and_3_out, and_4_out, and_5_out, and_6_out, and_7_out, and_8_out, and_9_out,
       and_10_out, and_11_out, and_12_out, and_13_out, and_14_out, and_15_out, and_16_out, and_17_out,
       and_18_out, and_19_out, and_20_out, and_21_out, and_22_out, and_23_out, and_24_out, and_25_out,
       and_26_out, and_27_out, and_28_out, and_29_out, and_30_out, and_31_out, and_32_out, and_33_out,
       and_34_out, and_35_out, and_36_out, and_37_out, and_38_out, and_39_out, and_40_out, and_41_out,
       and_42_out, and_43_out, and_44_out, and_45_out, and_46_out, and_47_out, and_48_out, and_49_out,
       and_50_out, and_51_out, and_52_out, and_53_out, and_54_out, and_55_out, and_56_out, and_57_out,
       and_58_out, and_59_out, and_60_out, and_61_out, and_62_out, and_63_out, and_64_out, and_65_out,
       and_66_out, and_67_out, and_68_out, and_69_out, and_70_out, and_71_out, and_72_out, nor_1_out,
       nor_2_out, nor_3_out, nor_4_out, nor_5_out, nor_6_out, nor_7_out, nor_8_out, nor_9_out, nor_10_out,
       nor_11_out, nor_12_out, nor_13_out, nor_14_out, nor_15_out, nor_16_out, nor_17_out, nor_18_out,
       nor_19_out, nor_20_out, nor_21_out, nor_22_out, nor_23_out, nor_24_out, nor_25_out, nor_26_out,
       nor_27_out, nor_28_out, nor_29_out, nor_30_out, nor_31_out, nor_32_out, nor_33_out, nor_34_out,
       nor_35_out, nor_36_out, nor_37_out, nor_38_out, nor_39_out, nor_40_out, nor_41_out, nor_42_out,
       nor_43_out, nor_44_out, nor_45_out, nor_46_out, nor_47_out, nor_48_out, nor_49_out, nor_50_out,
       nor_51_out, nor_52_out, nor_53_out, nor_54_out, nor_55_out, nor_56_out, nor_57_out, nor_58_out,
       nor_59_out, nor_60_out, nor_61_out, nor_62_out, nor_63_out, nor_64_out, not_1_out, not_2_out,
       not_3_out, not_4_out, not_5_out, not_6_out, not_7_out, not_8_out, not_9_out, not_10_out, not_11_out,
       not_12_out, not_13_out, not_14_out, not_15_out, not_16_out, not_17_out, not_18_out, not_19_out,
       not_20_out, not_21_out, not_22_out, not_23_out, not_24_out, not_25_out, not_26_out, not_27_out,
       not_28_out, not_29_out, not_30_out, not_31_out, not_32_out;

  and and_1 (and_1_out, in_2, in_12);
  and and_2 (and_2_out, in_2, in_13);
  and and_3 (and_3_out, in_2, in_14);
  and and_4 (and_4_out, in_2, in_15);
  not not_1 (not_1_out, in_3);
  not not_2 (not_2_out, in_3);
  not not_3 (not_3_out, in_3);
  not not_4 (not_4_out, in_3);
  and and_5 (and_5_out, not_1_out, and_1_out);
  and and_6 (and_6_out, in_3, and_1_out);
  and and_7 (and_7_out, not_3_out, and_3_out);
  and and_8 (and_8_out, in_3, and_3_out);
  and and_9 (and_9_out, not_2_out, and_2_out);
  and and_10 (and_10_out, in_3, and_2_out);
  and and_11 (and_11_out, not_4_out, and_4_out);
  and and_12 (and_12_out, in_3, and_4_out);
  nor nor_1 (nor_1_out, and_5_out, nor_2_out, in_11);
  nor nor_2 (nor_2_out, nor_1_out, and_6_out);
  nor nor_3 (nor_3_out, and_9_out, nor_4_out, in_11);
  nor nor_4 (nor_4_out, nor_3_out, and_10_out);
  nor nor_5 (nor_5_out, and_7_out, nor_6_out, in_11);
  nor nor_6 (nor_6_out, nor_5_out, and_8_out);
  nor nor_7 (nor_7_out, and_11_out, nor_8_out, in_11);
  nor nor_8 (nor_8_out, nor_7_out, and_12_out);
  not not_5 (not_5_out, in_4);
  not not_6 (not_6_out, in_4);
  not not_7 (not_7_out, in_4);
  not not_8 (not_8_out, in_4);
  and and_13 (and_13_out, not_5_out, and_1_out);
  and and_14 (and_14_out, in_4, and_1_out);
  and and_15 (and_15_out, not_7_out, and_3_out);
  and and_16 (and_16_out, in_4, and_3_out);
  nor nor_9 (nor_9_out, and_13_out, nor_10_out, in_11);
  nor nor_10 (nor_10_out, nor_9_out, and_14_out);
  and and_17 (and_17_out, not_6_out, and_2_out);
  and and_18 (and_18_out, in_4, and_2_out);
  nor nor_11 (nor_11_out, and_15_out, nor_12_out, in_11);
  nor nor_12 (nor_12_out, nor_11_out, and_16_out);
  and and_19 (and_19_out, not_8_out, and_4_out);
  and and_20 (and_20_out, in_4, and_4_out);
  nor nor_13 (nor_13_out, and_17_out, nor_14_out, in_11);
  nor nor_14 (nor_14_out, nor_13_out, and_18_out);
  nor nor_15 (nor_15_out, and_19_out, nor_16_out, in_11);
  nor nor_16 (nor_16_out, nor_15_out, and_20_out);
  not not_9 (not_9_out, in_5);
  not not_10 (not_10_out, in_5);
  not not_11 (not_11_out, in_5);
  not not_12 (not_12_out, in_5);
  and and_21 (and_21_out, not_9_out, and_1_out);
  and and_22 (and_22_out, in_5, and_1_out);
  and and_23 (and_23_out, not_10_out, and_2_out);
  and and_24 (and_24_out, in_5, and_2_out);
  and and_25 (and_25_out, not_11_out, and_3_out);
  and and_26 (and_26_out, in_5, and_3_out);
  and and_27 (and_27_out, not_12_out, and_4_out);
  and and_28 (and_28_out, in_5, and_4_out);
  nor nor_17 (nor_17_out, and_21_out, nor_18_out, in_11);
  nor nor_18 (nor_18_out, nor_17_out, and_22_out);
  nor nor_19 (nor_19_out, and_23_out, nor_20_out, in_11);
  nor nor_20 (nor_20_out, nor_19_out, and_24_out);
  nor nor_21 (nor_21_out, and_25_out, nor_22_out, in_11);
  nor nor_22 (nor_22_out, nor_21_out, and_26_out);
  nor nor_23 (nor_23_out, and_27_out, nor_24_out, in_11);
  nor nor_24 (nor_24_out, nor_23_out, and_28_out);
  not not_13 (not_13_out, in_6);
  not not_14 (not_14_out, in_6);
  not not_15 (not_15_out, in_6);
  not not_16 (not_16_out, in_6);
  and and_29 (and_29_out, not_13_out, and_1_out);
  and and_30 (and_30_out, in_6, and_1_out);
  and and_31 (and_31_out, not_15_out, and_2_out);
  and and_32 (and_32_out, in_6, and_2_out);
  and and_33 (and_33_out, not_14_out, and_3_out);
  and and_34 (and_34_out, in_6, and_3_out);
  and and_35 (and_35_out, not_16_out, and_4_out);
  and and_36 (and_36_out, in_6, and_4_out);
  nor nor_25 (nor_25_out, and_29_out, nor_26_out, in_11);
  nor nor_26 (nor_26_out, nor_25_out, and_30_out);
  nor nor_27 (nor_27_out, and_31_out, nor_28_out, in_11);
  nor nor_28 (nor_28_out, nor_27_out, and_32_out);
  nor nor_29 (nor_29_out, and_33_out, nor_30_out, in_11);
  nor nor_30 (nor_30_out, nor_29_out, and_34_out);
  nor nor_31 (nor_31_out, and_35_out, nor_32_out, in_11);
  nor nor_32 (nor_32_out, nor_31_out, and_36_out);
  not not_17 (not_17_out, in_7);
  not not_18 (not_18_out, in_7);
  not not_19 (not_19_out, in_7);
  not not_20 (not_20_out, in_7);
  and and_37 (and_37_out, not_17_out, and_1_out);
  and and_38 (and_38_out, in_7, and_1_out);
  and and_39 (and_39_out, not_18_out, and_2_out);
  and and_40 (and_40_out, in_7, and_2_out);
  and and_41 (and_41_out, not_19_out, and_3_out);
  and and_42 (and_42_out, in_7, and_3_out);
  and and_43 (and_43_out, not_20_out, and_4_out);
  and and_44 (and_44_out, in_7, and_4_out);
  nor nor_33 (nor_33_out, and_37_out, nor_34_out, in_11);
  nor nor_34 (nor_34_out, nor_33_out, and_38_out);
  nor nor_35 (nor_35_out, and_39_out, nor_36_out, in_11);
  nor nor_36 (nor_36_out, nor_35_out, and_40_out);
  nor nor_37 (nor_37_out, and_41_out, nor_38_out, in_11);
  nor nor_38 (nor_38_out, nor_37_out, and_42_out);
  nor nor_39 (nor_39_out, and_43_out, nor_40_out, in_11);
  nor nor_40 (nor_40_out, nor_39_out, and_44_out);
  not not_21 (not_21_out, in_8);
  not not_22 (not_22_out, in_8);
  not not_23 (not_23_out, in_8);
  not not_24 (not_24_out, in_8);
  and and_45 (and_45_out, not_21_out, and_1_out);
  and and_46 (and_46_out, in_8, and_1_out);
  and and_47 (and_47_out, not_22_out, and_2_out);
  and and_48 (and_48_out, in_8, and_2_out);
  and and_49 (and_49_out, not_23_out, and_3_out);
  and and_50 (and_50_out, in_8, and_3_out);
  and and_51 (and_51_out, not_24_out, and_4_out);
  and and_52 (and_52_out, in_8, and_4_out);
  nor nor_41 (nor_41_out, and_45_out, nor_42_out, in_11);
  nor nor_42 (nor_42_out, nor_41_out, and_46_out);
  nor nor_43 (nor_43_out, and_47_out, nor_44_out, in_11);
  nor nor_44 (nor_44_out, nor_43_out, and_48_out);
  nor nor_45 (nor_45_out, and_49_out, nor_46_out, in_11);
  nor nor_46 (nor_46_out, nor_45_out, and_50_out);
  nor nor_47 (nor_47_out, and_51_out, nor_48_out, in_11);
  nor nor_48 (nor_48_out, nor_47_out, and_52_out);
  not not_25 (not_25_out, in_9);
  not not_26 (not_26_out, in_9);
  not not_27 (not_27_out, in_9);
  not not_28 (not_28_out, in_9);
  and and_53 (and_53_out, not_25_out, and_1_out);
  and and_54 (and_54_out, in_9, and_1_out);
  and and_55 (and_55_out, not_26_out, and_2_out);
  and and_56 (and_56_out, in_9, and_2_out);
  and and_57 (and_57_out, not_27_out, and_3_out);
  and and_58 (and_58_out, in_9, and_3_out);
  and and_59 (and_59_out, not_28_out, and_4_out);
  and and_60 (and_60_out, in_9, and_4_out);
  nor nor_49 (nor_49_out, and_53_out, nor_50_out, in_11);
  nor nor_50 (nor_50_out, nor_49_out, and_54_out);
  nor nor_51 (nor_51_out, and_55_out, nor_52_out, in_11);
  nor nor_52 (nor_52_out, nor_51_out, and_56_out);
  nor nor_53 (nor_53_out, and_57_out, nor_54_out, in_11);
  nor nor_54 (nor_54_out, nor_53_out, and_58_out);
  nor nor_55 (nor_55_out, and_59_out, nor_56_out, in_11);
  nor nor_56 (nor_56_out, nor_55_out, and_60_out);
  not not_29 (not_29_out, in_10);
  not not_30 (not_30_out, in_10);
  not not_31 (not_31_out, in_10);
  not not_32 (not_32_out, in_10);
  and and_61 (and_61_out, not_29_out, and_1_out);
  and and_62 (and_62_out, in_10, and_1_out);
  and and_63 (and_63_out, not_31_out, and_3_out);
  and and_64 (and_64_out, in_10, and_3_out);
  and and_65 (and_65_out, not_30_out, and_2_out);
  and and_66 (and_66_out, in_10, and_2_out);
  and and_67 (and_67_out, not_32_out, and_4_out);
  and and_68 (and_68_out, in_10, and_4_out);
  nor nor_57 (nor_57_out, and_61_out, nor_58_out, in_11);
  nor nor_58 (nor_58_out, nor_57_out, and_62_out);
  nor nor_59 (nor_59_out, and_65_out, nor_60_out, in_11);
  nor nor_60 (nor_60_out, nor_59_out, and_66_out);
  nor nor_61 (nor_61_out, and_63_out, nor_62_out, in_11);
  nor nor_62 (nor_62_out, nor_61_out, and_64_out);
  nor nor_63 (nor_63_out, and_67_out, nor_64_out, in_11);
  nor nor_64 (nor_64_out, nor_63_out, and_68_out);
  and and_69 (and_69_out, in_1, in_13);
  and and_70 (and_70_out, in_1, in_14);
  and and_71 (and_71_out, in_1, in_12);
  and and_72 (and_72_out, in_1, in_15);
  alternador alternador_1 (
    .in_1(and_69_out), .in_2(nor_3_out), .in_3(nor_13_out), .in_4(nor_19_out), .in_5(nor_27_out),
    .in_6(nor_35_out), .in_7(nor_43_out), .in_8(nor_51_out), .in_9(nor_59_out), .out_10(out_16),
    .out_11(out_17), .out_12(out_18), .out_13(out_19), .out_14(out_20), .out_15(out_21), .out_16(out_22),
    .out_17(out_23));
  alternador alternador_2 (
    .in_1(and_71_out), .in_2(nor_1_out), .in_3(nor_9_out), .in_4(nor_17_out), .in_5(nor_25_out),
    .in_6(nor_33_out), .in_7(nor_41_out), .in_8(nor_49_out), .in_9(nor_57_out), .out_10(out_16),
    .out_11(out_17), .out_12(out_18), .out_13(out_19), .out_14(out_20), .out_15(out_21), .out_16(out_22),
    .out_17(out_23));
  alternador alternador_3 (
    .in_1(and_70_out), .in_2(nor_5_out), .in_3(nor_11_out), .in_4(nor_21_out), .in_5(nor_29_out),
    .in_6(nor_37_out), .in_7(nor_45_out), .in_8(nor_53_out), .in_9(nor_61_out), .out_10(out_16),
    .out_11(out_17), .out_12(out_18), .out_13(out_19), .out_14(out_20), .out_15(out_21), .out_16(out_22),
    .out_17(out_23));
  alternador alternador_4 (
    .in_1(and_72_out), .in_2(nor_7_out), .in_3(nor_15_out), .in_4(nor_23_out), .in_5(nor_31_out),
    .in_6(nor_39_out), .in_7(nor_47_out), .in_8(nor_55_out), .in_9(nor_63_out), .out_10(out_16),
    .out_11(out_17), .out_12(out_18), .out_13(out_19), .out_14(out_20), .out_15(out_21), .out_16(out_22),
    .out_17(out_23));
endmodule

module habilitador8 (
  input  in_1,
  input  in_2,
  input  in_3,
  input  in_4,
  input  in_5,
  input  in_6,
  input  in_7,
  input  in_8,
  input  in_9,
  output out_10,
  output out_11,
  output out_12,
  output out_13,
  output out_14,
  output out_15,
  output out_16,
  output out_17
);

  and and_1 (out_10, in_1, in_2);
  and and_2 (out_11, in_1, in_3);
  and and_3 (out_12, in_1, in_4);
  and and_4 (out_13, in_1, in_5);
  and and_5 (out_14, in_1, in_6);
  and and_6 (out_15, in_1, in_7);
  and and_7 (out_16, in_1, in_8);
  and and_8 (out_17, in_1, in_9);
endmodule

module habilitador12 (
  input  in_1,
  input  in_2,
  input  in_3,
  input  in_4,
  input  in_5,
  input  in_6,
  input  in_7,
  input  in_8,
  input  in_9,
  input  in_10,
  input  in_11,
  input  in_12,
  input  in_13,
  output out_14,
  output out_15,
  output out_16,
  output out_17,
  output out_18,
  output out_19,
  output out_20,
  output out_21,
  output out_22,
  output out_23,
  output out_24,
  output out_25
);

  and and_1 (out_14, in_1, in_2);
  and and_2 (out_15, in_1, in_3);
  and and_3 (out_16, in_1, in_4);
  and and_4 (out_17, in_1, in_5);
  and and_5 (out_18, in_1, in_6);
  and and_6 (out_19, in_1, in_7);
  and and_7 (out_20, in_1, in_8);
  and and_8 (out_21, in_1, in_9);
  and and_9 (out_22, in_1, in_10);
  and and_10 (out_23, in_1, in_11);
  and and_11 (out_24, in_1, in_12);
  and and_12 (out_25, in_1, in_13);
endmodule

module mixador (
  input  [7:0] in_1,
  input  [11:0] in_2,
  input  [7:0] in_3,
  input  [7:0] in_4,
  output out_5,
  output out_6,
  output out_7,
  output out_8,
  output out_9,
  output out_10,
  output out_11,
  output out_12,
  output out_13,
  output out_14,
  output out_15,
  output out_16
);

  buf or_1 (out_5, in_2[11]);  // OR_Gate
  buf or_2 (out_6, in_2[10]);  // OR_Gate
  buf or_3 (out_7, in_2[9]);  // OR_Gate
  buf or_4 (out_8, in_2[8]);  // OR_Gate
  or or_5 (out_9, in_4[7], in_3[7], in_1[7], in_2[7]);
  or or_6 (out_10, in_4[6], in_3[6], in_1[6], in_2[6]);
  or or_7 (out_11, in_4[5], in_3[5], in_1[5], in_2[5]);
  or or_8 (out_12, in_4[4], in_3[4], in_1[4], in_2[4]);
  or or_9 (out_13, in_4[3], in_3[3], in_1[3], in_2[3]);
  or or_10 (out_14, in_4[2], in_3[2], in_1[2], in_2[2]);
  or or_11 (out_15, in_4[1], in_3[1], in_1[1], in_2[1]);
  or or_12 (out_16, in_4[0], in_3[0], in_1[0], in_2[0]);
endmodule

module alternador_12 (
  input  in_1,
  input  in_2,
  input  in_3,
  input  in_4,
  input  in_5,
  input  in_6,
  input  in_7,
  input  in_8,
  input  in_9,
  input  in_10,
  input  in_11,
  input  in_12,
  input  in_13,
  output out_14,
  output out_15,
  output out_16,
  output out_17,
  output out_18,
  output out_19,
  output out_20,
  output out_21,
  output out_22,
  output out_23,
  output out_24,
  output out_25
);

  assign out_14 = in_1 ? in_2 : 1'bz;  // Controlled_Buffer controlled_buffer_1
  assign out_15 = in_1 ? in_3 : 1'bz;  // Controlled_Buffer controlled_buffer_2
  assign out_16 = in_1 ? in_4 : 1'bz;  // Controlled_Buffer controlled_buffer_3
  assign out_17 = in_1 ? in_5 : 1'bz;  // Controlled_Buffer controlled_buffer_4
  assign out_18 = in_1 ? in_6 : 1'bz;  // Controlled_Buffer controlled_buffer_5
  assign out_19 = in_1 ? in_7 : 1'bz;  // Controlled_Buffer controlled_buffer_6
  assign out_20 = in_1 ? in_8 : 1'bz;  // Controlled_Buffer controlled_buffer_7
  assign out_21 = in_1 ? in_9 : 1'bz;  // Controlled_Buffer controlled_buffer_8
  assign out_22 = in_1 ? in_10 : 1'bz;  // Controlled_Buffer controlled_buffer_9
  assign out_23 = in_1 ? in_11 : 1'bz;  // Controlled_Buffer controlled_buffer_10
  assign out_24 = in_1 ? in_12 : 1'bz;  // Controlled_Buffer controlled_buffer_11
  assign out_25 = in_1 ? in_13 : 1'bz;  // Controlled_Buffer controlled_buffer_12
endmodule

// IN
module pc_input (
  input  in_1,
  input  in_2,
  input  in_3,
  output out_4,
  output out_5
);

  wire and_2_out, not_1_out;

  not not_1 (not_1_out, in_2);
  and and_1 (out_4, in_1, in_2);
  and and_2 (and_2_out, in_1, not_1_out);
  or or_1 (out_5, and_2_out, in_3);
endmodule

module RAM_control (
  input  in_1,
  input  in_2,
  input  in_3,
  input  in_4,
  input  in_5,
  input  in_6,
  input  in_7,
  input  in_8,
  input  in_9,
  input  in_10,
  input  in_11,
  output out_12,
  output out_13,
  output out_14,
  output out_15,
  output out_16,
  output out_17,
  output out_18,
  output out_19,
  output out_20,
  output out_21
);

  wire and_2_out, not_1_out, not_2_out, not_3_out;

  not not_1 (not_1_out, in_1);
  not not_2 (not_2_out, in_3);
  and and_1 (out_12, not_1_out, in_2);
  and and_2 (and_2_out, not_2_out, in_2);
  not not_3 (not_3_out, and_2_out);
  and and_3 (out_13, not_3_out, in_2);
  alternador alternador_1 (
    .in_1(and_2_out), .in_2(in_4), .in_3(in_5), .in_4(in_6), .in_5(in_7), .in_6(in_8), .in_7(in_9),
    .in_8(in_10), .in_9(in_11), .out_10(out_14), .out_11(out_15), .out_12(out_16), .out_13(out_17),
    .out_14(out_18), .out_15(out_19), .out_16(out_20), .out_17(out_21));
endmodule

module or_buffer (
  input  in_1,
  input  in_2,
  input  in_3,
  input  in_4,
  input  in_5,
  output out_6
);

  wire or_1_out;

  assign out_6 = in_1 ? or_1_out : 1'bz;  // Controlled_Buffer controlled_buffer_1
  or or_1 (or_1_out, in_2, in_3, in_4, in_5);
endmodule

module wr80_processor (
  input  in_1,
  input  in_2,
  input  in_3,
  input  in_4
);

  wire and_1_out, not_1_out, ON_out, ram_control_1_out_12, ram_control_1_out_13, RS_out, WR80_clk_out,
       WR80_mem_en, WR80_out_21, WR80_p6s, WR80_p7s;
  wire [7:0] ram_1_data, ram_control_1_out_21, WR80_p2_out, WR80_p3_out;
  wire [11:0] WR80_out_8;

  Button ON (.out(ON_out));
  Button RS (.out(RS_out));
  main WR80 (
    .ON(ON_out), .RESET(RS_out), .CLK_IN(1'b0), .CLK_EN(in_1), .OVERFLOW_EN(in_2), .CLK_OUT(WR80_clk_out),
    .P6S(WR80_p6s), .MEM_EN(WR80_mem_en), .out_21(WR80_out_21), .out_20(WR80_out_8[11]),
    .out_19(WR80_out_8[10]), .out_17(WR80_out_8[9]), .out_16(WR80_out_8[8]), .out_15(WR80_out_8[7]),
    .out_14(WR80_out_8[6]), .out_13(WR80_out_8[5]), .out_12(WR80_out_8[4]), .out_11(WR80_out_8[3]),
    .out_10(WR80_out_8[2]), .out_9(WR80_out_8[1]), .out_8(WR80_out_8[0]), .P2_IN(ram_control_1_out_21),
    .P2_OUT(WR80_p2_out), .P3_OUT(WR80_p3_out), .P7S(WR80_p7s));  // open: P3_IN
  not not_1 (not_1_out, WR80_clk_out);
  TTY tty_1 (.data(WR80_p3_out[6:0]), .clk(and_1_out), .we(in_3), .clr(in_4));
  and and_1 (and_1_out, WR80_p7s, not_1_out);
  RAM #(.addrWidth(12), .bus("separate")) ram_1 (
    .addr(WR80_out_8), .din(WR80_p2_out), .data(ram_1_data), .str(ram_control_1_out_13),
    .sel(ram_control_1_out_12), .clk(WR80_clk_out), .ld(ram_control_1_out_12));  // open: clr
  RAM_control ram_control_1 (
    .in_1(WR80_out_21), .in_2(WR80_mem_en), .in_3(WR80_p6s), .in_4(ram_1_data[7]), .in_5(ram_1_data[6]),
    .in_6(ram_1_data[5]), .in_7(ram_1_data[4]), .in_8(ram_1_data[3]), .in_9(ram_1_data[2]),
    .in_10(ram_1_data[1]), .in_11(ram_1_data[0]), .out_12(ram_control_1_out_12),
    .out_13(ram_control_1_out_13), .out_14(ram_control_1_out_21[7]), .out_15(ram_control_1_out_21[6]),
    .out_16(ram_control_1_out_21[5]), .out_17(ram_control_1_out_21[4]), .out_18(ram_control_1_out_21[3]),
    .out_19(ram_control_1_out_21[2]), .out_20(ram_control_1_out_21[1]), .out_21(ram_control_1_out_21[0]));
endmodule
module parallel_selector (
  input  in_1,
  input  in_2,
  input  in_3,
  output out_4,
  output out_5,
  output out_6,
  output out_7,
  output out_8,
  output out_9,
  output out_10,
  output out_11,
  output out_12,
  output out_13,
  output out_14,
  output out_15,
  output out_16,
  output out_17,
  output out_18,
  output out_19
);

  wire not_1_out, not_2_out, not_3_out, not_4_out;

  not not_1 (not_1_out, in_2);
  not not_2 (not_2_out, in_1);
  not not_3 (not_3_out, in_1);
  not not_4 (not_4_out, in_2);
  and and_1 (out_4, not_1_out, not_2_out);
  and and_2 (out_8, not_3_out, in_2);
  and and_3 (out_12, not_4_out, in_1);
  and and_4 (out_16, in_2, in_1);
  Multiplexer multiplexer_1 (.in0(out_4), .in1(out_8), .out(out_5), .sel(in_3));  // open: en
  Multiplexer multiplexer_2 (.in0(out_8), .in1(out_12), .out(out_9), .sel(in_3));  // open: en
  Multiplexer multiplexer_3 (.in0(out_12), .in1(out_16), .out(out_13), .sel(in_3));  // open: en
  Multiplexer multiplexer_4 (.in0(out_16), .in1(out_4), .out(out_17), .sel(in_3));  // open: en
  Multiplexer multiplexer_5 (.in0(out_5), .in1(out_9), .out(out_6), .sel(in_3));  // open: en
  Multiplexer multiplexer_6 (.in0(out_9), .in1(out_13), .out(out_10), .sel(in_3));  // open: en
  Multiplexer multiplexer_7 (.in0(out_13), .in1(out_17), .out(out_14), .sel(in_3));  // open: en
  Multiplexer multiplexer_8 (.in0(out_17), .in1(out_5), .out(out_18), .sel(in_3));  // open: en
  Multiplexer multiplexer_9 (.in0(out_6), .in1(out_10), .out(out_7), .sel(in_3));  // open: en
  Multiplexer multiplexer_10 (.in0(out_10), .in1(out_14), .out(out_11), .sel(in_3));  // open: en
  Multiplexer multiplexer_11 (.in0(out_14), .in1(out_18), .out(out_15), .sel(in_3));  // open: en
  Multiplexer multiplexer_12 (.in0(out_18), .in1(out_6), .out(out_19), .sel(in_3));  // open: en

  // Notes on the sheet:
  //   Decodificador Paralelo de Estágios
endmodule

module decoding_register (
  input  dec_signal,
  input  inst,
  output inst_dec,
  output inst_exec
);

  D_Flip_Flop d_ff_1 (.clk(dec_signal), .D(inst), .Q(inst_dec));  // open: Qn, preset, en, reset
  D_Flip_Flop d_ff_2 (.clk(dec_signal), .D(inst_dec), .Q(inst_exec));  // open: Qn, preset, en, reset
endmodule

module buffer_register (
  input  in_1,
  input  in_2,
  input  in_3,
  input  in_4,
  input  in_5,
  input  in_6,
  input  in_7,
  input  in_8,
  input  in_9,
  input  in_10,
  output out_11,
  output out_12,
  output out_13,
  output out_14,
  output out_15,
  output out_16,
  output out_17,
  output out_18
);

  wire detector_borda_1_out_3;

  detector_borda detector_borda_1 (.in_1(in_9), .in_2(in_10), .out_3(detector_borda_1_out_3));
  D_Flip_Flop d_ff_1 (.clk(detector_borda_1_out_3), .D(in_1), .Q(out_11));  // open: Qn, preset, en, reset
  D_Flip_Flop d_ff_2 (.clk(detector_borda_1_out_3), .D(in_2), .Q(out_12));  // open: Qn, preset, en, reset
  D_Flip_Flop d_ff_3 (.clk(detector_borda_1_out_3), .D(out_11));  // open: Q, Qn, preset, en, reset
  D_Flip_Flop d_ff_4 (.clk(detector_borda_1_out_3), .D(in_3), .Q(out_13));  // open: Qn, preset, en, reset
  D_Flip_Flop d_ff_5 (.clk(detector_borda_1_out_3), .D(out_12));  // open: Q, Qn, preset, en, reset
  D_Flip_Flop d_ff_6 (.clk(detector_borda_1_out_3), .D(in_4), .Q(out_14));  // open: Qn, preset, en, reset
  D_Flip_Flop d_ff_7 (.clk(detector_borda_1_out_3), .D(out_13));  // open: Q, Qn, preset, en, reset
  D_Flip_Flop d_ff_8 (.clk(detector_borda_1_out_3), .D(in_5), .Q(out_15));  // open: Qn, preset, en, reset
  D_Flip_Flop d_ff_9 (.clk(detector_borda_1_out_3), .D(out_14));  // open: Q, Qn, preset, en, reset
  D_Flip_Flop d_ff_10 (.clk(detector_borda_1_out_3), .D(in_6), .Q(out_16));  // open: Qn, preset, en, reset
  D_Flip_Flop d_ff_11 (.clk(detector_borda_1_out_3), .D(out_15));  // open: Q, Qn, preset, en, reset
  D_Flip_Flop d_ff_12 (.clk(detector_borda_1_out_3), .D(in_7), .Q(out_17));  // open: Qn, preset, en, reset
  D_Flip_Flop d_ff_13 (.clk(detector_borda_1_out_3), .D(out_16));  // open: Q, Qn, preset, en, reset
  D_Flip_Flop d_ff_14 (.clk(detector_borda_1_out_3), .D(in_8), .Q(out_18));  // open: Qn, preset, en, reset
  D_Flip_Flop d_ff_15 (.clk(detector_borda_1_out_3), .D(out_17));  // open: Q, Qn, preset, en, reset
  D_Flip_Flop d_ff_16 (.clk(detector_borda_1_out_3), .D(out_18));  // open: Q, Qn, preset, en, reset
endmodule

module detector_borda (
  input  in_1,
  input  in_2,
  output out_3
);

  wire and_1_out, and_2_out, nand_1_out, not_1_out, not_2_out;

  not not_1 (not_1_out, in_2);
  not not_2 (not_2_out, in_2);
  nand nand_1 (nand_1_out, not_1_out, in_2);
  and and_1 (and_1_out, not_2_out, in_2);
  and and_2 (and_2_out, in_1, nand_1_out);
  Multiplexer multiplexer_1 (.in0(and_2_out), .in1(and_1_out), .out(out_3), .sel(in_2));  // open: en
endmodule
